// Logisim project flappy_bird_final_project.circ as structural Verilog: 3 circuits, main circuit main
module main (
  input  in_1,
  output up_down,
  output [3:0] out_3
);

  wire and_2_out, and_3_out, and_4_out, and_5_out, and_6_out, and_7_out, and_8_out, and_9_out, and_10_out,
       and_11_out, and_12_out, and_13_out, and_14_out, and_15_out, binary_to_bcd_converter_1_p1, clock_1_out,
       clock_2_out, clock_3_out, comparator_1_eq, comparator_2_eq, decoder_1_out0, decoder_1_out1,
       decoder_1_out2, decoder_1_out3, decoder_1_out4, decoder_1_out5, decoder_1_out6, decoder_1_out7,
       not_1_out, not_2_out, not_3_out, not_4_out, or_1_out, or_2_out, or_3_out, or_4_out, or_5_out,
       or_6_out, or_7_out, or_8_out, or_9_out, shift_register_1_p1, shift_register_1_p3, shift_register_1_p4,
       shift_register_1_p6, shift_register_1_p7, shift_register_1_p8, shift_register_1_p9,
       shift_register_1_p10, shift_register_1_p11, shift_register_1_p12, shift_register_1_p13,
       shift_register_1_p14, shift_register_2_p1, shift_register_2_p4, shift_register_2_p5,
       shift_register_2_p6, shift_register_2_p7, shift_register_2_p8, shift_register_2_p9,
       shift_register_2_p10, shift_register_2_p11, shift_register_2_p12, shift_register_2_p17,
       shift_register_2_p18, shift_register_2_p19, shift_register_2_p20, shift_register_2_p21,
       shift_register_3_p3, shift_register_3_p5, shift_register_3_p6, shift_register_3_p7,
       shift_register_3_p8, shift_register_3_p9, shift_register_3_p10, shift_register_3_p11,
       shift_register_3_p12, shift_register_3_p13, shift_register_3_p14, shift_register_3_p15,
       shift_register_3_p16, shift_register_3_p17, shift_register_3_p18, shift_register_3_p19,
       shift_register_3_p20, shift_register_4_p2, shift_register_4_p4, shift_register_4_p5,
       shift_register_4_p6, shift_register_4_p7, shift_register_4_p8, shift_register_4_p9,
       shift_register_4_p10, shift_register_4_p11, shift_register_4_p12, shift_register_4_p13,
       shift_register_4_p14, shift_register_4_p15, shift_register_4_p16, shift_register_4_p17,
       shift_register_4_p18, shift_register_4_p19, shift_register_4_p20, shift_register_5_p3,
       shift_register_5_p4, shift_register_5_p5, shift_register_5_p6, shift_register_5_p7,
       shift_register_5_p8, shift_register_5_p9, shift_register_5_p10, shift_register_5_p11,
       shift_register_5_p12, shift_register_5_p13, shift_register_5_p14, shift_register_5_p15,
       shift_register_5_p16, shift_register_5_p17, shift_register_5_p18, shift_register_5_p19,
       shift_register_5_p20, subtractor_1_bout, t_ff_1_qn, t_ff_2_qn, t_ff_3_qn, t_ff_4_qn, t_ff_5_q,
       t_ff_6_qn, t_ff_7_q, t_ff_8_qn, t_ff_9_q, t_ff_11_q, t_ff_12_q, undriven, undriven_2, undriven_3,
       undriven_4, undriven_5;
  wire [2:0] counter_1_q;
  wire [3:0] binary_to_bcd_converter_1_p4, binary_to_bcd_converter_1_p5, subtractor_1_out, t_ff_1_q, t_ff_4_q;

  Clock clock_1 (.out(clock_1_out));
  T_Flip_Flop t_ff_1 (.T(1'b1), .clk(clock_1_out), .Q(t_ff_1_q[0]), .Qn(t_ff_1_qn));  // open: reset, preset
  T_Flip_Flop t_ff_2 (.T(1'b1), .clk(t_ff_1_qn), .Q(t_ff_1_q[1]), .Qn(t_ff_2_qn));  // open: reset, preset
  T_Flip_Flop t_ff_3 (.T(1'b1), .clk(t_ff_2_qn), .Q(t_ff_1_q[2]), .Qn(t_ff_3_qn));  // open: reset, preset
  T_Flip_Flop t_ff_4 (
    .T(1'b1), .clk(shift_register_2_p21), .Q(t_ff_4_q[0]), .Qn(t_ff_4_qn), .reset(or_9_out), .preset(undriven));
  T_Flip_Flop t_ff_5 (.T(1'b1), .clk(t_ff_3_qn), .Q(t_ff_5_q));  // open: Qn, reset, preset
  and and_1 (t_ff_1_q[3], in_1, t_ff_5_q);
  Clock clock_2 (.out(clock_2_out));
  T_Flip_Flop t_ff_6 (.T(1'b1), .clk(t_ff_4_qn), .Q(t_ff_4_q[1]), .Qn(t_ff_6_qn), .reset(or_9_out), .preset(undriven));
  not not_1 (not_1_out, t_ff_11_q);
  not not_2 (not_2_out, clock_2_out);
  T_Flip_Flop t_ff_7 (.T(not_1_out), .clk(not_2_out), .Q(t_ff_7_q));  // open: Qn, reset, preset
  T_Flip_Flop t_ff_8 (.T(1'b1), .clk(t_ff_6_qn), .Q(t_ff_4_q[2]), .Qn(t_ff_8_qn), .reset(or_9_out), .preset(undriven));
  Clock clock_3 (.out(clock_3_out));
  T_Flip_Flop t_ff_9 (.T(t_ff_7_q), .clk(not_2_out), .Q(t_ff_9_q));  // open: Qn, reset, preset
  T_Flip_Flop t_ff_10 (.T(1'b1), .clk(t_ff_8_qn), .Q(t_ff_4_q[3]), .reset(or_9_out), .preset(undriven));  // open: Qn
  Counter #(.max('h7), .width(3)) counter_1 (
    .up(up_down), .clk(and_2_out), .Q(counter_1_q));  // open: clr, load, count, D, carry
  and and_2 (and_2_out, clock_3_out, not_4_out);
  Comparator #(.width(4)) comparator_1 (.a(t_ff_1_q), .b({in_1, 3'b111}), .eq(comparator_1_eq));  // open: gt, lt
  not not_3 (not_3_out, t_ff_9_q);
  T_Flip_Flop t_ff_11 (.T(not_3_out), .clk(not_2_out), .Q(t_ff_11_q));  // open: Qn, reset, preset
  T_Flip_Flop t_ff_12 (.T(not_1_out), .clk(not_2_out), .Q(t_ff_12_q));  // open: Qn, reset, preset
  and and_3 (and_3_out, comparator_1_eq, t_ff_11_q);
  Hex_Digit_Display hex_digit_display_1 (.value(binary_to_bcd_converter_1_p4));  // open: dp
  Hex_Digit_Display hex_digit_display_2 (.value(binary_to_bcd_converter_1_p5));  // open: dp
  // Binary_to_BCD_converter #(.binvalue(4)) binary_to_bcd_converter_1: pin names not known; wires that end beside it: binary_to_bcd_converter_1_p1, binary_to_bcd_converter_1_p1, t_ff_4_q, binary_to_bcd_converter_1_p4, binary_to_bcd_converter_1_p5
  Decoder #(.select(3)) decoder_1 (
    .out0(decoder_1_out0), .out1(decoder_1_out1), .out2(decoder_1_out2), .out3(decoder_1_out3),
    .out4(decoder_1_out4), .out5(decoder_1_out5), .out6(decoder_1_out6), .out7(decoder_1_out7),
    .sel(counter_1_q));  // open: en
  and and_4 (and_4_out, comparator_1_eq, t_ff_12_q);
  Joystick joystick_1 (.y(out_3));  // open: x
  and and_5 (and_5_out, comparator_1_eq, t_ff_7_q);
  Subtractor #(.width(4)) subtractor_1 (
    .a(out_3), .b(4'b1000), .out(subtractor_1_out), .bout(subtractor_1_bout));  // open: bin
  and and_6 (and_6_out, comparator_1_eq, t_ff_9_q);
  Comparator #(.width(4)) comparator_2 (.a(subtractor_1_out), .b(4'b0000), .eq(comparator_2_eq));  // open: gt, lt
  not not_4 (not_4_out, comparator_2_eq);
  and and_7 (and_7_out, not_4_out, subtractor_1_bout);
  not not_5 (up_down, and_7_out);
  // Shift_Register #(.length(16)) shift_register_1: pin names not known; wires that end beside it: shift_register_1_p1, comparator_1_eq, shift_register_1_p3, shift_register_1_p4, shift_register_1_p3, shift_register_1_p6, shift_register_1_p7, shift_register_1_p8, shift_register_1_p9, shift_register_1_p10, shift_register_1_p11, shift_register_1_p12, shift_register_1_p13, shift_register_1_p14, shift_register_1_p10, shift_register_1_p9, shift_register_1_p8
  Clock clock_4 (.out(shift_register_1_p1));
  // Shift_Register #(.length(16)) shift_register_2: pin names not known; wires that end beside it: shift_register_2_p1, and_5_out, shift_register_1_p11, shift_register_2_p4, shift_register_2_p5, shift_register_2_p6, shift_register_2_p7, shift_register_2_p8, shift_register_2_p9, shift_register_2_p10, shift_register_2_p11, shift_register_2_p12, shift_register_1_p14, shift_register_1_p13, shift_register_1_p12, shift_register_1_p11, shift_register_2_p17, shift_register_2_p18, shift_register_2_p19, shift_register_2_p20, shift_register_2_p21
  Clock clock_5 (.out(shift_register_2_p1));
  // Shift_Register #(.length(16)) shift_register_3: pin names not known; wires that end beside it: and_3_out, comparator_2_eq, shift_register_3_p3, and_6_out, shift_register_3_p5, shift_register_3_p6, shift_register_3_p7, shift_register_3_p8, shift_register_3_p9, shift_register_3_p10, shift_register_3_p11, shift_register_3_p12, shift_register_3_p13, shift_register_3_p14, shift_register_3_p15, shift_register_3_p16, shift_register_3_p17, shift_register_3_p18, shift_register_3_p19, shift_register_3_p20
  Clock clock_6 (.out(shift_register_3_p3));
  // Shift_Register #(.length(16)) shift_register_4: pin names not known; wires that end beside it: comparator_2_eq, shift_register_4_p2, and_3_out, shift_register_4_p4, shift_register_4_p5, shift_register_4_p6, shift_register_4_p7, shift_register_4_p8, shift_register_4_p9, shift_register_4_p10, shift_register_4_p11, shift_register_4_p12, shift_register_4_p13, shift_register_4_p14, shift_register_4_p15, shift_register_4_p16, shift_register_4_p17, shift_register_4_p18, shift_register_4_p19, shift_register_4_p20
  Clock clock_7 (.out(shift_register_4_p2));
  // Shift_Register #(.length(16)) shift_register_5: pin names not known; wires that end beside it: shift_register_4_p2, and_4_out, shift_register_5_p3, shift_register_5_p4, shift_register_5_p5, shift_register_5_p6, shift_register_5_p7, shift_register_5_p8, shift_register_5_p9, shift_register_5_p10, shift_register_5_p11, shift_register_5_p12, shift_register_5_p13, shift_register_5_p14, shift_register_5_p15, shift_register_5_p16, shift_register_5_p17, shift_register_5_p18, shift_register_5_p19, shift_register_5_p20
  and and_8 (and_8_out, decoder_1_out3, shift_register_4_p10);
  and and_9 (and_9_out, shift_register_5_p8, decoder_1_out4);
  and and_10 (and_10_out, shift_register_2_p21, decoder_1_out6);
  and and_11 (and_11_out, shift_register_2_p21, decoder_1_out7);
  and and_12 (and_12_out, decoder_1_out1, shift_register_2_p21);
  or or_1 (or_1_out, decoder_1_out1, shift_register_2_p21);
  and and_13 (and_13_out, decoder_1_out2, shift_register_3_p11);
  or or_2 (or_2_out, decoder_1_out2, shift_register_3_p11);
  or or_3 (or_3_out, decoder_1_out3, shift_register_4_p10);
  or or_4 (or_4_out, shift_register_5_p8, decoder_1_out4);
  and and_14 (and_14_out, decoder_1_out5, undriven_2);
  or or_5 (or_5_out, shift_register_2_p21, decoder_1_out0);
  and and_15 (and_15_out, shift_register_2_p21, decoder_1_out0);
  or or_6 (or_6_out, decoder_1_out5, undriven_2);
  or or_7 (or_7_out, shift_register_2_p21, decoder_1_out6);
  or or_8 (or_8_out, shift_register_2_p21, decoder_1_out7);
  _7_Segment_Display u_7_segment_display_1 (
    .f(or_5_out), .a(or_5_out), .b(or_5_out), .e(or_5_out), .d(or_5_out), .c(or_5_out), .dp(or_5_out));  // open: g
  _7_Segment_Display u_7_segment_display_2 (
    .f(or_1_out), .a(or_1_out), .b(or_1_out), .e(or_1_out), .d(or_1_out), .c(or_1_out), .dp(or_1_out));  // open: g
  _7_Segment_Display u_7_segment_display_3 (
    .f(or_2_out), .a(or_2_out), .b(or_2_out), .e(or_2_out), .d(or_2_out), .c(or_2_out), .dp(or_2_out));  // open: g
  _7_Segment_Display u_7_segment_display_4 (
    .f(or_3_out), .a(or_3_out), .b(or_3_out), .e(or_3_out), .d(or_3_out), .c(or_3_out), .dp(or_3_out));  // open: g
  _7_Segment_Display u_7_segment_display_5 (
    .f(or_4_out), .a(or_4_out), .b(or_4_out), .e(or_4_out), .d(or_4_out), .c(or_4_out), .dp(or_4_out));  // open: g
  _7_Segment_Display u_7_segment_display_6 (
    .f(or_6_out), .a(or_6_out), .b(or_6_out), .e(or_6_out), .d(or_6_out), .c(or_6_out), .dp(or_6_out));  // open: g
  _7_Segment_Display u_7_segment_display_7 (
    .f(or_7_out), .a(or_7_out), .b(or_7_out), .e(or_7_out), .d(or_7_out), .c(or_7_out), .dp(or_7_out));  // open: g
  _7_Segment_Display u_7_segment_display_8 (
    .f(or_8_out), .a(or_8_out), .b(or_8_out), .e(or_8_out), .d(or_8_out), .c(or_8_out), .dp(or_8_out));  // open: g
  or or_9 (or_9_out, and_14_out, and_15_out, and_12_out, and_13_out, and_9_out, and_8_out, and_10_out, and_11_out);
  _7_Segment_Display u_7_segment_display_9 (
    .f(shift_register_2_p20), .a(shift_register_2_p20), .b(shift_register_2_p20), .e(shift_register_2_p20),
    .d(shift_register_2_p20), .c(shift_register_2_p20), .dp(shift_register_2_p20));  // open: g
  _7_Segment_Display u_7_segment_display_10 (
    .f(shift_register_2_p20), .a(shift_register_2_p20), .b(shift_register_2_p20), .e(shift_register_2_p20),
    .d(shift_register_2_p20), .c(shift_register_2_p20), .dp(shift_register_2_p20));  // open: g
  _7_Segment_Display u_7_segment_display_11 (
    .f(shift_register_3_p10), .a(shift_register_3_p10), .b(shift_register_3_p10), .e(shift_register_3_p10),
    .d(shift_register_3_p10), .c(shift_register_3_p10), .dp(shift_register_3_p10));  // open: g
  _7_Segment_Display u_7_segment_display_12 (
    .f(shift_register_4_p9), .a(shift_register_4_p9), .b(shift_register_4_p9), .e(shift_register_4_p9),
    .d(shift_register_4_p9), .c(shift_register_4_p9), .dp(shift_register_4_p9));  // open: g
  _7_Segment_Display u_7_segment_display_13 (
    .f(shift_register_5_p7), .a(shift_register_5_p7), .b(shift_register_5_p7), .e(shift_register_5_p7),
    .d(shift_register_5_p7), .c(shift_register_5_p7), .dp(shift_register_5_p7));  // open: g
  _7_Segment_Display u_7_segment_display_14 (
    .f(undriven_3), .a(undriven_3), .b(undriven_3), .e(undriven_3), .d(undriven_3), .c(undriven_3),
    .dp(undriven_3));  // open: g
  _7_Segment_Display u_7_segment_display_15 (
    .f(shift_register_2_p20), .a(shift_register_2_p20), .b(shift_register_2_p20), .e(shift_register_2_p20),
    .d(shift_register_2_p20), .c(shift_register_2_p20), .dp(shift_register_2_p20));  // open: g
  _7_Segment_Display u_7_segment_display_16 (
    .f(shift_register_2_p20), .a(shift_register_2_p20), .b(shift_register_2_p20), .e(shift_register_2_p20),
    .d(shift_register_2_p20), .c(shift_register_2_p20), .dp(shift_register_2_p20));  // open: g
  _7_Segment_Display u_7_segment_display_17 (
    .f(shift_register_2_p19), .a(shift_register_2_p19), .b(shift_register_2_p19), .e(shift_register_2_p19),
    .d(shift_register_2_p19), .c(shift_register_2_p19), .dp(shift_register_2_p19));  // open: g
  _7_Segment_Display u_7_segment_display_18 (
    .f(shift_register_2_p19), .a(shift_register_2_p19), .b(shift_register_2_p19), .e(shift_register_2_p19),
    .d(shift_register_2_p19), .c(shift_register_2_p19), .dp(shift_register_2_p19));  // open: g
  _7_Segment_Display u_7_segment_display_19 (
    .f(shift_register_3_p9), .a(shift_register_3_p9), .b(shift_register_3_p9), .e(shift_register_3_p9),
    .d(shift_register_3_p9), .c(shift_register_3_p9), .dp(shift_register_3_p9));  // open: g
  _7_Segment_Display u_7_segment_display_20 (
    .f(shift_register_4_p8), .a(shift_register_4_p8), .b(shift_register_4_p8), .e(shift_register_4_p8),
    .d(shift_register_4_p8), .c(shift_register_4_p8), .dp(shift_register_4_p8));  // open: g
  _7_Segment_Display u_7_segment_display_21 (
    .f(shift_register_5_p6), .a(shift_register_5_p6), .b(shift_register_5_p6), .e(shift_register_5_p6),
    .d(shift_register_5_p6), .c(shift_register_5_p6), .dp(shift_register_5_p6));  // open: g
  _7_Segment_Display u_7_segment_display_22 (
    .f(undriven_4), .a(undriven_4), .b(undriven_4), .e(undriven_4), .d(undriven_4), .c(undriven_4),
    .dp(undriven_4));  // open: g
  _7_Segment_Display u_7_segment_display_23 (
    .f(shift_register_2_p19), .a(shift_register_2_p19), .b(shift_register_2_p19), .e(shift_register_2_p19),
    .d(shift_register_2_p19), .c(shift_register_2_p19), .dp(shift_register_2_p19));  // open: g
  _7_Segment_Display u_7_segment_display_24 (
    .f(shift_register_2_p19), .a(shift_register_2_p19), .b(shift_register_2_p19), .e(shift_register_2_p19),
    .d(shift_register_2_p19), .c(shift_register_2_p19), .dp(shift_register_2_p19));  // open: g
  _7_Segment_Display u_7_segment_display_25 (
    .f(shift_register_2_p18), .a(shift_register_2_p18), .b(shift_register_2_p18), .e(shift_register_2_p18),
    .d(shift_register_2_p18), .c(shift_register_2_p18), .dp(shift_register_2_p18));  // open: g
  _7_Segment_Display u_7_segment_display_26 (
    .f(shift_register_2_p17), .a(shift_register_2_p17), .b(shift_register_2_p17), .e(shift_register_2_p17),
    .d(shift_register_2_p17), .c(shift_register_2_p17), .dp(shift_register_2_p17));  // open: g
  _7_Segment_Display u_7_segment_display_27 (
    .f(shift_register_2_p18), .a(shift_register_2_p18), .b(shift_register_2_p18), .e(shift_register_2_p18),
    .d(shift_register_2_p18), .c(shift_register_2_p18), .dp(shift_register_2_p18));  // open: g
  _7_Segment_Display u_7_segment_display_28 (
    .f(shift_register_2_p17), .a(shift_register_2_p17), .b(shift_register_2_p17), .e(shift_register_2_p17),
    .d(shift_register_2_p17), .c(shift_register_2_p17), .dp(shift_register_2_p17));  // open: g
  _7_Segment_Display u_7_segment_display_29 (
    .f(shift_register_3_p8), .a(shift_register_3_p8), .b(shift_register_3_p8), .e(shift_register_3_p8),
    .d(shift_register_3_p8), .c(shift_register_3_p8), .dp(shift_register_3_p8));  // open: g
  _7_Segment_Display u_7_segment_display_30 (
    .f(shift_register_3_p7), .a(shift_register_3_p7), .b(shift_register_3_p7), .e(shift_register_3_p7),
    .d(shift_register_3_p7), .c(shift_register_3_p7), .dp(shift_register_3_p7));  // open: g
  _7_Segment_Display u_7_segment_display_31 (
    .f(shift_register_4_p7), .a(shift_register_4_p7), .b(shift_register_4_p7), .e(shift_register_4_p7),
    .d(shift_register_4_p7), .c(shift_register_4_p7), .dp(shift_register_4_p7));  // open: g
  _7_Segment_Display u_7_segment_display_32 (
    .f(shift_register_4_p6), .a(shift_register_4_p6), .b(shift_register_4_p6), .e(shift_register_4_p6),
    .d(shift_register_4_p6), .c(shift_register_4_p6), .dp(shift_register_4_p6));  // open: g
  _7_Segment_Display u_7_segment_display_33 (
    .f(shift_register_5_p5), .a(shift_register_5_p5), .b(shift_register_5_p5), .e(shift_register_5_p5),
    .d(shift_register_5_p5), .c(shift_register_5_p5), .dp(shift_register_5_p5));  // open: g
  _7_Segment_Display u_7_segment_display_34 (
    .f(shift_register_5_p4), .a(shift_register_5_p4), .b(shift_register_5_p4), .e(shift_register_5_p4),
    .d(shift_register_5_p4), .c(shift_register_5_p4), .dp(shift_register_5_p4));  // open: g
  _7_Segment_Display u_7_segment_display_35 (
    .f(undriven_5), .a(undriven_5), .b(undriven_5), .e(undriven_5), .d(undriven_5), .c(undriven_5),
    .dp(undriven_5));  // open: g
  _7_Segment_Display u_7_segment_display_36 (
    .f(shift_register_5_p20), .a(shift_register_5_p20), .b(shift_register_5_p20), .e(shift_register_5_p20),
    .d(shift_register_5_p20), .c(shift_register_5_p20), .dp(shift_register_5_p20));  // open: g
  _7_Segment_Display u_7_segment_display_37 (
    .f(shift_register_2_p18), .a(shift_register_2_p18), .b(shift_register_2_p18), .e(shift_register_2_p18),
    .d(shift_register_2_p18), .c(shift_register_2_p18), .dp(shift_register_2_p18));  // open: g
  _7_Segment_Display u_7_segment_display_38 (
    .f(shift_register_2_p17), .a(shift_register_2_p17), .b(shift_register_2_p17), .e(shift_register_2_p17),
    .d(shift_register_2_p17), .c(shift_register_2_p17), .dp(shift_register_2_p17));  // open: g
  _7_Segment_Display u_7_segment_display_39 (
    .f(shift_register_2_p18), .a(shift_register_2_p18), .b(shift_register_2_p18), .e(shift_register_2_p18),
    .d(shift_register_2_p18), .c(shift_register_2_p18), .dp(shift_register_2_p18));  // open: g
  _7_Segment_Display u_7_segment_display_40 (
    .f(shift_register_2_p17), .a(shift_register_2_p17), .b(shift_register_2_p17), .e(shift_register_2_p17),
    .d(shift_register_2_p17), .c(shift_register_2_p17), .dp(shift_register_2_p17));  // open: g
  _7_Segment_Display u_7_segment_display_41 (
    .f(shift_register_1_p11), .a(shift_register_1_p11), .b(shift_register_1_p11), .e(shift_register_1_p11),
    .d(shift_register_1_p11), .c(shift_register_1_p11), .dp(shift_register_1_p11));  // open: g
  _7_Segment_Display u_7_segment_display_42 (
    .f(shift_register_1_p11), .a(shift_register_1_p11), .b(shift_register_1_p11), .e(shift_register_1_p11),
    .d(shift_register_1_p11), .c(shift_register_1_p11), .dp(shift_register_1_p11));  // open: g
  _7_Segment_Display u_7_segment_display_43 (
    .f(shift_register_3_p6), .a(shift_register_3_p6), .b(shift_register_3_p6), .e(shift_register_3_p6),
    .d(shift_register_3_p6), .c(shift_register_3_p6), .dp(shift_register_3_p6));  // open: g
  _7_Segment_Display u_7_segment_display_44 (
    .f(shift_register_4_p5), .a(shift_register_4_p5), .b(shift_register_4_p5), .e(shift_register_4_p5),
    .d(shift_register_4_p5), .c(shift_register_4_p5), .dp(shift_register_4_p5));  // open: g
  _7_Segment_Display u_7_segment_display_45 (
    .f(shift_register_5_p3), .a(shift_register_5_p3), .b(shift_register_5_p3), .e(shift_register_5_p3),
    .d(shift_register_5_p3), .c(shift_register_5_p3), .dp(shift_register_5_p3));  // open: g
  _7_Segment_Display u_7_segment_display_46 (
    .f(shift_register_5_p19), .a(shift_register_5_p19), .b(shift_register_5_p19), .e(shift_register_5_p19),
    .d(shift_register_5_p19), .c(shift_register_5_p19), .dp(shift_register_5_p19));  // open: g
  _7_Segment_Display u_7_segment_display_47 (
    .f(shift_register_1_p11), .a(shift_register_1_p11), .b(shift_register_1_p11), .e(shift_register_1_p11),
    .d(shift_register_1_p11), .c(shift_register_1_p11), .dp(shift_register_1_p11));  // open: g
  _7_Segment_Display u_7_segment_display_48 (
    .f(shift_register_1_p11), .a(shift_register_1_p11), .b(shift_register_1_p11), .e(shift_register_1_p11),
    .d(shift_register_1_p11), .c(shift_register_1_p11), .dp(shift_register_1_p11));  // open: g
  _7_Segment_Display u_7_segment_display_49 (
    .f(shift_register_1_p12), .a(shift_register_1_p12), .b(shift_register_1_p12), .e(shift_register_1_p12),
    .d(shift_register_1_p12), .c(shift_register_1_p12), .dp(shift_register_1_p12));  // open: g
  _7_Segment_Display u_7_segment_display_50 (
    .f(shift_register_1_p12), .a(shift_register_1_p12), .b(shift_register_1_p12), .e(shift_register_1_p12),
    .d(shift_register_1_p12), .c(shift_register_1_p12), .dp(shift_register_1_p12));  // open: g
  _7_Segment_Display u_7_segment_display_51 (
    .f(shift_register_3_p5), .a(shift_register_3_p5), .b(shift_register_3_p5), .e(shift_register_3_p5),
    .d(shift_register_3_p5), .c(shift_register_3_p5), .dp(shift_register_3_p5));  // open: g
  _7_Segment_Display u_7_segment_display_52 (
    .f(shift_register_4_p4), .a(shift_register_4_p4), .b(shift_register_4_p4), .e(shift_register_4_p4),
    .d(shift_register_4_p4), .c(shift_register_4_p4), .dp(shift_register_4_p4));  // open: g
  _7_Segment_Display u_7_segment_display_53 (
    .f(shift_register_4_p20), .a(shift_register_4_p20), .b(shift_register_4_p20), .e(shift_register_4_p20),
    .d(shift_register_4_p20), .c(shift_register_4_p20), .dp(shift_register_4_p20));  // open: g
  _7_Segment_Display u_7_segment_display_54 (
    .f(shift_register_5_p18), .a(shift_register_5_p18), .b(shift_register_5_p18), .e(shift_register_5_p18),
    .d(shift_register_5_p18), .c(shift_register_5_p18), .dp(shift_register_5_p18));  // open: g
  _7_Segment_Display u_7_segment_display_55 (
    .f(shift_register_1_p12), .a(shift_register_1_p12), .b(shift_register_1_p12), .e(shift_register_1_p12),
    .d(shift_register_1_p12), .c(shift_register_1_p12), .dp(shift_register_1_p12));  // open: g
  _7_Segment_Display u_7_segment_display_56 (
    .f(shift_register_1_p12), .a(shift_register_1_p12), .b(shift_register_1_p12), .e(shift_register_1_p12),
    .d(shift_register_1_p12), .c(shift_register_1_p12), .dp(shift_register_1_p12));  // open: g
  _7_Segment_Display u_7_segment_display_57 (
    .f(shift_register_1_p13), .a(shift_register_1_p13), .b(shift_register_1_p13), .e(shift_register_1_p13),
    .d(shift_register_1_p13), .c(shift_register_1_p13), .dp(shift_register_1_p13));  // open: g
  _7_Segment_Display u_7_segment_display_58 (
    .f(shift_register_1_p13), .a(shift_register_1_p13), .b(shift_register_1_p13), .e(shift_register_1_p13),
    .d(shift_register_1_p13), .c(shift_register_1_p13), .dp(shift_register_1_p13));  // open: g
  _7_Segment_Display u_7_segment_display_59 (
    .f(shift_register_2_p12), .a(shift_register_2_p12), .b(shift_register_2_p12), .e(shift_register_2_p12),
    .d(shift_register_2_p12), .c(shift_register_2_p12), .dp(shift_register_2_p12));  // open: g
  _7_Segment_Display u_7_segment_display_60 (
    .f(shift_register_3_p20), .a(shift_register_3_p20), .b(shift_register_3_p20), .e(shift_register_3_p20),
    .d(shift_register_3_p20), .c(shift_register_3_p20), .dp(shift_register_3_p20));  // open: g
  _7_Segment_Display u_7_segment_display_61 (
    .f(shift_register_4_p19), .a(shift_register_4_p19), .b(shift_register_4_p19), .e(shift_register_4_p19),
    .d(shift_register_4_p19), .c(shift_register_4_p19), .dp(shift_register_4_p19));  // open: g
  _7_Segment_Display u_7_segment_display_62 (
    .f(shift_register_5_p17), .a(shift_register_5_p17), .b(shift_register_5_p17), .e(shift_register_5_p17),
    .d(shift_register_5_p17), .c(shift_register_5_p17), .dp(shift_register_5_p17));  // open: g
  _7_Segment_Display u_7_segment_display_63 (
    .f(shift_register_1_p13), .a(shift_register_1_p13), .b(shift_register_1_p13), .e(shift_register_1_p13),
    .d(shift_register_1_p13), .c(shift_register_1_p13), .dp(shift_register_1_p13));  // open: g
  _7_Segment_Display u_7_segment_display_64 (
    .f(shift_register_1_p13), .a(shift_register_1_p13), .b(shift_register_1_p13), .e(shift_register_1_p13),
    .d(shift_register_1_p13), .c(shift_register_1_p13), .dp(shift_register_1_p13));  // open: g
  _7_Segment_Display u_7_segment_display_65 (
    .f(shift_register_1_p14), .a(shift_register_1_p14), .b(shift_register_1_p14), .e(shift_register_1_p14),
    .d(shift_register_1_p14), .c(shift_register_1_p14), .dp(shift_register_1_p14));  // open: g
  _7_Segment_Display u_7_segment_display_66 (
    .f(shift_register_1_p14), .a(shift_register_1_p14), .b(shift_register_1_p14), .e(shift_register_1_p14),
    .d(shift_register_1_p14), .c(shift_register_1_p14), .dp(shift_register_1_p14));  // open: g
  _7_Segment_Display u_7_segment_display_67 (
    .f(shift_register_2_p11), .a(shift_register_2_p11), .b(shift_register_2_p11), .e(shift_register_2_p11),
    .d(shift_register_2_p11), .c(shift_register_2_p11), .dp(shift_register_2_p11));  // open: g
  _7_Segment_Display u_7_segment_display_68 (
    .f(shift_register_3_p19), .a(shift_register_3_p19), .b(shift_register_3_p19), .e(shift_register_3_p19),
    .d(shift_register_3_p19), .c(shift_register_3_p19), .dp(shift_register_3_p19));  // open: g
  _7_Segment_Display u_7_segment_display_69 (
    .f(shift_register_4_p18), .a(shift_register_4_p18), .b(shift_register_4_p18), .e(shift_register_4_p18),
    .d(shift_register_4_p18), .c(shift_register_4_p18), .dp(shift_register_4_p18));  // open: g
  _7_Segment_Display u_7_segment_display_70 (
    .f(shift_register_5_p16), .a(shift_register_5_p16), .b(shift_register_5_p16), .e(shift_register_5_p16),
    .d(shift_register_5_p16), .c(shift_register_5_p16), .dp(shift_register_5_p16));  // open: g
  _7_Segment_Display u_7_segment_display_71 (
    .f(shift_register_1_p14), .a(shift_register_1_p14), .b(shift_register_1_p14), .e(shift_register_1_p14),
    .d(shift_register_1_p14), .c(shift_register_1_p14), .dp(shift_register_1_p14));  // open: g
  _7_Segment_Display u_7_segment_display_72 (
    .f(shift_register_1_p14), .a(shift_register_1_p14), .b(shift_register_1_p14), .e(shift_register_1_p14),
    .d(shift_register_1_p14), .c(shift_register_1_p14), .dp(shift_register_1_p14));  // open: g
  _7_Segment_Display u_7_segment_display_73 (
    .f(shift_register_1_p10), .a(shift_register_1_p10), .b(shift_register_1_p10), .e(shift_register_1_p10),
    .d(shift_register_1_p10), .c(shift_register_1_p10), .dp(shift_register_1_p10));  // open: g
  _7_Segment_Display u_7_segment_display_74 (
    .f(shift_register_1_p10), .a(shift_register_1_p10), .b(shift_register_1_p10), .e(shift_register_1_p10),
    .d(shift_register_1_p10), .c(shift_register_1_p10), .dp(shift_register_1_p10));  // open: g
  _7_Segment_Display u_7_segment_display_75 (
    .f(shift_register_2_p10), .a(shift_register_2_p10), .b(shift_register_2_p10), .e(shift_register_2_p10),
    .d(shift_register_2_p10), .c(shift_register_2_p10), .dp(shift_register_2_p10));  // open: g
  _7_Segment_Display u_7_segment_display_76 (
    .f(shift_register_3_p18), .a(shift_register_3_p18), .b(shift_register_3_p18), .e(shift_register_3_p18),
    .d(shift_register_3_p18), .c(shift_register_3_p18), .dp(shift_register_3_p18));  // open: g
  _7_Segment_Display u_7_segment_display_77 (
    .f(shift_register_4_p17), .a(shift_register_4_p17), .b(shift_register_4_p17), .e(shift_register_4_p17),
    .d(shift_register_4_p17), .c(shift_register_4_p17), .dp(shift_register_4_p17));  // open: g
  _7_Segment_Display u_7_segment_display_78 (
    .f(shift_register_5_p15), .a(shift_register_5_p15), .b(shift_register_5_p15), .e(shift_register_5_p15),
    .d(shift_register_5_p15), .c(shift_register_5_p15), .dp(shift_register_5_p15));  // open: g
  _7_Segment_Display u_7_segment_display_79 (
    .f(shift_register_1_p10), .a(shift_register_1_p10), .b(shift_register_1_p10), .e(shift_register_1_p10),
    .d(shift_register_1_p10), .c(shift_register_1_p10), .dp(shift_register_1_p10));  // open: g
  _7_Segment_Display u_7_segment_display_80 (
    .f(shift_register_1_p10), .a(shift_register_1_p10), .b(shift_register_1_p10), .e(shift_register_1_p10),
    .d(shift_register_1_p10), .c(shift_register_1_p10), .dp(shift_register_1_p10));  // open: g
  _7_Segment_Display u_7_segment_display_81 (
    .f(shift_register_1_p9), .a(shift_register_1_p9), .b(shift_register_1_p9), .e(shift_register_1_p9),
    .d(shift_register_1_p9), .c(shift_register_1_p9), .dp(shift_register_1_p9));  // open: g
  _7_Segment_Display u_7_segment_display_82 (
    .f(shift_register_1_p9), .a(shift_register_1_p9), .b(shift_register_1_p9), .e(shift_register_1_p9),
    .d(shift_register_1_p9), .c(shift_register_1_p9), .dp(shift_register_1_p9));  // open: g
  _7_Segment_Display u_7_segment_display_83 (
    .f(shift_register_2_p9), .a(shift_register_2_p9), .b(shift_register_2_p9), .e(shift_register_2_p9),
    .d(shift_register_2_p9), .c(shift_register_2_p9), .dp(shift_register_2_p9));  // open: g
  _7_Segment_Display u_7_segment_display_84 (
    .f(shift_register_3_p17), .a(shift_register_3_p17), .b(shift_register_3_p17), .e(shift_register_3_p17),
    .d(shift_register_3_p17), .c(shift_register_3_p17), .dp(shift_register_3_p17));  // open: g
  _7_Segment_Display u_7_segment_display_85 (
    .f(shift_register_4_p16), .a(shift_register_4_p16), .b(shift_register_4_p16), .e(shift_register_4_p16),
    .d(shift_register_4_p16), .c(shift_register_4_p16), .dp(shift_register_4_p16));  // open: g
  _7_Segment_Display u_7_segment_display_86 (
    .f(shift_register_5_p14), .a(shift_register_5_p14), .b(shift_register_5_p14), .e(shift_register_5_p14),
    .d(shift_register_5_p14), .c(shift_register_5_p14), .dp(shift_register_5_p14));  // open: g
  _7_Segment_Display u_7_segment_display_87 (
    .f(shift_register_1_p9), .a(shift_register_1_p9), .b(shift_register_1_p9), .e(shift_register_1_p9),
    .d(shift_register_1_p9), .c(shift_register_1_p9), .dp(shift_register_1_p9));  // open: g
  _7_Segment_Display u_7_segment_display_88 (
    .f(shift_register_1_p9), .a(shift_register_1_p9), .b(shift_register_1_p9), .e(shift_register_1_p9),
    .d(shift_register_1_p9), .c(shift_register_1_p9), .dp(shift_register_1_p9));  // open: g
  _7_Segment_Display u_7_segment_display_89 (
    .f(shift_register_1_p8), .a(shift_register_1_p8), .b(shift_register_1_p8), .e(shift_register_1_p8),
    .d(shift_register_1_p8), .c(shift_register_1_p8), .dp(shift_register_1_p8));  // open: g
  _7_Segment_Display u_7_segment_display_90 (
    .f(shift_register_1_p7), .a(shift_register_1_p7), .b(shift_register_1_p7), .e(shift_register_1_p7),
    .d(shift_register_1_p7), .c(shift_register_1_p7), .dp(shift_register_1_p7));  // open: g
  _7_Segment_Display u_7_segment_display_91 (
    .f(shift_register_1_p8), .a(shift_register_1_p8), .b(shift_register_1_p8), .e(shift_register_1_p8),
    .d(shift_register_1_p8), .c(shift_register_1_p8), .dp(shift_register_1_p8));  // open: g
  _7_Segment_Display u_7_segment_display_92 (
    .f(shift_register_1_p7), .a(shift_register_1_p7), .b(shift_register_1_p7), .e(shift_register_1_p7),
    .d(shift_register_1_p7), .c(shift_register_1_p7), .dp(shift_register_1_p7));  // open: g
  _7_Segment_Display u_7_segment_display_93 (
    .f(shift_register_2_p8), .a(shift_register_2_p8), .b(shift_register_2_p8), .e(shift_register_2_p8),
    .d(shift_register_2_p8), .c(shift_register_2_p8), .dp(shift_register_2_p8));  // open: g
  _7_Segment_Display u_7_segment_display_94 (
    .f(shift_register_2_p7), .a(shift_register_2_p7), .b(shift_register_2_p7), .e(shift_register_2_p7),
    .d(shift_register_2_p7), .c(shift_register_2_p7), .dp(shift_register_2_p7));  // open: g
  _7_Segment_Display u_7_segment_display_95 (
    .f(shift_register_3_p16), .a(shift_register_3_p16), .b(shift_register_3_p16), .e(shift_register_3_p16),
    .d(shift_register_3_p16), .c(shift_register_3_p16), .dp(shift_register_3_p16));  // open: g
  _7_Segment_Display u_7_segment_display_96 (
    .f(shift_register_3_p15), .a(shift_register_3_p15), .b(shift_register_3_p15), .e(shift_register_3_p15),
    .d(shift_register_3_p15), .c(shift_register_3_p15), .dp(shift_register_3_p15));  // open: g
  _7_Segment_Display u_7_segment_display_97 (
    .f(shift_register_4_p15), .a(shift_register_4_p15), .b(shift_register_4_p15), .e(shift_register_4_p15),
    .d(shift_register_4_p15), .c(shift_register_4_p15), .dp(shift_register_4_p15));  // open: g
  _7_Segment_Display u_7_segment_display_98 (
    .f(shift_register_4_p14), .a(shift_register_4_p14), .b(shift_register_4_p14), .e(shift_register_4_p14),
    .d(shift_register_4_p14), .c(shift_register_4_p14), .dp(shift_register_4_p14));  // open: g
  _7_Segment_Display u_7_segment_display_99 (
    .f(shift_register_5_p13), .a(shift_register_5_p13), .b(shift_register_5_p13), .e(shift_register_5_p13),
    .d(shift_register_5_p13), .c(shift_register_5_p13), .dp(shift_register_5_p13));  // open: g
  _7_Segment_Display u_7_segment_display_100 (
    .f(shift_register_5_p12), .a(shift_register_5_p12), .b(shift_register_5_p12), .e(shift_register_5_p12),
    .d(shift_register_5_p12), .c(shift_register_5_p12), .dp(shift_register_5_p12));  // open: g
  _7_Segment_Display u_7_segment_display_101 (
    .f(shift_register_1_p8), .a(shift_register_1_p8), .b(shift_register_1_p8), .e(shift_register_1_p8),
    .d(shift_register_1_p8), .c(shift_register_1_p8), .dp(shift_register_1_p8));  // open: g
  _7_Segment_Display u_7_segment_display_102 (
    .f(shift_register_1_p7), .a(shift_register_1_p7), .b(shift_register_1_p7), .e(shift_register_1_p7),
    .d(shift_register_1_p7), .c(shift_register_1_p7), .dp(shift_register_1_p7));  // open: g
  _7_Segment_Display u_7_segment_display_103 (
    .f(shift_register_1_p8), .a(shift_register_1_p8), .b(shift_register_1_p8), .e(shift_register_1_p8),
    .d(shift_register_1_p8), .c(shift_register_1_p8), .dp(shift_register_1_p8));  // open: g
  _7_Segment_Display u_7_segment_display_104 (
    .f(shift_register_1_p7), .a(shift_register_1_p7), .b(shift_register_1_p7), .e(shift_register_1_p7),
    .d(shift_register_1_p7), .c(shift_register_1_p7), .dp(shift_register_1_p7));  // open: g
  _7_Segment_Display u_7_segment_display_105 (
    .f(shift_register_1_p6), .a(shift_register_1_p6), .b(shift_register_1_p6), .e(shift_register_1_p6),
    .d(shift_register_1_p6), .c(shift_register_1_p6), .dp(shift_register_1_p6));  // open: g
  _7_Segment_Display u_7_segment_display_106 (
    .f(shift_register_1_p6), .a(shift_register_1_p6), .b(shift_register_1_p6), .e(shift_register_1_p6),
    .d(shift_register_1_p6), .c(shift_register_1_p6), .dp(shift_register_1_p6));  // open: g
  _7_Segment_Display u_7_segment_display_107 (
    .f(shift_register_2_p6), .a(shift_register_2_p6), .b(shift_register_2_p6), .e(shift_register_2_p6),
    .d(shift_register_2_p6), .c(shift_register_2_p6), .dp(shift_register_2_p6));  // open: g
  _7_Segment_Display u_7_segment_display_108 (
    .f(shift_register_3_p14), .a(shift_register_3_p14), .b(shift_register_3_p14), .e(shift_register_3_p14),
    .d(shift_register_3_p14), .c(shift_register_3_p14), .dp(shift_register_3_p14));  // open: g
  _7_Segment_Display u_7_segment_display_109 (
    .f(shift_register_4_p13), .a(shift_register_4_p13), .b(shift_register_4_p13), .e(shift_register_4_p13),
    .d(shift_register_4_p13), .c(shift_register_4_p13), .dp(shift_register_4_p13));  // open: g
  _7_Segment_Display u_7_segment_display_110 (
    .f(shift_register_5_p11), .a(shift_register_5_p11), .b(shift_register_5_p11), .e(shift_register_5_p11),
    .d(shift_register_5_p11), .c(shift_register_5_p11), .dp(shift_register_5_p11));  // open: g
  _7_Segment_Display u_7_segment_display_111 (
    .f(shift_register_1_p6), .a(shift_register_1_p6), .b(shift_register_1_p6), .e(shift_register_1_p6),
    .d(shift_register_1_p6), .c(shift_register_1_p6), .dp(shift_register_1_p6));  // open: g
  _7_Segment_Display u_7_segment_display_112 (
    .f(shift_register_1_p6), .a(shift_register_1_p6), .b(shift_register_1_p6), .e(shift_register_1_p6),
    .d(shift_register_1_p6), .c(shift_register_1_p6), .dp(shift_register_1_p6));  // open: g
  _7_Segment_Display u_7_segment_display_113 (
    .f(shift_register_1_p3), .a(shift_register_1_p3), .b(shift_register_1_p3), .e(shift_register_1_p3),
    .d(shift_register_1_p3), .c(shift_register_1_p3), .dp(shift_register_1_p3));  // open: g
  _7_Segment_Display u_7_segment_display_114 (
    .f(shift_register_1_p3), .a(shift_register_1_p3), .b(shift_register_1_p3), .e(shift_register_1_p3),
    .d(shift_register_1_p3), .c(shift_register_1_p3), .dp(shift_register_1_p3));  // open: g
  _7_Segment_Display u_7_segment_display_115 (
    .f(shift_register_2_p5), .a(shift_register_2_p5), .b(shift_register_2_p5), .e(shift_register_2_p5),
    .d(shift_register_2_p5), .c(shift_register_2_p5), .dp(shift_register_2_p5));  // open: g
  _7_Segment_Display u_7_segment_display_116 (
    .f(shift_register_3_p13), .a(shift_register_3_p13), .b(shift_register_3_p13), .e(shift_register_3_p13),
    .d(shift_register_3_p13), .c(shift_register_3_p13), .dp(shift_register_3_p13));  // open: g
  _7_Segment_Display u_7_segment_display_117 (
    .f(shift_register_4_p12), .a(shift_register_4_p12), .b(shift_register_4_p12), .e(shift_register_4_p12),
    .d(shift_register_4_p12), .c(shift_register_4_p12), .dp(shift_register_4_p12));  // open: g
  _7_Segment_Display u_7_segment_display_118 (
    .f(shift_register_5_p10), .a(shift_register_5_p10), .b(shift_register_5_p10), .e(shift_register_5_p10),
    .d(shift_register_5_p10), .c(shift_register_5_p10), .dp(shift_register_5_p10));  // open: g
  _7_Segment_Display u_7_segment_display_119 (
    .f(shift_register_1_p3), .a(shift_register_1_p3), .b(shift_register_1_p3), .e(shift_register_1_p3),
    .d(shift_register_1_p3), .c(shift_register_1_p3), .dp(shift_register_1_p3));  // open: g
  _7_Segment_Display u_7_segment_display_120 (
    .f(shift_register_1_p3), .a(shift_register_1_p3), .b(shift_register_1_p3), .e(shift_register_1_p3),
    .d(shift_register_1_p3), .c(shift_register_1_p3), .dp(shift_register_1_p3));  // open: g
  _7_Segment_Display u_7_segment_display_121 (
    .f(shift_register_1_p4), .a(shift_register_1_p4), .b(shift_register_1_p4), .e(shift_register_1_p4),
    .d(shift_register_1_p4), .c(shift_register_1_p4), .dp(shift_register_1_p4));  // open: g
  _7_Segment_Display u_7_segment_display_122 (
    .f(shift_register_1_p4), .a(shift_register_1_p4), .b(shift_register_1_p4), .e(shift_register_1_p4),
    .d(shift_register_1_p4), .c(shift_register_1_p4), .dp(shift_register_1_p4));  // open: g
  _7_Segment_Display u_7_segment_display_123 (
    .f(shift_register_2_p4), .a(shift_register_2_p4), .b(shift_register_2_p4), .e(shift_register_2_p4),
    .d(shift_register_2_p4), .c(shift_register_2_p4), .dp(shift_register_2_p4));  // open: g
  _7_Segment_Display u_7_segment_display_124 (
    .f(shift_register_3_p12), .a(shift_register_3_p12), .b(shift_register_3_p12), .e(shift_register_3_p12),
    .d(shift_register_3_p12), .c(shift_register_3_p12), .dp(shift_register_3_p12));  // open: g
  _7_Segment_Display u_7_segment_display_125 (
    .f(shift_register_4_p11), .a(shift_register_4_p11), .b(shift_register_4_p11), .e(shift_register_4_p11),
    .d(shift_register_4_p11), .c(shift_register_4_p11), .dp(shift_register_4_p11));  // open: g
  _7_Segment_Display u_7_segment_display_126 (
    .f(shift_register_5_p9), .a(shift_register_5_p9), .b(shift_register_5_p9), .e(shift_register_5_p9),
    .d(shift_register_5_p9), .c(shift_register_5_p9), .dp(shift_register_5_p9));  // open: g
  _7_Segment_Display u_7_segment_display_127 (
    .f(shift_register_1_p4), .a(shift_register_1_p4), .b(shift_register_1_p4), .e(shift_register_1_p4),
    .d(shift_register_1_p4), .c(shift_register_1_p4), .dp(shift_register_1_p4));  // open: g
  _7_Segment_Display u_7_segment_display_128 (
    .f(shift_register_1_p4), .a(shift_register_1_p4), .b(shift_register_1_p4), .e(shift_register_1_p4),
    .d(shift_register_1_p4), .c(shift_register_1_p4), .dp(shift_register_1_p4));  // open: g
endmodule

module counter1 (
  input  in_1
);

  wire not_1_out, not_2_out, t_ff_1_q, t_ff_2_q, t_ff_3_q;

  not not_1 (not_1_out, t_ff_3_q);
  T_Flip_Flop t_ff_1 (.T(not_1_out), .clk(in_1), .Q(t_ff_1_q));  // open: Qn, reset, preset
  T_Flip_Flop t_ff_2 (.T(t_ff_1_q), .clk(in_1), .Q(t_ff_2_q));  // open: Qn, reset, preset
  not not_2 (not_2_out, t_ff_2_q);
  T_Flip_Flop t_ff_3 (.T(not_2_out), .clk(in_1), .Q(t_ff_3_q));  // open: Qn, reset, preset
  T_Flip_Flop t_ff_4 (.T(not_1_out), .clk(in_1));  // open: Q, Qn, reset, preset
endmodule

module counter2 (
  input  in_1,
  output out_2
);

  wire t_ff_1_q, t_ff_2_q, undriven;

  T_Flip_Flop t_ff_1 (.T(1'b1), .clk(in_1), .Q(t_ff_1_q), .preset(undriven));  // open: Qn, reset
  T_Flip_Flop t_ff_2 (.T(1'b1), .clk(t_ff_1_q), .Q(t_ff_2_q), .preset(undriven));  // open: Qn, reset
  T_Flip_Flop t_ff_3 (.T(1'b1), .clk(t_ff_2_q), .Qn(out_2), .preset(undriven));  // open: Q, reset
endmodule
