// Logisim project bank.circ as structural Verilog: 2 circuits, main circuit main
module main (
  input  in_1,
  input  [3:0] id,
  input  [3:0] password,
  output [7:0] out_4
);

  wire and_1_out, clock_1_out, comparator_1_eq, comparator_1_gt, decoder_1_out0, decoder_1_out1,
       decoder_1_out2, decoder_1_out3, decoder_1_out4, decoder_1_out5, decoder_1_out6, decoder_1_out7,
       decoder_1_out8, decoder_1_out9, decoder_1_out10, decoder_1_out11, decoder_1_out12, decoder_1_out13,
       decoder_1_out14, decoder_1_out15, or_1_out, t_ff_1_qn, t_ff_2_qn, t_ff_3_qn, t_ff_4_qn, t_ff_5_qn,
       t_ff_6_qn, t_ff_7_qn;
  wire [3:0] and_2_out, bit_extender_1_out;
  wire [7:0] bit_extender_2_out;

  T_Flip_Flop t_ff_1 (.T(1'b1), .clk(clock_1_out), .Q(out_4[0]), .Qn(t_ff_1_qn));  // open: reset, preset
  Clock clock_1 (.out(clock_1_out));
  assign bit_extender_1_out = {{3{1'b1}}, in_1};  // Bit_Extender bit_extender_1
  and and_1 (and_1_out, or_1_out, clock_1_out);
  T_Flip_Flop t_ff_2 (.T(1'b1), .clk(t_ff_1_qn), .Q(out_4[1]), .Qn(t_ff_2_qn));  // open: reset, preset
  assign and_2_out = bit_extender_1_out & id;  // AND_Gate and_2, 4 bits wide
  T_Flip_Flop t_ff_3 (.T(1'b1), .clk(t_ff_2_qn), .Q(out_4[2]), .Qn(t_ff_3_qn));  // open: reset, preset
  Decoder #(.select(4)) decoder_1 (
    .out0(decoder_1_out0), .out1(decoder_1_out1), .out2(decoder_1_out2), .out3(decoder_1_out3),
    .out4(decoder_1_out4), .out5(decoder_1_out5), .out6(decoder_1_out6), .out7(decoder_1_out7),
    .out8(decoder_1_out8), .out9(decoder_1_out9), .out10(decoder_1_out10), .out11(decoder_1_out11),
    .out12(decoder_1_out12), .out13(decoder_1_out13), .out14(decoder_1_out14), .out15(decoder_1_out15),
    .sel(and_2_out));  // open: en
  T_Flip_Flop t_ff_4 (.T(1'b1), .clk(t_ff_3_qn), .Q(out_4[3]), .Qn(t_ff_4_qn));  // open: reset, preset
  Register #(.width(4)) register_1 (.D(password), .en(decoder_1_out0), .clk(and_1_out));  // open: Q, clr
  Register #(.width(4)) register_2 (.D(password), .en(decoder_1_out1), .clk(and_1_out));  // open: Q, clr
  Register #(.width(4)) register_3 (.D(password), .en(decoder_1_out2), .clk(and_1_out));  // open: Q, clr
  Register #(.width(4)) register_4 (.D(password), .en(decoder_1_out4), .clk(and_1_out));  // open: Q, clr
  T_Flip_Flop t_ff_5 (.T(1'b1), .clk(t_ff_4_qn), .Q(out_4[4]), .Qn(t_ff_5_qn));  // open: reset, preset
  Register #(.width(4)) register_5 (.D(password), .en(decoder_1_out3), .clk(and_1_out));  // open: Q, clr
  Register #(.width(4)) register_6 (.D(password), .en(decoder_1_out5), .clk(and_1_out));  // open: Q, clr
  T_Flip_Flop t_ff_6 (.T(1'b1), .clk(t_ff_5_qn), .Q(out_4[5]), .Qn(t_ff_6_qn));  // open: reset, preset
  Register #(.width(4)) register_7 (.D(password), .en(decoder_1_out6), .clk(and_1_out));  // open: Q, clr
  Register #(.width(4)) register_8 (.D(password), .en(decoder_1_out7), .clk(and_1_out));  // open: Q, clr
  Register #(.width(4)) register_9 (.D(password), .en(decoder_1_out8), .clk(and_1_out));  // open: Q, clr
  Register #(.width(4)) register_10 (.D(password), .en(decoder_1_out10), .clk(and_1_out));  // open: Q, clr
  T_Flip_Flop t_ff_7 (.T(1'b1), .clk(t_ff_6_qn), .Q(out_4[6]), .Qn(t_ff_7_qn));  // open: reset, preset
  Register #(.width(4)) register_11 (.D(password), .en(decoder_1_out9), .clk(and_1_out));  // open: Q, clr
  Register #(.width(4)) register_12 (.D(password), .en(decoder_1_out11), .clk(and_1_out));  // open: Q, clr
  Register #(.width(4)) register_13 (.D(password), .en(decoder_1_out12), .clk(and_1_out));  // open: Q, clr
  Register #(.width(4)) register_14 (.D(password), .en(decoder_1_out13), .clk(and_1_out));  // open: Q, clr
  T_Flip_Flop t_ff_8 (.T(1'b1), .clk(t_ff_7_qn), .Q(out_4[7]));  // open: Qn, reset, preset
  Register #(.width(4)) register_15 (.D(password), .en(decoder_1_out14), .clk(and_1_out));  // open: Q, clr
  Register #(.width(4)) register_16 (.D(password), .en(decoder_1_out15), .clk(and_1_out));  // open: Q, clr
  assign bit_extender_2_out = {{6{1'b0}}, 2'b10};  // Bit_Extender bit_extender_2
  Register #(.width(4)) register_17 (.D(and_2_out), .en(in_1));  // open: clk, Q, clr
  Comparator comparator_1 (.a(out_4), .b(bit_extender_2_out), .gt(comparator_1_gt), .eq(comparator_1_eq));  // open: lt
  or or_1 (or_1_out, comparator_1_gt, comparator_1_eq);
endmodule

module test (
  input  [7:0] in_1,
  input  in_2,
  input  in_3
);

  Register register_1 (.D(in_1), .en(in_2), .clk(in_3));  // open: Q, clr
endmodule
