// Logisim project btc_miner.circ as structural Verilog: 2 circuits, main circuit main
module main (
  output [15:0] pc,
  output [6:0] out_2,
  output [31:0] t_2,
  output [31:0] out_4,
  output [31:0] out_5,
  output [31:0] t_7,
  output [31:0] t_15,
  output [31:0] out_8,
  output [31:0] t_16,
  output [31:0] out_10,
  output [3:0] number_of_digit_counter,
  output [5:0] out_12,
  output [5:0] t_2a,
  output [5:0] t_7a,
  output [5:0] out_15,
  output [31:0] rotate_7,
  output [31:0] right_3,
  output [31:0] rotate_18,
  output [5:0] t_15a,
  output [5:0] out_20,
  output [31:0] small_sigma_0,
  output [31:0] sigma_1,
  output [31:0] out_23,
  output [5:0] t_16a,
  output [5:0] out_25,
  output [31:0] ch,
  output [31:0] small_sigma_1,
  output [31:0] out_28,
  output [31:0] out_29,
  output [31:0] out_30,
  output [31:0] out_31,
  output [31:0] out_32,
  output [31:0] out_33,
  output [31:0] sigma_0,
  output [31:0] out_35,
  output [31:0] out_36
);

  wire adder_1_cout, adder_2_cout, and_1_out, and_2_out, and_5_out, and_7_out, and_12_out, and_16_out, b_qn,
       buffer_1_out, buffer_2_out, buffer_3_out, buffer_4_out, buffer_5_out, buffer_6_out, buffer_7_out,
       buffer_8_out, buffer_9_out, buffer_10_out, buffer_11_out, buffer_12_out, buffer_13_out, buffer_14_out,
       c_qn, clock_1_out, clock_2_out, clock_3_out, comparator_1_gt, comparator_2_lt, comparator_3_eq,
       comparator_4_gt, comparator_4_lt, comparator_5_gt, comparator_5_lt, comparator_6_eq, d_ff_1_q,
       d_ff_2_q, d_ff_3_q, d_ff_4_q, d_ff_5_q, d_ff_6_q, d_ff_7_q, d_ff_8_q, d_ff_9_q, d_ff_10_q, d_ff_11_q,
       d_ff_12_q, demultiplexer_1_out1, demultiplexer_1_out2, demultiplexer_1_out3, demultiplexer_1_out4,
       demultiplexer_1_out5, demultiplexer_1_out6, demultiplexer_1_out7, demultiplexer_1_out8,
       demultiplexer_1_out9, demultiplexer_1_out10, demultiplexer_1_out11, demultiplexer_1_out12,
       demultiplexer_2_out0, demultiplexer_2_out1, demultiplexer_2_out2, demultiplexer_2_out3,
       demultiplexer_2_out4, demultiplexer_2_out5, demultiplexer_2_out6, demultiplexer_2_out7,
       demultiplexer_3_out0, demultiplexer_3_out1, keyboard_1_avail, not_1_out, not_2_out, not_3_out,
       not_9_out, or_2_out, or_3_out, or_4_out, or_5_out, or_6_out, or_7_out, or_8_out, or_9_out, or_10_out,
       pull_resistor_16_node, t_ff_1_qn, t_ff_2_qn, t_ff_3_qn, t_ff_4_qn, t_ff_5_qn, t_ff_6_qn, t_ff_8_qn,
       t_ff_9_qn, t_ff_10_qn, t_ff_11_qn, t_ff_12_qn, t_ff_13_qn, t_ff_14_qn, t_ff_15_qn, t_ff_16_qn,
       t_ff_17_qn, t_ff_18_qn, t_ff_19_qn, t_ff_21_qn, t_ff_22_qn, t_ff_23_qn, t_ff_24_qn, t_ff_25_qn,
       t_ff_26_qn, t_ff_27_qn, t_ff_28_qn, t_ff_29_qn, t_ff_30_qn, t_ff_31_qn, t_ff_34_qn, t_ff_35_qn,
       t_ff_36_qn, t_ff_37_qn, t_ff_38_qn, undriven, undriven_2, undriven_3, undriven_4, undriven_5;
  wire [2:0] multiplexer_23_out, multiplexer_23_out_2, t_ff_29_q;
  wire [5:0] adder_4_out, adder_6_out, and_6_out, b_q, bit_extender_5_out, bit_extender_6_out,
       bit_extender_7_out, bit_extender_8_out, bit_extender_9_out, bit_extender_10_out, bit_extender_11_out,
       bit_extender_13_out, not_5_out, not_6_out, not_7_out, not_8_out, t_ff_23_q, t_ff_34_q;
  wire [5:5] subtractor_1_bout, subtractor_2_bout, subtractor_3_bout, subtractor_4_bout;
  wire [7:0] bit_extender_1_out, demultiplexer_4_out16, demultiplexer_4_out24, demultiplexer_5_out0,
       demultiplexer_5_out8, demultiplexer_5_out16, demultiplexer_5_out24, pull_resistor_1_node,
       register_1_q, register_2_q, register_3_q, register_4_q, register_5_q, register_6_q, register_7_q,
       register_8_q, register_9_q, register_10_q, register_11_q, register_12_q, register_13_q, register_14_q,
       register_17_q;
  wire [15:0] bit_extender_2_out, bit_extender_3_out, bit_extender_12_out;
  wire [31:0] aa_q, aaa_q, adder_1_out, adder_2_out, adder_5_out, adder_7_out, adder_8_out, adder_9_out,
       adder_10_out, adder_11_out, adder_12_out, and_3_out, and_4_out, and_13_out, and_14_out, and_15_out,
       bb_q, bbb_q, bit_extender_4_out, cc_q, ccc_q, dd_q, ee_q, ff_q, gg_q, h_values_data, k_values_data,
       multiplexer_9_out, multiplexer_10_out, multiplexer_11_out, multiplexer_12_out, multiplexer_13_out,
       multiplexer_14_out, multiplexer_15_out, multiplexer_16_out, multiplexer_26_out, multiplexer_27_out,
       multiplexer_28_out, multiplexer_29_out, multiplexer_30_out, multiplexer_31_out, multiplexer_32_out,
       multiplexer_33_out, multiplexer_34_out, multiplexer_35_out, multiplexer_37_out, not_4_out, or_11_out,
       register_18_q, register_19_q, register_20_q, register_21_q, register_22_q, register_23_q,
       register_24_q, register_25_q, register_26_q, register_27_q, register_28_q, register_29_q,
       register_30_q, register_31_q, register_32_q, register_33_q, register_34_q, register_35_q,
       register_36_q, register_37_q, register_38_q, register_39_q, register_40_q, register_41_q,
       register_42_q, register_43_q, register_44_q, register_45_q, register_46_q, register_47_q,
       register_48_q, register_49_q, register_50_q, register_51_q, register_52_q, register_53_q,
       register_54_q, register_55_q, register_56_q, register_57_q, register_58_q, register_59_q,
       register_60_q, register_61_q, register_62_q, register_63_q, register_64_q, register_65_q,
       register_66_q, register_67_q, register_68_q, register_69_q, register_70_q, register_71_q,
       register_72_q, register_73_q, register_74_q, register_75_q, register_76_q, register_77_q,
       register_78_q, register_79_q, register_80_q, register_81_q, register_82_q, register_83_q,
       register_84_q, t1_q, t2_q, w0_q, w1_q, xor_1_out, xor_2_out, xor_4_out, xor_7_out;

  Clock clock_1 (.out(clock_1_out));
  T_Flip_Flop t_ff_1 (
    .T(1'b1), .clk(buffer_2_out), .Q(number_of_digit_counter[0]), .Qn(t_ff_1_qn));  // open: reset, preset
  T_Flip_Flop t_ff_2 (.T(1'b1), .clk(clock_1_out), .Q(pc[0]), .Qn(t_ff_2_qn));  // open: reset, preset
  Demultiplexer #(.select(4)) demultiplexer_1 (
    .out1(demultiplexer_1_out1), .out2(demultiplexer_1_out2), .out3(demultiplexer_1_out3),
    .out4(demultiplexer_1_out4), .out5(demultiplexer_1_out5), .out6(demultiplexer_1_out6),
    .out7(demultiplexer_1_out7), .out8(demultiplexer_1_out8), .out9(demultiplexer_1_out9),
    .out10(demultiplexer_1_out10), .out11(demultiplexer_1_out11), .out12(demultiplexer_1_out12), .in(1'b1),
    .sel(number_of_digit_counter));  // open: out0, out13, out14, out15
  T_Flip_Flop t_ff_3 (
    .T(1'b1), .clk(t_ff_1_qn), .Q(number_of_digit_counter[1]), .Qn(t_ff_3_qn));  // open: reset, preset
  T_Flip_Flop t_ff_4 (.T(1'b1), .clk(t_ff_2_qn), .Q(pc[1]), .Qn(t_ff_4_qn));  // open: reset, preset
  Keyboard keyboard_1 (.clk(clock_1_out), .avail(keyboard_1_avail), .data(out_2));  // open: re, clr
  T_Flip_Flop t_ff_5 (
    .T(1'b1), .clk(t_ff_3_qn), .Q(number_of_digit_counter[2]), .Qn(t_ff_5_qn));  // open: reset, preset
  T_Flip_Flop t_ff_6 (.T(1'b1), .clk(t_ff_4_qn), .Q(pc[2]), .Qn(t_ff_6_qn));  // open: reset, preset
  D_Flip_Flop d_ff_1 (.D(demultiplexer_1_out9), .clk(clock_1_out), .Q(d_ff_1_q));  // open: Qn, preset, reset
  D_Flip_Flop d_ff_2 (.D(demultiplexer_1_out10), .clk(clock_1_out), .Q(d_ff_2_q));  // open: Qn, preset, reset
  D_Flip_Flop d_ff_3 (.D(demultiplexer_1_out11), .clk(clock_1_out), .Q(d_ff_3_q));  // open: Qn, preset, reset
  D_Flip_Flop d_ff_4 (.D(demultiplexer_1_out12), .clk(clock_1_out), .Q(d_ff_4_q));  // open: Qn, preset, reset
  T_Flip_Flop t_ff_7 (.T(1'b1), .clk(t_ff_5_qn), .Q(number_of_digit_counter[3]));  // open: Qn, reset, preset
  T_Flip_Flop t_ff_8 (.T(1'b1), .clk(t_ff_6_qn), .Q(pc[3]), .Qn(t_ff_8_qn));  // open: reset, preset
  and and_1 (and_1_out, keyboard_1_avail, clock_1_out);
  T_Flip_Flop t_ff_9 (.T(1'b1), .clk(t_ff_8_qn), .Q(pc[4]), .Qn(t_ff_9_qn));  // open: reset, preset
  assign bit_extender_1_out = {{1{1'b0}}, out_2};  // Bit_Extender bit_extender_1
  buf buffer_1 (buffer_1_out, clock_1_out);
  T_Flip_Flop t_ff_10 (.T(1'b1), .clk(t_ff_9_qn), .Q(pc[5]), .Qn(t_ff_10_qn));  // open: reset, preset
  Register register_1 (.D(bit_extender_1_out), .clk(clock_1_out), .Q(register_1_q));  // open: en, clr
  buf buffer_2 (buffer_2_out, buffer_1_out);
  D_Flip_Flop d_ff_5 (.D(demultiplexer_1_out1), .clk(clock_1_out), .Q(d_ff_5_q));  // open: Qn, preset, reset
  D_Flip_Flop d_ff_6 (.D(demultiplexer_1_out2), .clk(clock_1_out), .Q(d_ff_6_q));  // open: Qn, preset, reset
  D_Flip_Flop d_ff_7 (.D(demultiplexer_1_out3), .clk(clock_1_out), .Q(d_ff_7_q));  // open: Qn, preset, reset
  D_Flip_Flop d_ff_8 (.D(demultiplexer_1_out4), .clk(clock_1_out), .Q(d_ff_8_q));  // open: Qn, preset, reset
  D_Flip_Flop d_ff_9 (.D(demultiplexer_1_out5), .clk(clock_1_out), .Q(d_ff_9_q));  // open: Qn, preset, reset
  D_Flip_Flop d_ff_10 (.D(demultiplexer_1_out6), .clk(clock_1_out), .Q(d_ff_10_q));  // open: Qn, preset, reset
  D_Flip_Flop d_ff_11 (.D(demultiplexer_1_out7), .clk(clock_1_out), .Q(d_ff_11_q));  // open: Qn, preset, reset
  D_Flip_Flop d_ff_12 (.D(demultiplexer_1_out8), .clk(clock_1_out), .Q(d_ff_12_q));  // open: Qn, preset, reset
  T_Flip_Flop t_ff_11 (.T(1'b1), .clk(t_ff_10_qn), .Q(pc[6]), .Qn(t_ff_11_qn));  // open: reset, preset
  T_Flip_Flop t_ff_12 (.T(1'b1), .clk(t_ff_11_qn), .Q(pc[7]), .Qn(t_ff_12_qn));  // open: reset, preset
  T_Flip_Flop t_ff_13 (.T(1'b1), .clk(t_ff_12_qn), .Q(pc[8]), .Qn(t_ff_13_qn));  // open: reset, preset
  Register register_2 (.D(register_1_q), .clk(d_ff_5_q), .Q(register_2_q));  // open: en, clr
  Register register_3 (.D(register_1_q), .clk(d_ff_6_q), .Q(register_3_q));  // open: en, clr
  Register register_4 (.D(register_1_q), .clk(d_ff_7_q), .Q(register_4_q));  // open: en, clr
  Register register_5 (.D(register_1_q), .clk(d_ff_8_q), .Q(register_5_q));  // open: en, clr
  Register register_6 (.D(register_1_q), .clk(d_ff_9_q), .Q(register_6_q));  // open: en, clr
  Register register_7 (.D(register_1_q), .clk(d_ff_10_q), .Q(register_7_q));  // open: en, clr
  Register register_8 (.D(register_1_q), .clk(d_ff_11_q), .Q(register_8_q));  // open: en, clr
  Register register_9 (.D(register_1_q), .clk(d_ff_12_q), .Q(register_9_q));  // open: en, clr
  T_Flip_Flop t_ff_14 (.T(1'b1), .clk(t_ff_13_qn), .Q(pc[9]), .Qn(t_ff_14_qn));  // open: reset, preset
  T_Flip_Flop t_ff_15 (.T(1'b1), .clk(t_ff_14_qn), .Q(pc[10]), .Qn(t_ff_15_qn));  // open: reset, preset
  T_Flip_Flop t_ff_16 (.T(1'b1), .clk(t_ff_15_qn), .Q(pc[11]), .Qn(t_ff_16_qn));  // open: reset, preset
  T_Flip_Flop t_ff_17 (.T(1'b1), .clk(t_ff_16_qn), .Q(pc[12]), .Qn(t_ff_17_qn));  // open: reset, preset
  Pull_Resistor pull_resistor_1 (.node(pull_resistor_1_node));
  T_Flip_Flop t_ff_18 (.T(1'b1), .clk(t_ff_17_qn), .Q(pc[13]), .Qn(t_ff_18_qn));  // open: reset, preset
  Register register_10 (.D(register_1_q), .clk(d_ff_1_q), .Q(register_10_q));  // open: en, clr
  Register register_11 (.D(register_1_q), .clk(d_ff_2_q), .Q(register_11_q));  // open: en, clr
  Register register_12 (.D(register_1_q), .clk(d_ff_3_q), .Q(register_12_q));  // open: en, clr
  Register register_13 (.D(register_1_q), .clk(d_ff_4_q), .Q(register_13_q));  // open: en, clr
  Register register_14 (.D(8'h80), .clk(buffer_2_out), .Q(register_14_q));  // open: en, clr
  Register register_15 (.D(pull_resistor_1_node), .clk(buffer_2_out));  // open: en, Q, clr
  Register register_16 (.D(pull_resistor_1_node), .clk(buffer_2_out));  // open: en, Q, clr
  Register register_17 (.D(8'h60), .clk(buffer_2_out), .Q(register_17_q));  // open: en, clr
  assign bit_extender_2_out = {{12{1'b0}}, 4'b0011};  // Bit_Extender bit_extender_2
  T_Flip_Flop t_ff_19 (.T(1'b1), .clk(t_ff_18_qn), .Q(pc[14]), .Qn(t_ff_19_qn), .preset(undriven));  // open: reset
  T_Flip_Flop t_ff_20 (.T(1'b1), .clk(t_ff_19_qn), .Q(pc[15]));  // open: Qn, reset, preset
  Comparator #(.width(16)) comparator_1 (.a(bit_extender_2_out), .b(pc), .gt(comparator_1_gt));  // open: eq, lt
  not not_1 (not_1_out, comparator_1_gt);
  assign bit_extender_3_out = {{12{1'b0}}, 4'b1111};  // Bit_Extender bit_extender_3
  not not_2 (not_2_out, and_5_out);
  Comparator #(.width(16)) comparator_2 (.a(bit_extender_3_out), .b(pc), .lt(comparator_2_lt));  // open: gt, eq
  Register #(.width(32)) w0 (
    .D({register_2_q, register_3_q, register_4_q, register_5_q}), .clk(and_2_out), .Q(w0_q));  // open: en, clr
  Register #(.width(32)) w1 (
    .D({register_6_q, register_7_q, register_8_q, register_9_q}), .clk(and_2_out), .Q(w1_q));  // open: en, clr
  and and_2 (and_2_out, not_1_out, not_2_out, clock_1_out);
  assign bit_extender_4_out = {{24{1'b0}}, register_17_q};  // Bit_Extender bit_extender_4
  assign xor_1_out = {aa_q[19], aa_q[20], aa_q[18:0], aa_q[31:21]} ^ aa_q;  // XOR_Gate xor_1, 32 bits wide
  not not_3 (not_3_out, comparator_2_lt);
  assign xor_2_out = {right_3[14:0], rotate_7[27:25], right_3[28:15]} ^ {right_3[3:0], rotate_7[27:25], right_3[28:4]};  // XOR_Gate xor_2, 32 bits wide
  assign sigma_0 = xor_1_out ^ {aa_q[8:0], aa_q[31:9]};  // XOR_Gate xor_3, 32 bits wide
  assign xor_4_out = multiplexer_34_out ^ {multiplexer_34_out[1:0], multiplexer_34_out[31:2]};  // XOR_Gate xor_4, 32 bits wide
  Register #(.width(32)) register_18 (
    .D({register_10_q, register_11_q, register_12_q, register_13_q}), .clk(and_2_out), .Q(register_18_q));  // open: en, clr
  assign small_sigma_0 = xor_2_out ^ {3'b000, right_3[28:0]};  // XOR_Gate xor_5, 32 bits wide
  assign small_sigma_1 = xor_4_out ^ {{10{1'b0}}, multiplexer_34_out[14:0], multiplexer_34_out[31:25]};  // XOR_Gate xor_6, 32 bits wide
  Pull_Resistor pull_resistor_2 (.node(and_2_out));
  Register #(.width(32)) register_19 (
    .D({register_14_q, {24{1'b0}}}), .clk(and_2_out), .Q(register_19_q));  // open: en, clr
  Adder #(.width(32)) adder_1 (
    .a(small_sigma_0), .b(small_sigma_1), .out(adder_1_out), .cout(adder_1_cout));  // open: cin
  buf buffer_3 (buffer_3_out, and_2_out);
  Pull_Resistor pull_resistor_3 (.node(buffer_3_out));
  Adder #(.width(32)) adder_2 (
    .a(adder_1_out), .b(multiplexer_35_out), .out(adder_2_out), .cin(undriven_2), .cout(adder_2_cout));
  Adder #(.width(32)) adder_3 (.a(adder_2_out), .b(multiplexer_37_out), .out(out_23), .cin(undriven_3));  // open: cout
  Register #(.width(32)) register_20 (
    .D(out_23), .en(demultiplexer_5_out0[0]), .clk(buffer_4_out), .Q(register_20_q));  // open: clr
  Register #(.width(32)) register_21 (
    .D(out_23), .en(demultiplexer_5_out0[1]), .clk(buffer_4_out), .Q(register_21_q));  // open: clr
  Register #(.width(32)) register_22 (
    .D(out_23), .en(demultiplexer_5_out0[2]), .clk(buffer_4_out), .Q(register_22_q));  // open: clr
  Register #(.width(32)) register_23 (
    .D(out_23), .en(demultiplexer_5_out0[3]), .clk(buffer_4_out), .Q(register_23_q));  // open: clr
  Register #(.width(32)) register_24 (
    .D(out_23), .en(demultiplexer_5_out0[4]), .clk(buffer_4_out), .Q(register_24_q));  // open: clr
  Register #(.width(32)) register_25 (
    .D(out_23), .en(demultiplexer_5_out0[5]), .clk(buffer_4_out), .Q(register_25_q));  // open: clr
  Register #(.width(32)) register_26 (
    .D(out_23), .en(demultiplexer_5_out0[6]), .clk(buffer_4_out), .Q(register_26_q));  // open: clr
  Register #(.width(32)) register_27 (
    .D(out_23), .en(demultiplexer_5_out0[7]), .clk(buffer_4_out), .Q(register_27_q));  // open: clr
  assign not_4_out = ~{ee_q[0], ee_q[1], ee_q[2], ee_q[3], ee_q[4], ee_q[5], ee_q[31:6]};  // NOT_Gate not_4, 32 bits wide
  Multiplexer #(.select(3), .width(32)) multiplexer_1 (
    .in0(register_20_q), .in1(register_21_q), .in2(register_22_q), .in3(register_23_q), .in4(register_24_q),
    .in5(register_25_q), .in6(register_26_q), .in7(register_27_q), .out(out_28), .sel(multiplexer_23_out));
  Register #(.width(32)) register_28 (.D(w0_q), .en(not_3_out), .clk(buffer_3_out), .Q(register_28_q));  // open: clr
  Register #(.width(32)) register_29 (.D(w1_q), .en(not_3_out), .clk(buffer_3_out), .Q(register_29_q));  // open: clr
  Register #(.width(32)) register_30 (
    .D(register_18_q), .en(not_3_out), .clk(buffer_3_out), .Q(register_30_q));  // open: clr
  Register #(.width(32)) register_31 (
    .D(register_19_q), .en(not_3_out), .clk(buffer_3_out), .Q(register_31_q));  // open: clr
  Register #(.width(32)) register_32 (
    .D({32{1'b0}}), .en(not_3_out), .clk(buffer_3_out), .Q(register_32_q));  // open: clr
  Register #(.width(32)) register_33 (
    .D({32{1'b0}}), .en(not_3_out), .clk(buffer_3_out), .Q(register_33_q));  // open: clr
  Register #(.width(32)) register_34 (
    .D({32{1'b0}}), .en(not_3_out), .clk(buffer_3_out), .Q(register_34_q));  // open: clr
  Register #(.width(32)) register_35 (
    .D({32{1'b0}}), .en(not_3_out), .clk(buffer_3_out), .Q(register_35_q));  // open: clr
  assign and_3_out = ff_q & {ee_q[0], ee_q[1], ee_q[2], ee_q[3], ee_q[4], ee_q[5], ee_q[31:6]};  // AND_Gate and_3, 32 bits wide
  assign and_4_out = gg_q & not_4_out;  // AND_Gate and_4, 32 bits wide
  Multiplexer #(.select(3), .width(32)) multiplexer_2 (
    .in0(register_20_q), .in1(register_21_q), .in2(register_22_q), .in3(register_23_q), .in4(register_24_q),
    .in5(register_25_q), .in6(register_26_q), .in7(register_27_q), .out(out_30), .sel(t_7a[2:0]));
  ROM #(.addrWidth(6), .dataWidth(32)) k_values (.addr(b_q), .data(k_values_data));
  Multiplexer #(.select(3), .width(32)) multiplexer_3 (
    .in0(register_20_q), .in1(register_21_q), .in2(register_22_q), .in3(register_23_q), .in4(register_24_q),
    .in5(register_25_q), .in6(register_26_q), .in7(register_27_q), .out(out_32), .sel(t_15a[2:0]));
  assign ch = and_3_out | and_4_out;  // OR_Gate or_1, 32 bits wide
  Multiplexer #(.select(3), .width(32)) multiplexer_4 (
    .in0(register_20_q), .in1(register_21_q), .in2(register_22_q), .in3(register_23_q), .in4(register_24_q),
    .in5(register_25_q), .in6(register_26_q), .in7(register_27_q), .out(out_35), .sel(t_16a[2:0]));
  ROM #(.addrWidth(6), .dataWidth(32)) rom_1 ();  // open: addr, data
  T_Flip_Flop b (.T(not_1_out), .clk(clock_1_out), .Q(b_q[0]), .Qn(b_qn), .reset(undriven_5), .preset(undriven_4));
  assign xor_7_out = {ee_q[0], ee_q[1], ee_q[2], ee_q[3], ee_q[4], ee_q[5], ee_q[31:6]} ^ {ee_q[10:0], ee_q[31:11]};  // XOR_Gate xor_7, 32 bits wide
  Register #(.width(32)) register_36 (
    .D(out_23), .en(demultiplexer_5_out8[0]), .clk(buffer_4_out), .Q(register_36_q));  // open: clr
  Register #(.width(32)) register_37 (
    .D(out_23), .en(demultiplexer_5_out8[1]), .clk(buffer_4_out), .Q(register_37_q));  // open: clr
  Register #(.width(32)) register_38 (
    .D(out_23), .en(demultiplexer_5_out8[2]), .clk(buffer_4_out), .Q(register_38_q));  // open: clr
  Register #(.width(32)) register_39 (
    .D(out_23), .en(demultiplexer_5_out8[3]), .clk(buffer_4_out), .Q(register_39_q));  // open: clr
  Register #(.width(32)) register_40 (
    .D(out_23), .en(demultiplexer_5_out8[4]), .clk(buffer_4_out), .Q(register_40_q));  // open: clr
  Register #(.width(32)) register_41 (
    .D(out_23), .en(demultiplexer_5_out8[5]), .clk(buffer_4_out), .Q(register_41_q));  // open: clr
  Register #(.width(32)) register_42 (
    .D(out_23), .en(demultiplexer_5_out8[6]), .clk(buffer_4_out), .Q(register_42_q));  // open: clr
  Register #(.width(32)) register_43 (
    .D(out_23), .en(demultiplexer_5_out8[7]), .clk(buffer_4_out), .Q(register_43_q));  // open: clr
  Multiplexer #(.select(3), .width(32)) multiplexer_5 (
    .in0(register_28_q), .in1(register_29_q), .in2(register_30_q), .in3(register_31_q), .in4(register_32_q),
    .in5(register_33_q), .in6(register_34_q), .in7(register_35_q), .out(t_2), .sel(multiplexer_23_out));
  Multiplexer #(.select(3), .width(32)) multiplexer_6 (
    .in0(register_28_q), .in1(register_29_q), .in2(register_30_q), .in3(register_31_q), .in4(register_32_q),
    .in5(register_33_q), .in6(register_34_q), .in7(register_35_q), .out(t_7), .sel(t_7a[2:0]));
  buf buffer_4 (buffer_4_out, buffer_3_out);
  Pull_Resistor pull_resistor_4 (.node(b_q[0]));
  T_Flip_Flop c (.T(not_1_out), .clk(b_qn), .Q(b_q[1]), .Qn(c_qn), .reset(undriven_5), .preset(undriven_4));
  Pull_Resistor #(.pull(1)) pull_resistor_5 (.node(b_qn));
  assign sigma_1 = xor_7_out ^ {ee_q[24:0], ee_q[31:25]};  // XOR_Gate xor_8, 32 bits wide
  Pull_Resistor pull_resistor_6 (.node(b_q[1]));
  T_Flip_Flop t_ff_21 (.T(not_1_out), .clk(c_qn), .Q(b_q[2]), .Qn(t_ff_21_qn), .reset(undriven_5), .preset(undriven_4));
  Pull_Resistor #(.pull(1)) pull_resistor_7 (.node(c_qn));
  Multiplexer #(.select(3), .width(32)) multiplexer_7 (
    .in0(register_28_q), .in1(register_29_q), .in2(register_30_q), .in3(register_31_q), .in4(register_32_q),
    .in5(register_33_q), .in6(register_34_q), .in7(register_35_q), .out(t_15), .sel(t_15a[2:0]));
  Pull_Resistor pull_resistor_8 (.node(b_q[2]));
  T_Flip_Flop t_ff_22 (
    .T(not_1_out), .clk(t_ff_21_qn), .Q(b_q[3]), .Qn(t_ff_22_qn), .reset(undriven_5), .preset(undriven_4));
  Pull_Resistor #(.pull(1)) pull_resistor_9 (.node(t_ff_21_qn));
  assign bit_extender_5_out = {{5{1'b1}}, 1'b1};  // Bit_Extender bit_extender_5
  Comparator #(.width(16)) comparator_3 (.a(pc), .b(16'h8), .eq(comparator_3_eq));  // open: gt, lt
  T_Flip_Flop t_ff_23 (
    .T(comparator_5_gt), .clk(clock_2_out), .Q(t_ff_23_q[0]), .Qn(t_ff_23_qn), .preset(and_7_out));  // open: reset
  Clock clock_2 (.out(clock_2_out));
  Multiplexer #(.select(3), .width(32)) multiplexer_8 (
    .in0(register_28_q), .in1(register_29_q), .in2(register_30_q), .in3(register_31_q), .in4(register_32_q),
    .in5(register_33_q), .in6(register_34_q), .in7(register_35_q), .out(t_16), .sel(t_16a[2:0]));
  Pull_Resistor pull_resistor_10 (.node(b_q[3]));
  T_Flip_Flop t_ff_24 (
    .T(not_1_out), .clk(t_ff_22_qn), .Q(b_q[4]), .Qn(t_ff_24_qn), .reset(undriven_5));  // open: preset
  Pull_Resistor #(.pull(1)) pull_resistor_11 (.node(t_ff_22_qn));
  and and_5 (and_5_out, and_6_out[0], and_6_out[1], and_6_out[2], and_6_out[4], and_6_out[5], and_6_out[3]);
  Multiplexer #(.select(3), .width(32)) multiplexer_9 (
    .in0(register_36_q), .in1(register_37_q), .in2(register_38_q), .in3(register_39_q), .in4(register_40_q),
    .in5(register_41_q), .in6(register_42_q), .in7(register_43_q), .out(multiplexer_9_out),
    .sel(multiplexer_23_out));
  ROM #(.addrWidth(3), .dataWidth(32)) h_values (.addr(t_ff_29_q), .data(h_values_data));
  T_Flip_Flop t_ff_25 (
    .T(comparator_5_gt), .clk(t_ff_23_qn), .Q(t_ff_23_q[1]), .Qn(t_ff_25_qn), .preset(and_7_out));  // open: reset
  Register #(.width(32)) register_44 (.D({32{1'b0}}), .clk(buffer_4_out), .Q(register_44_q));  // open: en, clr
  Register #(.width(32)) register_45 (.D({32{1'b0}}), .clk(buffer_4_out), .Q(register_45_q));  // open: en, clr
  Register #(.width(32)) register_46 (.D({32{1'b0}}), .clk(buffer_4_out), .Q(register_46_q));  // open: en, clr
  Register #(.width(32)) register_47 (.D({32{1'b0}}), .clk(buffer_4_out), .Q(register_47_q));  // open: en, clr
  Register #(.width(32)) register_48 (.D({32{1'b0}}), .clk(buffer_4_out), .Q(register_48_q));  // open: en, clr
  Register #(.width(32)) register_49 (.D({32{1'b0}}), .clk(buffer_4_out), .Q(register_49_q));  // open: en, clr
  Register #(.width(32)) register_50 (.D({32{1'b0}}), .clk(buffer_4_out), .Q(register_50_q));  // open: en, clr
  Register #(.width(32)) register_51 (.D(bit_extender_4_out), .clk(buffer_4_out), .Q(register_51_q));  // open: en, clr
  Pull_Resistor pull_resistor_12 (.node(b_q[4]));
  T_Flip_Flop t_ff_26 (
    .T(not_1_out), .clk(t_ff_24_qn), .Q(b_q[5]), .Qn(t_ff_26_qn), .reset(undriven_5), .preset(undriven_4));
  Pull_Resistor #(.pull(1)) pull_resistor_13 (.node(t_ff_24_qn));
  assign and_6_out = adder_4_out & bit_extender_5_out;  // AND_Gate and_6, 6 bits wide
  Multiplexer #(.select(3), .width(32)) multiplexer_10 (
    .in0(register_36_q), .in1(register_37_q), .in2(register_38_q), .in3(register_39_q), .in4(register_40_q),
    .in5(register_41_q), .in6(register_42_q), .in7(register_43_q), .out(multiplexer_10_out), .sel(t_7a[2:0]));
  ROM #(.addrWidth(3), .dataWidth(32)) rom_2 ();  // open: addr, data
  Pull_Resistor pull_resistor_14 (.node(b_q[5]));
  Pull_Resistor #(.pull(1)) pull_resistor_15 (.node(t_ff_26_qn));
  Multiplexer #(.select(3), .width(32)) multiplexer_11 (
    .in0(register_36_q), .in1(register_37_q), .in2(register_38_q), .in3(register_39_q), .in4(register_40_q),
    .in5(register_41_q), .in6(register_42_q), .in7(register_43_q), .out(multiplexer_11_out), .sel(t_15a[2:0]));
  T_Flip_Flop t_ff_27 (
    .T(comparator_5_gt), .clk(t_ff_25_qn), .Q(t_ff_23_q[2]), .Qn(t_ff_27_qn), .preset(and_7_out));  // open: reset
  Multiplexer #(.select(3), .width(32)) multiplexer_12 (
    .in0(register_36_q), .in1(register_37_q), .in2(register_38_q), .in3(register_39_q), .in4(register_40_q),
    .in5(register_41_q), .in6(register_42_q), .in7(register_43_q), .out(multiplexer_12_out), .sel(t_16a[2:0]));
  Clock clock_3 (.out(clock_3_out));
  T_Flip_Flop t_ff_28 (
    .T(comparator_5_gt), .clk(t_ff_27_qn), .Q(t_ff_23_q[3]), .Qn(t_ff_28_qn), .preset(and_7_out));  // open: reset
  Register #(.width(32)) register_52 (
    .D(out_23), .en(demultiplexer_5_out16[0]), .clk(buffer_4_out), .Q(register_52_q));  // open: clr
  Register #(.width(32)) register_53 (
    .D(out_23), .en(demultiplexer_5_out16[1]), .clk(buffer_4_out), .Q(register_53_q));  // open: clr
  Register #(.width(32)) register_54 (
    .D(out_23), .en(demultiplexer_5_out16[2]), .clk(buffer_4_out), .Q(register_54_q));  // open: clr
  Register #(.width(32)) register_55 (
    .D(out_23), .en(demultiplexer_5_out16[3]), .clk(buffer_4_out), .Q(register_55_q));  // open: clr
  Register #(.width(32)) register_56 (
    .D(out_23), .en(demultiplexer_5_out16[4]), .clk(buffer_4_out), .Q(register_56_q));  // open: clr
  Register #(.width(32)) register_57 (
    .D(out_23), .en(demultiplexer_5_out16[5]), .clk(buffer_4_out), .Q(register_57_q));  // open: clr
  T_Flip_Flop t_ff_29 (
    .T(1'b1), .clk(clock_3_out), .Q(t_ff_29_q[0]), .Qn(t_ff_29_qn), .preset(and_12_out));  // open: reset
  T_Flip_Flop t_ff_30 (
    .T(comparator_5_gt), .clk(t_ff_28_qn), .Q(t_ff_23_q[4]), .Qn(t_ff_30_qn), .preset(and_7_out));  // open: reset
  Multiplexer #(.select(3), .width(32)) multiplexer_13 (
    .in0(register_44_q), .in1(register_45_q), .in2(register_46_q), .in3(register_47_q), .in4(register_48_q),
    .in5(register_49_q), .in6(register_50_q), .in7(register_51_q), .out(multiplexer_13_out),
    .sel(multiplexer_23_out));
  assign bit_extender_6_out = {{5{1'b0}}, 1'b1};  // Bit_Extender bit_extender_6
  assign bit_extender_7_out = {{4{1'b0}}, 2'b10};  // Bit_Extender bit_extender_7
  assign bit_extender_8_out = {{3{1'b0}}, 3'b111};  // Bit_Extender bit_extender_8
  assign bit_extender_9_out = {{2{1'b0}}, 4'b1111};  // Bit_Extender bit_extender_9
  assign bit_extender_10_out = {{1{1'b0}}, 5'b10000};  // Bit_Extender bit_extender_10
  Register #(.width(32)) register_58 (
    .D(out_23), .en(demultiplexer_5_out16[6]), .clk(buffer_4_out), .Q(register_58_q));  // open: clr
  Register #(.width(32)) register_59 (
    .D(out_23), .en(demultiplexer_5_out16[7]), .clk(buffer_4_out), .Q(register_59_q));  // open: clr
  T_Flip_Flop t_ff_31 (
    .T(1'b1), .clk(t_ff_29_qn), .Q(t_ff_29_q[1]), .Qn(t_ff_31_qn), .preset(and_12_out));  // open: reset
  T_Flip_Flop t_ff_32 (.T(comparator_5_gt), .clk(t_ff_30_qn), .Q(t_ff_23_q[5]), .preset(and_7_out));  // open: Qn, reset
  Multiplexer #(.select(3), .width(32)) multiplexer_14 (
    .in0(register_44_q), .in1(register_45_q), .in2(register_46_q), .in3(register_47_q), .in4(register_48_q),
    .in5(register_49_q), .in6(register_50_q), .in7(register_51_q), .out(multiplexer_14_out), .sel(t_7a[2:0]));
  Adder #(.width(6)) adder_4 (.a(bit_extender_6_out), .b(b_q), .out(adder_4_out));  // open: cin, cout
  Subtractor #(.width(6)) subtractor_1 (
    .a(adder_4_out), .b(bit_extender_7_out), .out(out_12), .bout(subtractor_1_bout[5]));  // open: bin
  Subtractor #(.width(6)) subtractor_2 (
    .a(adder_4_out), .b(bit_extender_8_out), .out(out_15), .bout(subtractor_2_bout[5]));  // open: bin
  T_Flip_Flop t_ff_33 (.T(1'b1), .clk(t_ff_31_qn), .Q(t_ff_29_q[2]), .preset(and_12_out));  // open: Qn, reset
  Multiplexer #(.select(3), .width(32)) multiplexer_15 (
    .in0(register_44_q), .in1(register_45_q), .in2(register_46_q), .in3(register_47_q), .in4(register_48_q),
    .in5(register_49_q), .in6(register_50_q), .in7(register_51_q), .out(multiplexer_15_out), .sel(t_15a[2:0]));
  assign not_5_out = ~{6{subtractor_1_bout[5]}};  // NOT_Gate not_5, 6 bits wide
  assign not_6_out = ~{6{subtractor_2_bout[5]}};  // NOT_Gate not_6, 6 bits wide
  Subtractor #(.width(6)) subtractor_3 (
    .a(adder_4_out), .b(bit_extender_9_out), .out(out_20), .bout(subtractor_3_bout[5]));  // open: bin
  Subtractor #(.width(6)) subtractor_4 (
    .a(adder_4_out), .b(bit_extender_10_out), .out(out_25), .bout(subtractor_4_bout[5]));  // open: bin
  and and_7 (and_7_out, t_ff_23_q[0], t_ff_23_q[1], t_ff_23_q[2], t_ff_23_q[3], t_ff_23_q[4], t_ff_23_q[5]);
  Multiplexer #(.select(3), .width(32)) multiplexer_16 (
    .in0(register_44_q), .in1(register_45_q), .in2(register_46_q), .in3(register_47_q), .in4(register_48_q),
    .in5(register_49_q), .in6(register_50_q), .in7(register_51_q), .out(multiplexer_16_out), .sel(t_16a[2:0]));
  assign t_2a = out_12 & not_5_out;  // AND_Gate and_8, 6 bits wide
  assign t_7a = out_15 & not_6_out;  // AND_Gate and_9, 6 bits wide
  assign not_7_out = ~{6{subtractor_3_bout[5]}};  // NOT_Gate not_7, 6 bits wide
  assign not_8_out = ~{6{subtractor_4_bout[5]}};  // NOT_Gate not_8, 6 bits wide
  Multiplexer #(.select(3), .width(32)) multiplexer_17 (
    .in0(register_52_q), .in1(register_53_q), .in2(register_54_q), .in3(register_55_q), .in4(register_56_q),
    .in5(register_57_q), .in6(register_58_q), .in7(register_59_q), .out(out_29), .sel(multiplexer_23_out));
  Pull_Resistor pull_resistor_16 (.node(pull_resistor_16_node));
  buf buffer_5 (buffer_5_out, clock_3_out);
  Register #(.width(32)) register_60 (
    .D(out_23), .en(demultiplexer_4_out16[0]), .clk(buffer_4_out), .Q(register_60_q));  // open: clr
  Register #(.width(32)) register_61 (
    .D(out_23), .en(demultiplexer_4_out16[1]), .clk(buffer_4_out), .Q(register_61_q));  // open: clr
  Register #(.width(32)) register_62 (
    .D(out_23), .en(demultiplexer_4_out16[2]), .clk(buffer_4_out), .Q(register_62_q));  // open: clr
  Register #(.width(32)) register_63 (
    .D(out_23), .en(demultiplexer_4_out16[3]), .clk(buffer_4_out), .Q(register_63_q));  // open: clr
  Register #(.width(32)) register_64 (
    .D(out_23), .en(demultiplexer_4_out16[4]), .clk(buffer_4_out), .Q(register_64_q));  // open: clr
  Register #(.width(32)) register_65 (
    .D(out_23), .en(demultiplexer_4_out16[5]), .clk(buffer_4_out), .Q(register_65_q));  // open: clr
  Register #(.width(32)) register_66 (
    .D(out_23), .en(demultiplexer_4_out16[6]), .clk(buffer_4_out), .Q(register_66_q));  // open: clr
  Register #(.width(32)) register_67 (
    .D(out_23), .en(demultiplexer_4_out16[7]), .clk(buffer_4_out), .Q(register_67_q));  // open: clr
  assign t_15a = out_20 & not_7_out;  // AND_Gate and_10, 6 bits wide
  assign t_16a = out_25 & not_8_out;  // AND_Gate and_11, 6 bits wide
  Multiplexer #(.select(3), .width(32)) multiplexer_18 (
    .in0(register_52_q), .in1(register_53_q), .in2(register_54_q), .in3(register_55_q), .in4(register_56_q),
    .in5(register_57_q), .in6(register_58_q), .in7(register_59_q), .out(out_31), .sel(t_7a[2:0]));
  Demultiplexer #(.select(3)) demultiplexer_2 (
    .out0(demultiplexer_2_out0), .out1(demultiplexer_2_out1), .out2(demultiplexer_2_out2),
    .out3(demultiplexer_2_out3), .out4(demultiplexer_2_out4), .out5(demultiplexer_2_out5),
    .out6(demultiplexer_2_out6), .out7(demultiplexer_2_out7), .in(pull_resistor_16_node), .sel(t_ff_29_q));
  and and_12 (and_12_out, t_ff_29_q[0], t_ff_29_q[1], t_ff_29_q[2]);
  not not_9 (not_9_out, and_12_out);
  assign pull_resistor_16_node = not_9_out ? 1'b1 : 1'bz;  // Controlled_Buffer controlled_buffer_1
  Multiplexer #(.select(3), .width(32)) multiplexer_19 (
    .in0(register_52_q), .in1(register_53_q), .in2(register_54_q), .in3(register_55_q), .in4(register_56_q),
    .in5(register_57_q), .in6(register_58_q), .in7(register_59_q), .out(out_33), .sel(t_15a[2:0]));
  Multiplexer #(.select(3), .width(32)) multiplexer_20 (
    .in0(register_52_q), .in1(register_53_q), .in2(register_54_q), .in3(register_55_q), .in4(register_56_q),
    .in5(register_57_q), .in6(register_58_q), .in7(register_59_q), .out(out_36), .sel(t_16a[2:0]));
  assign bit_extender_11_out = {{5{1'b0}}, 1'b0};  // Bit_Extender bit_extender_11
  assign bit_extender_12_out = {{6{1'b0}}, 10'h42};  // Bit_Extender bit_extender_12
  Pull_Resistor pull_resistor_17 (.node(bit_extender_12_out));
  Register #(.width(32)) register_68 (
    .D(out_23), .en(demultiplexer_5_out24[0]), .clk(buffer_4_out), .Q(register_68_q));  // open: clr
  Register #(.width(32)) register_69 (
    .D(out_23), .en(demultiplexer_5_out24[1]), .clk(buffer_4_out), .Q(register_69_q));  // open: clr
  buf or_2 (or_2_out, demultiplexer_2_out0);  // OR_Gate
  buf or_3 (or_3_out, demultiplexer_2_out1);  // OR_Gate
  buf or_4 (or_4_out, demultiplexer_2_out2);  // OR_Gate
  buf or_5 (or_5_out, demultiplexer_2_out3);  // OR_Gate
  buf or_6 (or_6_out, demultiplexer_2_out4);  // OR_Gate
  buf or_7 (or_7_out, demultiplexer_2_out5);  // OR_Gate
  buf or_8 (or_8_out, demultiplexer_2_out6);  // OR_Gate
  buf or_9 (or_9_out, comparator_3_eq);  // OR_Gate
  Comparator #(.width(6)) comparator_4 (
    .a(t_ff_23_q), .b(bit_extender_11_out), .gt(comparator_4_gt), .lt(comparator_4_lt));  // open: eq
  Multiplexer #(.select(3), .width(32)) multiplexer_21 (
    .in0(register_60_q), .in1(register_61_q), .in2(register_62_q), .in3(register_63_q), .in4(register_64_q),
    .in5(register_65_q), .in6(register_66_q), .in7(register_67_q), .out(out_4), .sel(multiplexer_23_out));
  Comparator #(.width(16)) comparator_5 (
    .a(pc), .b(bit_extender_12_out), .gt(comparator_5_gt), .lt(comparator_5_lt));  // open: eq
  Register #(.width(32)) register_70 (
    .D(out_23), .en(demultiplexer_5_out24[2]), .clk(buffer_4_out), .Q(register_70_q));  // open: clr
  Register #(.width(32)) register_71 (
    .D(out_23), .en(demultiplexer_5_out24[3]), .clk(buffer_4_out), .Q(register_71_q));  // open: clr
  Register #(.width(32)) register_72 (
    .D(out_23), .en(demultiplexer_5_out24[4]), .clk(buffer_4_out), .Q(register_72_q));  // open: clr
  Register #(.width(32)) register_73 (
    .D(out_23), .en(demultiplexer_5_out24[5]), .clk(buffer_4_out), .Q(register_73_q));  // open: clr
  Register #(.width(32)) register_74 (
    .D(out_23), .en(demultiplexer_5_out24[6]), .clk(buffer_4_out), .Q(register_74_q));  // open: clr
  Register #(.width(32)) register_75 (
    .D(out_23), .en(comparator_6_eq), .clk(buffer_4_out), .Q(register_75_q));  // open: clr
  Register #(.width(32)) aaa (.D(h_values_data), .en(or_2_out), .clk(buffer_5_out), .Q(aaa_q));  // open: clr
  Register #(.width(32)) bbb (.D(h_values_data), .en(or_3_out), .clk(buffer_5_out), .Q(bbb_q));  // open: clr
  Register #(.width(32)) ccc (.D(h_values_data), .en(or_4_out), .clk(buffer_5_out), .Q(ccc_q));  // open: clr
  Register #(.width(32)) ddd (.D(h_values_data), .en(or_5_out), .clk(buffer_5_out));  // open: Q, clr
  Register #(.width(32)) eee (.D(h_values_data), .en(or_6_out), .clk(buffer_5_out));  // open: Q, clr
  Register #(.width(32)) fff (.D(h_values_data), .en(or_7_out), .clk(buffer_5_out));  // open: Q, clr
  Register #(.width(32)) ggg (.D(h_values_data), .en(or_8_out), .clk(buffer_5_out));  // open: Q, clr
  Register #(.width(32)) hhh (.D(h_values_data), .en(or_9_out), .clk(buffer_5_out));  // open: Q, clr
  Multiplexer #(.select(3), .width(32)) multiplexer_22 (
    .in0(register_60_q), .in1(register_61_q), .in2(register_62_q), .in3(register_63_q), .in4(register_64_q),
    .in5(register_65_q), .in6(register_66_q), .in7(register_67_q), .out(out_5), .sel(t_7a[2:0]));
  Multiplexer #(.width(6)) multiplexer_23 (
    .in0(t_2a), .in1(b_q), .out({multiplexer_23_out_2, multiplexer_23_out}), .sel(comparator_5_gt));
  or or_10 (or_10_out, comparator_4_gt, comparator_4_lt);
  Multiplexer #(.select(3), .width(32)) multiplexer_24 (
    .in0(register_60_q), .in1(register_61_q), .in2(register_62_q), .in3(register_63_q), .in4(register_64_q),
    .in5(register_65_q), .in6(register_66_q), .in7(register_67_q), .out(out_8), .sel(t_15a[2:0]));
  Multiplexer #(.select(3), .width(32)) multiplexer_25 (
    .in0(register_60_q), .in1(register_61_q), .in2(register_62_q), .in3(register_63_q), .in4(register_64_q),
    .in5(register_65_q), .in6(register_66_q), .in7(register_67_q), .out(out_10), .sel(t_16a[2:0]));
  Multiplexer #(.select(3), .width(32)) multiplexer_26 (
    .in0(register_68_q), .in1(register_69_q), .in2(register_70_q), .in3(register_71_q), .in4(register_72_q),
    .in5(register_73_q), .in6(register_74_q), .in7(register_75_q), .out(multiplexer_26_out),
    .sel(multiplexer_23_out));
  Register #(.width(32)) register_76 (
    .D(out_23), .en(demultiplexer_4_out24[0]), .clk(buffer_4_out), .Q(register_76_q));  // open: clr
  Register #(.width(32)) register_77 (
    .D(out_23), .en(demultiplexer_4_out24[1]), .clk(buffer_4_out), .Q(register_77_q));  // open: clr
  Register #(.width(32)) register_78 (
    .D(out_23), .en(demultiplexer_4_out24[2]), .clk(buffer_4_out), .Q(register_78_q));  // open: clr
  Register #(.width(32)) register_79 (
    .D(out_23), .en(demultiplexer_4_out24[3]), .clk(buffer_4_out), .Q(register_79_q));  // open: clr
  Register #(.width(32)) register_80 (
    .D(out_23), .en(demultiplexer_4_out24[4]), .clk(buffer_4_out), .Q(register_80_q));  // open: clr
  Register #(.width(32)) register_81 (
    .D(out_23), .en(demultiplexer_4_out24[5]), .clk(buffer_4_out), .Q(register_81_q));  // open: clr
  Multiplexer #(.select(3), .width(32)) multiplexer_27 (
    .in0(register_68_q), .in1(register_69_q), .in2(register_70_q), .in3(register_71_q), .in4(register_72_q),
    .in5(register_73_q), .in6(register_74_q), .in7(register_75_q), .out(multiplexer_27_out), .sel(t_7a[2:0]));
  Register #(.width(32)) register_82 (
    .D(out_23), .en(demultiplexer_4_out24[6]), .clk(buffer_4_out), .Q(register_82_q));  // open: clr
  Register #(.width(32)) register_83 (
    .D(out_23), .en(demultiplexer_4_out24[7]), .clk(buffer_4_out), .Q(register_83_q));  // open: clr
  Multiplexer #(.select(3), .width(32)) multiplexer_28 (
    .in0(register_68_q), .in1(register_69_q), .in2(register_70_q), .in3(register_71_q), .in4(register_72_q),
    .in5(register_73_q), .in6(register_74_q), .in7(register_75_q), .out(multiplexer_28_out), .sel(t_15a[2:0]));
  Multiplexer #(.select(3), .width(32)) multiplexer_29 (
    .in0(register_68_q), .in1(register_69_q), .in2(register_70_q), .in3(register_71_q), .in4(register_72_q),
    .in5(register_73_q), .in6(register_74_q), .in7(register_75_q), .out(multiplexer_29_out), .sel(t_16a[2:0]));
  Multiplexer #(.select(3), .width(32)) multiplexer_30 (
    .in0(register_76_q), .in1(register_77_q), .in2(register_78_q), .in3(register_79_q), .in4(register_80_q),
    .in5(register_81_q), .in6(register_82_q), .in7(register_83_q), .out(multiplexer_30_out),
    .sel(multiplexer_23_out));
  Multiplexer #(.select(3), .width(32)) multiplexer_31 (
    .in0(register_76_q), .in1(register_77_q), .in2(register_78_q), .in3(register_79_q), .in4(register_80_q),
    .in5(register_81_q), .in6(register_82_q), .in7(register_83_q), .out(multiplexer_31_out), .sel(t_7a[2:0]));
  Multiplexer #(.select(3), .width(32)) multiplexer_32 (
    .in0(register_76_q), .in1(register_77_q), .in2(register_78_q), .in3(register_79_q), .in4(register_80_q),
    .in5(register_81_q), .in6(register_82_q), .in7(register_83_q), .out(multiplexer_32_out), .sel(t_15a[2:0]));
  buf buffer_6 (buffer_6_out, buffer_7_out);
  buf buffer_7 (buffer_7_out, buffer_8_out);
  buf buffer_8 (buffer_8_out, buffer_9_out);
  buf buffer_9 (buffer_9_out, buffer_12_out);
  buf buffer_10 (buffer_10_out, buffer_14_out);
  Multiplexer #(.select(3), .width(32)) multiplexer_33 (
    .in0(register_76_q), .in1(register_77_q), .in2(register_78_q), .in3(register_79_q), .in4(register_80_q),
    .in5(register_81_q), .in6(register_82_q), .in7(register_83_q), .out(multiplexer_33_out), .sel(t_16a[2:0]));
  Multiplexer #(.select(3), .width(32)) multiplexer_34 (
    .in0(t_2), .in1(multiplexer_13_out), .in2(out_4), .in3(multiplexer_30_out), .in4(out_28),
    .in5(multiplexer_9_out), .in6(out_29), .in7(multiplexer_26_out),
    .out({multiplexer_34_out[14:0], multiplexer_34_out[31:15]}), .sel(multiplexer_23_out_2));
  Multiplexer #(.select(3), .width(32)) multiplexer_35 (
    .in0(t_7), .in1(multiplexer_14_out), .in2(out_5), .in3(multiplexer_31_out), .in4(out_30),
    .in5(multiplexer_10_out), .in6(out_31), .in7(multiplexer_27_out), .out(multiplexer_35_out),
    .sel(t_7a[5:3]));
  Multiplexer #(.select(3), .width(32)) multiplexer_36 (
    .in0(t_15), .in1(multiplexer_15_out), .in2(out_8), .in3(multiplexer_32_out), .in4(out_32),
    .in5(multiplexer_11_out), .in6(out_33), .in7(multiplexer_28_out), .out({right_3[28:0], rotate_7[27:25]}),
    .sel(t_15a[5:3]));
  Register #(.width(32)) aa (
    .D(adder_12_out), .en(buffer_11_out), .clk(buffer_5_out), .Q({aa_q[18:0], aa_q[31:19]}));  // open: clr
  buf buffer_11 (buffer_11_out, buffer_6_out);
  Register #(.width(32)) bb (
    .D({aa_q[18:0], aa_q[31:19]}), .en(buffer_6_out), .clk(buffer_5_out), .Q(bb_q));  // open: clr
  Register #(.width(32)) cc (.D(bb_q), .en(buffer_7_out), .clk(buffer_5_out), .Q(cc_q));  // open: clr
  Register #(.width(32)) dd (.D(cc_q), .en(buffer_8_out), .clk(buffer_5_out), .Q(dd_q));  // open: clr
  Register #(.width(32)) ee (
    .D(adder_5_out), .en(buffer_9_out), .clk(buffer_5_out),
    .Q({ee_q[0], ee_q[1], ee_q[2], ee_q[3], ee_q[4], ee_q[5], ee_q[31:6]}));  // open: clr
  Register #(.width(32)) ff (
    .D({ee_q[0], ee_q[1], ee_q[2], ee_q[3], ee_q[4], ee_q[5], ee_q[31:6]}), .en(buffer_12_out),
    .clk(buffer_5_out), .Q(ff_q));  // open: clr
  buf buffer_12 (buffer_12_out, buffer_10_out);
  Register #(.width(32)) gg (.D(ff_q), .en(buffer_10_out), .clk(buffer_5_out), .Q(gg_q));  // open: clr
  Register #(.width(32)) register_84 (
    .D(gg_q), .en(buffer_14_out), .clk(buffer_5_out), .Q(register_84_q));  // open: clr
  Multiplexer #(.select(3), .width(32)) multiplexer_37 (
    .in0(t_16), .in1(multiplexer_16_out), .in2(out_10), .in3(multiplexer_33_out), .in4(out_35),
    .in5(multiplexer_12_out), .in6(out_36), .in7(multiplexer_29_out), .out(multiplexer_37_out),
    .sel(t_16a[5:3]));
  T_Flip_Flop t_ff_34 (
    .T(not_1_out), .clk(clock_1_out), .Q(t_ff_34_q[0]), .Qn(t_ff_34_qn), .preset(and_16_out));  // open: reset
  T_Flip_Flop t_ff_35 (
    .T(not_1_out), .clk(t_ff_34_qn), .Q(t_ff_34_q[1]), .Qn(t_ff_35_qn), .preset(and_16_out));  // open: reset
  T_Flip_Flop t_ff_36 (
    .T(not_1_out), .clk(t_ff_35_qn), .Q(t_ff_34_q[2]), .Qn(t_ff_36_qn), .preset(and_16_out));  // open: reset
  T_Flip_Flop t_ff_37 (
    .T(not_1_out), .clk(t_ff_36_qn), .Q(t_ff_34_q[3]), .Qn(t_ff_37_qn), .preset(and_16_out));  // open: reset
  assign and_13_out = {aa_q[18:0], aa_q[31:19]} & bb_q;  // AND_Gate and_13, 32 bits wide
  assign and_14_out = {aa_q[18:0], aa_q[31:19]} & cc_q;  // AND_Gate and_14, 32 bits wide
  assign and_15_out = cc_q & bb_q;  // AND_Gate and_15, 32 bits wide
  Adder #(.width(32)) adder_5 (.a(dd_q), .b(t1_q), .out(adder_5_out));  // open: cin, cout
  T_Flip_Flop t_ff_38 (
    .T(not_1_out), .clk(t_ff_37_qn), .Q(t_ff_34_q[4]), .Qn(t_ff_38_qn), .preset(and_16_out));  // open: reset
  and and_16 (and_16_out, t_ff_34_q[0], t_ff_34_q[1], t_ff_34_q[3], t_ff_34_q[4], t_ff_34_q[2], t_ff_34_q[5]);
  T_Flip_Flop t_ff_39 (.T(not_1_out), .clk(t_ff_38_qn), .Q(t_ff_34_q[5]), .preset(and_16_out));  // open: Qn, reset
  assign bit_extender_13_out = {{5{1'b0}}, 1'b1};  // Bit_Extender bit_extender_13
  assign or_11_out = and_13_out | and_14_out | and_15_out;  // OR_Gate or_11, 32 bits wide
  Adder #(.width(6)) adder_6 (.a(t_ff_34_q), .b(bit_extender_13_out), .out(adder_6_out));  // open: cin, cout
  Adder #(.width(32)) adder_7 (.a(or_11_out), .b(sigma_0), .out(adder_7_out));  // open: cin, cout
  Adder #(.width(32)) adder_8 (
    .a({multiplexer_34_out[14:0], multiplexer_34_out[31:15]}), .b(k_values_data), .out(adder_8_out));  // open: cin, cout
  Adder #(.width(32)) adder_9 (.a(adder_8_out), .b(register_84_q), .out(adder_9_out));  // open: cin, cout
  Comparator #(.width(16)) comparator_6 (.a(pc), .b(16'h41), .eq(comparator_6_eq));  // open: gt, lt
  Adder #(.width(32)) adder_10 (.a(adder_9_out), .b(ch), .out(adder_10_out));  // open: cin, cout
  buf buffer_13 (buffer_13_out, or_10_out);
  buf buffer_14 (buffer_14_out, buffer_13_out);
  Adder #(.width(32)) adder_11 (.a(adder_10_out), .b(sigma_1), .out(adder_11_out));  // open: cin, cout
  Register #(.width(32)) t1 (.D(adder_11_out), .en(or_10_out), .clk(buffer_5_out), .Q(t1_q));  // open: clr
  Register #(.width(32)) t2 (.D(adder_7_out), .en(buffer_13_out), .clk(buffer_5_out), .Q(t2_q));  // open: clr
  Adder #(.width(32)) adder_12 (.a(t1_q), .b(t2_q), .out(adder_12_out));  // open: cin, cout
  Demultiplexer demultiplexer_3 (
    .out0(demultiplexer_3_out0), .out1(demultiplexer_3_out1), .in(1'b1), .sel(adder_6_out[5]));
  Demultiplexer #(.select(5)) demultiplexer_4 (
    .out16(demultiplexer_4_out16[0]), .out17(demultiplexer_4_out16[1]), .out18(demultiplexer_4_out16[2]),
    .out19(demultiplexer_4_out16[3]), .out20(demultiplexer_4_out16[4]), .out21(demultiplexer_4_out16[5]),
    .out22(demultiplexer_4_out16[6]), .out23(demultiplexer_4_out16[7]), .out24(demultiplexer_4_out24[0]),
    .out25(demultiplexer_4_out24[1]), .out26(demultiplexer_4_out24[2]), .out27(demultiplexer_4_out24[3]),
    .out28(demultiplexer_4_out24[4]), .out29(demultiplexer_4_out24[5]), .out30(demultiplexer_4_out24[6]),
    .out31(demultiplexer_4_out24[7]), .in(demultiplexer_3_out0), .sel(adder_6_out[4:0]));  // open: out0, out1, out2, out3, out4, out5, out6, out7, out8, out9, out10, out11, out12, out13, out14, out15
  Demultiplexer #(.select(5)) demultiplexer_5 (
    .out0(demultiplexer_5_out0[0]), .out1(demultiplexer_5_out0[1]), .out2(demultiplexer_5_out0[2]),
    .out3(demultiplexer_5_out0[3]), .out4(demultiplexer_5_out0[4]), .out5(demultiplexer_5_out0[5]),
    .out6(demultiplexer_5_out0[6]), .out7(demultiplexer_5_out0[7]), .out8(demultiplexer_5_out8[0]),
    .out9(demultiplexer_5_out8[1]), .out10(demultiplexer_5_out8[2]), .out11(demultiplexer_5_out8[3]),
    .out12(demultiplexer_5_out8[4]), .out13(demultiplexer_5_out8[5]), .out14(demultiplexer_5_out8[6]),
    .out15(demultiplexer_5_out8[7]), .out16(demultiplexer_5_out16[0]), .out17(demultiplexer_5_out16[1]),
    .out18(demultiplexer_5_out16[2]), .out19(demultiplexer_5_out16[3]), .out20(demultiplexer_5_out16[4]),
    .out21(demultiplexer_5_out16[5]), .out22(demultiplexer_5_out16[6]), .out23(demultiplexer_5_out16[7]),
    .out24(demultiplexer_5_out24[0]), .out25(demultiplexer_5_out24[1]), .out26(demultiplexer_5_out24[2]),
    .out27(demultiplexer_5_out24[3]), .out28(demultiplexer_5_out24[4]), .out29(demultiplexer_5_out24[5]),
    .out30(demultiplexer_5_out24[6]), .out31(demultiplexer_5_out24[7]), .in(demultiplexer_3_out1),
    .sel(adder_6_out[4:0]));

  assign right_3[31:29] = 3'b000;
  assign {rotate_7[31:28], rotate_7[24:0]} = {right_3[3:0], right_3[28:4]};
  assign rotate_18 = {right_3[14:0], rotate_7[27:25], right_3[28:15]};

  // Notes on the sheet:
  //   contents of k_values (hex, n*v repeats v):
  //   428a2f98 71374491 b5c0fbcf e9b5dba5 3956c25b 59f111f1 923f82a4 ab1c5ed5 d807aa98 12835b01 234185be
  //   550c7dc3 72be5d74 80deb1fe 9dbc06a7 c19bf174 e49b69c1 efbe4786 fc19dc6 240ca1cc 2de92c6f 4a7484aa
  //   5cb0a9dc 74f988da 983e5152 a831c66d b00327c8 bf597fc7 c6e00bf3 d5a79147 6ca6351 14292967 27b70a85
  //   2e1b2138 4d2c6dfc 53380d13 650a7354 766a0abb 81c2c92e 92722c85 a2bfe8a1 a81a664b c24b8b70 c76c51a3
  //   d192e819 d6990624 f40e3585 106aa070 19a4c116 1e376c08 2748774c 34b0bcb5 391c0cb3 4ed8aa4a 5b9cca4f
  //   682e6ff3 748f82ee 78a5636f 84c87814 8cc70208 90befffa a4506ceb bef9a3f7 c67178f2
  //   contents of rom_1 (hex, n*v repeats v):
  //   428a2f98 71374491 b5c0fbcf e9b5dba5 3956c25b 59f111f1 923f82a4 ab1c5ed5 d807aa98 12835b01 234185be
  //   550c7dc3 72be5d74 80deb1fe 9dbc06a7 c19bf174 e49b69c1 efbe4786 fc19dc6 240ca1cc 2de92c6f 4a7484aa
  //   5cb0a9dc 74f988da 983e5152 a831c66d b00327c8 bf597fc7 c6e00bf3 d5a79147 6ca6351 14292967 27b70a85
  //   2e1b2138 4d2c6dfc 53380d13 650a7354 766a0abb 81c2c92e 92722c85 a2bfe8a1 a81a664b c24b8b70 c76c51a3
  //   d192e819 d6990624 f40e3585 106aa070 19a4c116 1e376c08 2748774c 34b0bcb5 391c0cb3 4ed8aa4a 5b9cca4f
  //   682e6ff3 748f82ee 78a5636f 84c87814 8cc70208 90befffa a4506ceb bef9a3f7 c67178f2
  //   contents of h_values (hex, n*v repeats v):
  //   6a09e667 bb67ae85 3c6ef372 a54ff53a 510e527f 9b05688c 1f83d9ab 5be0cd19
  //   contents of rom_2 (hex, n*v repeats v):
  //   6a09e667 bb67ae85 3c6ef372 a54ff53a 510e527f 9b05688c 1f83d9ab 5be0cd19
endmodule

module test (
  input  [31:0] in_1,
  input  in_2,
  input  in_3,
  output [31:0] out_4
);

  Register #(.width(32)) register_1 (.D(in_1), .en(in_2), .clk(in_3), .Q(out_4));  // open: clr
endmodule
