// Logisim project flappy_bird.circ as structural Verilog: 3 circuits, main circuit main
module main (
  input  in_1,
  input  in_2,
  output [3:0] out_3
);

  wire a, and_1_out, and_2_out, and_3_out, and_4_out, and_5_out, and_6_out, and_7_out, and_8_out, and_9_out,
       and_10_out, and_11_out, and_12_out, and_13_out, and_14_out, and_15_out, and_16_out, and_17_out,
       and_18_out, and_19_out, and_20_out, and_21_out, and_22_out, and_23_out, and_24_out, and_25_out,
       and_26_out, and_27_out, and_28_out, and_29_out, and_30_out, and_31_out, and_32_out, and_33_out,
       and_34_out, and_35_out, and_36_out, and_37_out, and_38_out, and_39_out, and_40_out, and_41_out,
       and_42_out, and_43_out, and_44_out, and_45_out, and_46_out, and_47_out, and_48_out, and_49_out,
       and_50_out, and_51_out, and_52_out, and_53_out, and_54_out, and_55_out, and_56_out, and_57_out,
       and_58_out, and_59_out, and_60_out, and_61_out, and_62_out, and_63_out, and_64_out, and_65_out,
       and_66_out, and_67_out, and_68_out, and_69_out, and_70_out, and_71_out, and_72_out, and_73_out,
       and_74_out, and_75_out, and_76_out, and_77_out, and_78_out, and_79_out, and_80_out, and_81_out,
       and_82_out, and_83_out, and_84_out, and_85_out, and_86_out, and_87_out, and_88_out, and_89_out,
       and_90_out, and_91_out, and_92_out, and_93_out, and_94_out, and_95_out, and_96_out, and_97_out,
       and_98_out, and_99_out, and_100_out, and_101_out, and_102_out, and_103_out, and_104_out, and_105_out,
       and_106_out, and_107_out, and_108_out, and_109_out, and_110_out, and_111_out, and_112_out,
       and_113_out, and_114_out, and_115_out, and_116_out, and_117_out, and_118_out, and_119_out,
       and_120_out, and_121_out, and_122_out, and_123_out, and_124_out, and_125_out, and_126_out,
       and_127_out, and_128_out, and_129_out, and_130_out, and_131_out, and_132_out, and_133_out,
       and_134_out, and_135_out, and_136_out, and_137_out, and_138_out, b, c, clock_1_out, comparator_1_eq,
       d, d_ff_1_q, d_ff_1_qn, decoder_1_out4, decoder_1_out5, decoder_1_out6, decoder_1_out7,
       decoder_2_out0, decoder_2_out1, decoder_2_out2, decoder_2_out3, decoder_2_out4, decoder_2_out5,
       decoder_2_out6, decoder_2_out7, decoder_2_out8, decoder_2_out9, decoder_2_out10, decoder_2_out11,
       decoder_2_out12, decoder_2_out13, decoder_2_out14, decoder_2_out15, not_1_out, not_2_out, not_3_out,
       not_4_out, or_1_out, or_2_out, or_3_out, or_4_out, or_5_out, or_6_out, or_7_out, or_8_out, or_9_out,
       subtractor_1_bout, t_ff_4_q, t_ff_6_q, t_ff_7_q, t_ff_8_q, t_ff_9_qn, t_ff_10_qn, t_ff_11_qn;
  wire [2:0] counter_1_q;
  wire [3:0] binary_to_bcd_converter_1_p3, binary_to_bcd_converter_1_p4, subtractor_1_out, t_ff_1_q, t_ff_9_q;

  Counter #(.max('h7), .width(3)) counter_1 (
    .up(not_4_out), .count(not_3_out), .clk(clock_1_out), .Q(counter_1_q));  // open: clr, load, D, carry
  Clock clock_1 (.out(clock_1_out));
  D_Flip_Flop d_ff_1 (.D(d_ff_1_qn), .clk(and_1_out), .Q(d_ff_1_q), .Qn(d_ff_1_qn));  // open: preset, reset
  and and_1 (and_1_out, in_1, clock_1_out);
  T_Flip_Flop t_ff_1 (.T(1'b1), .clk(d_ff_1_q), .Q(t_ff_1_q[0]));  // open: Qn, reset, preset
  Decoder #(.select(3)) decoder_1 (
    .out0(d), .out1(c), .out2(b), .out3(a), .out4(decoder_1_out4), .out5(decoder_1_out5),
    .out6(decoder_1_out6), .out7(decoder_1_out7), .sel(counter_1_q));  // open: en
  T_Flip_Flop t_ff_2 (.T(1'b1), .clk(t_ff_1_q[0]), .Q(t_ff_1_q[1]));  // open: Qn, reset, preset
  T_Flip_Flop t_ff_3 (.T(1'b1), .clk(t_ff_1_q[1]), .Q(t_ff_1_q[2]));  // open: Qn, reset, preset
  not not_1 (not_1_out, t_ff_7_q);
  T_Flip_Flop t_ff_4 (.T(not_1_out), .clk(decoder_2_out10), .Q(t_ff_4_q));  // open: Qn, reset, preset
  T_Flip_Flop t_ff_5 (.T(1'b1), .clk(t_ff_1_q[2]), .Q(t_ff_1_q[3]));  // open: Qn, reset, preset
  T_Flip_Flop t_ff_6 (.T(t_ff_4_q), .clk(decoder_2_out10), .Q(t_ff_6_q));  // open: Qn, reset, preset
  or or_1 (or_1_out, and_2_out, d);
  or or_2 (or_2_out, and_3_out, c);
  or or_3 (or_3_out, b, and_4_out);
  or or_4 (or_4_out, and_5_out, a);
  or or_5 (or_5_out, and_6_out, decoder_1_out4);
  or or_6 (or_6_out, and_7_out, decoder_1_out5);
  not not_2 (not_2_out, t_ff_6_q);
  T_Flip_Flop t_ff_7 (.T(not_2_out), .clk(decoder_2_out10), .Q(t_ff_7_q));  // open: Qn, reset, preset
  _7_Segment_Display u_7_segment_display_1 (.f(d), .a(d), .b(or_1_out), .e(d), .d(d), .c(or_1_out));  // open: g, dp
  and and_2 (and_2_out, 1'b1, decoder_2_out0);
  _7_Segment_Display u_7_segment_display_2 (.f(c), .a(c), .b(or_2_out), .e(c), .d(c), .c(or_2_out));  // open: g, dp
  and and_3 (and_3_out, 1'b1, decoder_2_out0);
  _7_Segment_Display u_7_segment_display_3 (.f(b), .a(b), .b(or_3_out), .e(b), .d(b), .c(or_3_out));  // open: g, dp
  and and_4 (and_4_out, t_ff_4_q, decoder_2_out0);
  _7_Segment_Display u_7_segment_display_4 (.f(a), .a(a), .b(or_4_out), .e(a), .d(a), .c(or_4_out));  // open: g, dp
  and and_5 (and_5_out, t_ff_6_q, decoder_2_out0);
  _7_Segment_Display u_7_segment_display_5 (
    .f(decoder_1_out4), .a(decoder_1_out4), .b(or_5_out), .e(decoder_1_out4), .d(decoder_1_out4), .c(or_5_out));  // open: g, dp
  and and_6 (and_6_out, t_ff_7_q, decoder_2_out0);
  _7_Segment_Display u_7_segment_display_6 (
    .f(decoder_1_out5), .a(decoder_1_out5), .b(or_6_out), .e(decoder_1_out5), .d(decoder_1_out5), .c(or_6_out));  // open: g, dp
  and and_7 (and_7_out, t_ff_8_q, decoder_2_out0);
  or or_7 (or_7_out, decoder_1_out6, and_8_out);
  _7_Segment_Display u_7_segment_display_7 (
    .f(decoder_1_out6), .a(decoder_1_out6), .b(or_7_out), .e(decoder_1_out6), .d(decoder_1_out6), .c(or_7_out));  // open: g, dp
  and and_8 (and_8_out, 1'b1, decoder_2_out0);
  or or_8 (or_8_out, and_9_out, decoder_1_out7);
  _7_Segment_Display u_7_segment_display_8 (
    .f(decoder_1_out7), .a(decoder_1_out7), .b(or_8_out), .e(decoder_1_out7), .d(decoder_1_out7), .c(or_8_out));  // open: g, dp
  and and_9 (and_9_out, 1'b1, decoder_2_out0);
  _7_Segment_Display u_7_segment_display_9 (.b(and_10_out), .c(and_10_out));  // open: g, f, a, e, d, dp
  _7_Segment_Display u_7_segment_display_10 (.b(and_27_out), .c(and_27_out));  // open: g, f, a, e, d, dp
  and and_10 (and_10_out, 1'b1, decoder_2_out1);
  _7_Segment_Display u_7_segment_display_11 (.b(and_11_out), .c(and_11_out));  // open: g, f, a, e, d, dp
  _7_Segment_Display u_7_segment_display_12 (.b(and_29_out), .c(and_29_out));  // open: g, f, a, e, d, dp
  and and_11 (and_11_out, 1'b1, decoder_2_out1);
  _7_Segment_Display u_7_segment_display_13 (.b(and_12_out), .c(and_12_out));  // open: g, f, a, e, d, dp
  _7_Segment_Display u_7_segment_display_14 (.b(and_31_out), .c(and_31_out));  // open: g, f, a, e, d, dp
  and and_12 (and_12_out, t_ff_4_q, decoder_2_out1);
  _7_Segment_Display u_7_segment_display_15 (.b(and_13_out), .c(and_13_out));  // open: g, f, a, e, d, dp
  _7_Segment_Display u_7_segment_display_16 (.b(and_33_out), .c(and_33_out));  // open: g, f, a, e, d, dp
  and and_13 (and_13_out, t_ff_6_q, decoder_2_out1);
  _7_Segment_Display u_7_segment_display_17 (.b(and_14_out), .c(and_14_out));  // open: g, f, a, e, d, dp
  _7_Segment_Display u_7_segment_display_18 (.b(and_35_out), .c(and_35_out));  // open: g, f, a, e, d, dp
  and and_14 (and_14_out, t_ff_7_q, decoder_2_out1);
  _7_Segment_Display u_7_segment_display_19 (.b(and_15_out), .c(and_15_out));  // open: g, f, a, e, d, dp
  _7_Segment_Display u_7_segment_display_20 (.b(and_37_out), .c(and_37_out));  // open: g, f, a, e, d, dp
  and and_15 (and_15_out, t_ff_8_q, decoder_2_out1);
  _7_Segment_Display u_7_segment_display_21 (.b(and_16_out), .c(and_16_out));  // open: g, f, a, e, d, dp
  _7_Segment_Display u_7_segment_display_22 (.b(and_39_out), .c(and_39_out));  // open: g, f, a, e, d, dp
  and and_16 (and_16_out, 1'b1, decoder_2_out1);
  _7_Segment_Display u_7_segment_display_23 (.b(and_17_out), .c(and_17_out));  // open: g, f, a, e, d, dp
  _7_Segment_Display u_7_segment_display_24 (.b(and_41_out), .c(and_41_out));  // open: g, f, a, e, d, dp
  and and_17 (and_17_out, 1'b1, decoder_2_out1);
  T_Flip_Flop t_ff_8 (.T(not_1_out), .clk(decoder_2_out10), .Q(t_ff_8_q));  // open: Qn, reset, preset
  and and_18 (and_18_out, decoder_1_out7, and_9_out);
  and and_19 (and_19_out, and_8_out, decoder_1_out6);
  and and_20 (and_20_out, decoder_1_out5, and_7_out);
  and and_21 (and_21_out, and_6_out, decoder_1_out4);
  and and_22 (and_22_out, and_5_out, a);
  and and_23 (and_23_out, b, and_4_out);
  and and_24 (and_24_out, and_3_out, c);
  and and_25 (and_25_out, d, and_2_out);
  _7_Segment_Display u_7_segment_display_25 (.b(and_42_out), .c(and_42_out));  // open: g, f, a, e, d, dp
  _7_Segment_Display u_7_segment_display_26 (.b(and_26_out), .c(and_26_out));  // open: g, f, a, e, d, dp
  and and_26 (and_26_out, 1'b1, decoder_2_out3);
  and and_27 (and_27_out, 1'b1, decoder_2_out2);
  _7_Segment_Display u_7_segment_display_27 (.b(and_44_out), .c(and_44_out));  // open: g, f, a, e, d, dp
  _7_Segment_Display u_7_segment_display_28 (.b(and_28_out), .c(and_28_out));  // open: g, f, a, e, d, dp
  and and_28 (and_28_out, 1'b1, decoder_2_out3);
  and and_29 (and_29_out, 1'b1, decoder_2_out2);
  _7_Segment_Display u_7_segment_display_29 (.b(and_46_out), .c(and_46_out));  // open: g, f, a, e, d, dp
  _7_Segment_Display u_7_segment_display_30 (.b(and_30_out), .c(and_30_out));  // open: g, f, a, e, d, dp
  and and_30 (and_30_out, t_ff_4_q, decoder_2_out3);
  and and_31 (and_31_out, t_ff_4_q, decoder_2_out2);
  _7_Segment_Display u_7_segment_display_31 (.b(and_48_out), .c(and_48_out));  // open: g, f, a, e, d, dp
  _7_Segment_Display u_7_segment_display_32 (.b(and_32_out), .c(and_32_out));  // open: g, f, a, e, d, dp
  and and_32 (and_32_out, t_ff_6_q, decoder_2_out3);
  and and_33 (and_33_out, t_ff_6_q, decoder_2_out2);
  _7_Segment_Display u_7_segment_display_33 (.b(and_50_out), .c(and_50_out));  // open: g, f, a, e, d, dp
  _7_Segment_Display u_7_segment_display_34 (.b(and_34_out), .c(and_34_out));  // open: g, f, a, e, d, dp
  and and_34 (and_34_out, t_ff_7_q, decoder_2_out3);
  and and_35 (and_35_out, t_ff_7_q, decoder_2_out2);
  _7_Segment_Display u_7_segment_display_35 (.b(and_52_out), .c(and_52_out));  // open: g, f, a, e, d, dp
  _7_Segment_Display u_7_segment_display_36 (.b(and_36_out), .c(and_36_out));  // open: g, f, a, e, d, dp
  and and_36 (and_36_out, t_ff_8_q, decoder_2_out3);
  and and_37 (and_37_out, t_ff_8_q, decoder_2_out2);
  _7_Segment_Display u_7_segment_display_37 (.b(and_54_out), .c(and_54_out));  // open: g, f, a, e, d, dp
  _7_Segment_Display u_7_segment_display_38 (.b(and_38_out), .c(and_38_out));  // open: g, f, a, e, d, dp
  and and_38 (and_38_out, 1'b1, decoder_2_out3);
  and and_39 (and_39_out, 1'b1, decoder_2_out2);
  _7_Segment_Display u_7_segment_display_39 (.b(and_56_out), .c(and_56_out));  // open: g, f, a, e, d, dp
  _7_Segment_Display u_7_segment_display_40 (.b(and_40_out), .c(and_40_out));  // open: g, f, a, e, d, dp
  and and_40 (and_40_out, 1'b1, decoder_2_out3);
  and and_41 (and_41_out, 1'b1, decoder_2_out2);
  _7_Segment_Display u_7_segment_display_41 (
    .b(and_43_out), .c(and_43_out), .dp(decoder_2_out6));  // open: g, f, a, e, d
  and and_42 (and_42_out, 1'b1, decoder_2_out4);
  and and_43 (and_43_out, 1'b1, decoder_2_out5);
  _7_Segment_Display u_7_segment_display_42 (.b(and_45_out), .c(and_45_out));  // open: g, f, a, e, d, dp
  and and_44 (and_44_out, 1'b1, decoder_2_out4);
  and and_45 (and_45_out, 1'b1, decoder_2_out5);
  _7_Segment_Display u_7_segment_display_43 (
    .b(and_47_out), .c(and_47_out), .dp(decoder_2_out6));  // open: g, f, a, e, d
  and and_46 (and_46_out, t_ff_4_q, decoder_2_out4);
  and and_47 (and_47_out, t_ff_4_q, decoder_2_out5);
  _7_Segment_Display u_7_segment_display_44 (.b(and_49_out), .c(and_49_out));  // open: g, f, a, e, d, dp
  and and_48 (and_48_out, t_ff_6_q, decoder_2_out4);
  and and_49 (and_49_out, t_ff_6_q, decoder_2_out5);
  _7_Segment_Display u_7_segment_display_45 (
    .b(and_51_out), .c(and_51_out), .dp(decoder_2_out6));  // open: g, f, a, e, d
  and and_50 (and_50_out, t_ff_7_q, decoder_2_out4);
  and and_51 (and_51_out, t_ff_7_q, decoder_2_out5);
  _7_Segment_Display u_7_segment_display_46 (.b(and_53_out), .c(and_53_out));  // open: g, f, a, e, d, dp
  and and_52 (and_52_out, t_ff_8_q, decoder_2_out4);
  and and_53 (and_53_out, t_ff_8_q, decoder_2_out5);
  _7_Segment_Display u_7_segment_display_47 (
    .b(and_55_out), .c(and_55_out), .dp(decoder_2_out6));  // open: g, f, a, e, d
  and and_54 (and_54_out, 1'b1, decoder_2_out4);
  and and_55 (and_55_out, 1'b1, decoder_2_out5);
  _7_Segment_Display u_7_segment_display_48 (.b(and_57_out), .c(and_57_out));  // open: g, f, a, e, d, dp
  and and_56 (and_56_out, 1'b1, decoder_2_out4);
  and and_57 (and_57_out, 1'b1, decoder_2_out5);
  or or_9 (or_9_out, and_18_out, and_19_out, and_20_out, and_21_out, and_22_out, and_23_out, and_24_out, and_25_out);
  _7_Segment_Display u_7_segment_display_49 (.b(and_58_out), .c(and_58_out));  // open: g, f, a, e, d, dp
  _7_Segment_Display u_7_segment_display_50 (.b(and_66_out), .c(and_66_out));  // open: g, f, a, e, d, dp
  and and_58 (and_58_out, 1'b1, decoder_2_out6);
  _7_Segment_Display u_7_segment_display_51 (.b(and_59_out), .c(and_59_out));  // open: g, f, a, e, d, dp
  _7_Segment_Display u_7_segment_display_52 (.b(and_68_out), .c(and_68_out));  // open: g, f, a, e, d, dp
  and and_59 (and_59_out, 1'b1, decoder_2_out6);
  _7_Segment_Display u_7_segment_display_53 (.b(and_60_out), .c(and_60_out));  // open: g, f, a, e, d, dp
  _7_Segment_Display u_7_segment_display_54 (.b(and_70_out), .c(and_70_out));  // open: g, f, a, e, d, dp
  and and_60 (and_60_out, t_ff_4_q, decoder_2_out6);
  _7_Segment_Display u_7_segment_display_55 (.b(and_61_out), .c(and_61_out));  // open: g, f, a, e, d, dp
  _7_Segment_Display u_7_segment_display_56 (.b(and_72_out), .c(and_72_out));  // open: g, f, a, e, d, dp
  and and_61 (and_61_out, t_ff_6_q, decoder_2_out6);
  _7_Segment_Display u_7_segment_display_57 (.b(and_62_out), .c(and_62_out));  // open: g, f, a, e, d, dp
  _7_Segment_Display u_7_segment_display_58 (.b(and_74_out), .c(and_74_out));  // open: g, f, a, e, d, dp
  and and_62 (and_62_out, t_ff_7_q, decoder_2_out6);
  _7_Segment_Display u_7_segment_display_59 (.b(and_63_out), .c(and_63_out));  // open: g, f, a, e, d, dp
  _7_Segment_Display u_7_segment_display_60 (.b(and_76_out), .c(and_76_out));  // open: g, f, a, e, d, dp
  and and_63 (and_63_out, t_ff_8_q, decoder_2_out6);
  _7_Segment_Display u_7_segment_display_61 (.b(and_64_out), .c(and_64_out));  // open: g, f, a, e, d, dp
  _7_Segment_Display u_7_segment_display_62 (.b(and_78_out), .c(and_78_out));  // open: g, f, a, e, d, dp
  and and_64 (and_64_out, 1'b1, decoder_2_out6);
  _7_Segment_Display u_7_segment_display_63 (.b(and_65_out), .c(and_65_out));  // open: g, f, a, e, d, dp
  _7_Segment_Display u_7_segment_display_64 (.b(and_80_out), .c(and_80_out));  // open: g, f, a, e, d, dp
  and and_65 (and_65_out, 1'b1, decoder_2_out6);
  T_Flip_Flop t_ff_9 (.T(1'b1), .clk(decoder_2_out0), .Q(t_ff_9_q[0]), .Qn(t_ff_9_qn), .reset(or_9_out), .preset(in_2));
  Decoder #(.select(4)) decoder_2 (
    .out0(decoder_2_out0), .out1(decoder_2_out1), .out2(decoder_2_out2), .out3(decoder_2_out3),
    .out4(decoder_2_out4), .out5(decoder_2_out5), .out6(decoder_2_out6), .out7(decoder_2_out7),
    .out8(decoder_2_out8), .out9(decoder_2_out9), .out10(decoder_2_out10), .out11(decoder_2_out11),
    .out12(decoder_2_out12), .out13(decoder_2_out13), .out14(decoder_2_out14), .out15(decoder_2_out15),
    .sel(t_ff_1_q), .en(1'b1));
  _7_Segment_Display u_7_segment_display_65 (.b(and_67_out), .c(and_67_out));  // open: g, f, a, e, d, dp
  and and_66 (and_66_out, 1'b1, decoder_2_out7);
  and and_67 (and_67_out, 1'b1, decoder_2_out8);
  _7_Segment_Display u_7_segment_display_66 (.b(and_69_out), .c(and_69_out));  // open: g, f, a, e, d, dp
  and and_68 (and_68_out, 1'b1, decoder_2_out7);
  and and_69 (and_69_out, 1'b1, decoder_2_out8);
  _7_Segment_Display u_7_segment_display_67 (.b(and_71_out), .c(and_71_out));  // open: g, f, a, e, d, dp
  and and_70 (and_70_out, t_ff_4_q, decoder_2_out7);
  and and_71 (and_71_out, t_ff_4_q, decoder_2_out8);
  _7_Segment_Display u_7_segment_display_68 (.b(and_73_out), .c(and_73_out));  // open: g, f, a, e, d, dp
  and and_72 (and_72_out, t_ff_6_q, decoder_2_out7);
  and and_73 (and_73_out, t_ff_6_q, decoder_2_out8);
  _7_Segment_Display u_7_segment_display_69 (.b(and_75_out), .c(and_75_out));  // open: g, f, a, e, d, dp
  and and_74 (and_74_out, t_ff_7_q, decoder_2_out7);
  and and_75 (and_75_out, t_ff_7_q, decoder_2_out8);
  _7_Segment_Display u_7_segment_display_70 (.b(and_77_out), .c(and_77_out));  // open: g, f, a, e, d, dp
  and and_76 (and_76_out, t_ff_8_q, decoder_2_out7);
  and and_77 (and_77_out, t_ff_8_q, decoder_2_out8);
  _7_Segment_Display u_7_segment_display_71 (.b(and_79_out), .c(and_79_out));  // open: g, f, a, e, d, dp
  and and_78 (and_78_out, 1'b1, decoder_2_out7);
  and and_79 (and_79_out, 1'b1, decoder_2_out8);
  _7_Segment_Display u_7_segment_display_72 (.b(and_81_out), .c(and_81_out));  // open: g, f, a, e, d, dp
  and and_80 (and_80_out, 1'b1, decoder_2_out7);
  and and_81 (and_81_out, 1'b1, decoder_2_out8);
  T_Flip_Flop t_ff_10 (.T(1'b1), .clk(t_ff_9_qn), .Q(t_ff_9_q[1]), .Qn(t_ff_10_qn), .reset(or_9_out), .preset(in_2));
  _7_Segment_Display u_7_segment_display_73 (.b(and_82_out), .c(and_82_out));  // open: g, f, a, e, d, dp
  _7_Segment_Display u_7_segment_display_74 (.b(and_90_out), .c(and_90_out));  // open: g, f, a, e, d, dp
  and and_82 (and_82_out, 1'b1, decoder_2_out9);
  _7_Segment_Display u_7_segment_display_75 (.b(and_83_out), .c(and_83_out));  // open: g, f, a, e, d, dp
  _7_Segment_Display u_7_segment_display_76 (.b(and_92_out), .c(and_92_out));  // open: g, f, a, e, d, dp
  and and_83 (and_83_out, 1'b1, decoder_2_out9);
  _7_Segment_Display u_7_segment_display_77 (.b(and_84_out), .c(and_84_out));  // open: g, f, a, e, d, dp
  _7_Segment_Display u_7_segment_display_78 (.b(and_94_out), .c(and_94_out));  // open: g, f, a, e, d, dp
  and and_84 (and_84_out, t_ff_4_q, decoder_2_out9);
  _7_Segment_Display u_7_segment_display_79 (.b(and_85_out), .c(and_85_out));  // open: g, f, a, e, d, dp
  _7_Segment_Display u_7_segment_display_80 (.b(and_96_out), .c(and_96_out));  // open: g, f, a, e, d, dp
  and and_85 (and_85_out, t_ff_6_q, decoder_2_out9);
  _7_Segment_Display u_7_segment_display_81 (.b(and_86_out), .c(and_86_out));  // open: g, f, a, e, d, dp
  _7_Segment_Display u_7_segment_display_82 (.b(and_98_out), .c(and_98_out));  // open: g, f, a, e, d, dp
  and and_86 (and_86_out, t_ff_7_q, decoder_2_out9);
  _7_Segment_Display u_7_segment_display_83 (.b(and_87_out), .c(and_87_out));  // open: g, f, a, e, d, dp
  _7_Segment_Display u_7_segment_display_84 (.b(and_100_out), .c(and_100_out));  // open: g, f, a, e, d, dp
  and and_87 (and_87_out, t_ff_8_q, decoder_2_out9);
  _7_Segment_Display u_7_segment_display_85 (.b(and_88_out), .c(and_88_out));  // open: g, f, a, e, d, dp
  _7_Segment_Display u_7_segment_display_86 (.b(and_102_out), .c(and_102_out));  // open: g, f, a, e, d, dp
  and and_88 (and_88_out, 1'b1, decoder_2_out9);
  _7_Segment_Display u_7_segment_display_87 (.b(and_89_out), .c(and_89_out));  // open: g, f, a, e, d, dp
  _7_Segment_Display u_7_segment_display_88 (.b(and_104_out), .c(and_104_out));  // open: g, f, a, e, d, dp
  and and_89 (and_89_out, 1'b1, decoder_2_out9);
  _7_Segment_Display u_7_segment_display_89 (.b(and_91_out), .c(and_91_out));  // open: g, f, a, e, d, dp
  _7_Segment_Display u_7_segment_display_90 (.b(and_106_out), .c(and_106_out));  // open: g, f, a, e, d, dp
  and and_90 (and_90_out, 1'b1, decoder_2_out10);
  and and_91 (and_91_out, 1'b1, decoder_2_out11);
  _7_Segment_Display u_7_segment_display_91 (.b(and_93_out), .c(and_93_out));  // open: g, f, a, e, d, dp
  _7_Segment_Display u_7_segment_display_92 (.b(and_108_out), .c(and_108_out));  // open: g, f, a, e, d, dp
  and and_92 (and_92_out, 1'b1, decoder_2_out10);
  and and_93 (and_93_out, 1'b1, decoder_2_out11);
  _7_Segment_Display u_7_segment_display_93 (.b(and_95_out), .c(and_95_out));  // open: g, f, a, e, d, dp
  _7_Segment_Display u_7_segment_display_94 (.b(and_110_out), .c(and_110_out));  // open: g, f, a, e, d, dp
  and and_94 (and_94_out, t_ff_4_q, decoder_2_out10);
  and and_95 (and_95_out, t_ff_4_q, decoder_2_out11);
  _7_Segment_Display u_7_segment_display_95 (.b(and_97_out), .c(and_97_out));  // open: g, f, a, e, d, dp
  _7_Segment_Display u_7_segment_display_96 (.b(and_112_out), .c(and_112_out));  // open: g, f, a, e, d, dp
  and and_96 (and_96_out, t_ff_6_q, decoder_2_out10);
  and and_97 (and_97_out, t_ff_6_q, decoder_2_out11);
  _7_Segment_Display u_7_segment_display_97 (.b(and_99_out), .c(and_99_out));  // open: g, f, a, e, d, dp
  _7_Segment_Display u_7_segment_display_98 (.b(and_114_out), .c(and_114_out));  // open: g, f, a, e, d, dp
  and and_98 (and_98_out, t_ff_7_q, decoder_2_out10);
  and and_99 (and_99_out, t_ff_7_q, decoder_2_out11);
  _7_Segment_Display u_7_segment_display_99 (.b(and_101_out), .c(and_101_out));  // open: g, f, a, e, d, dp
  _7_Segment_Display u_7_segment_display_100 (.b(and_116_out), .c(and_116_out));  // open: g, f, a, e, d, dp
  and and_100 (and_100_out, t_ff_8_q, decoder_2_out10);
  and and_101 (and_101_out, t_ff_8_q, decoder_2_out11);
  _7_Segment_Display u_7_segment_display_101 (.b(and_103_out), .c(and_103_out));  // open: g, f, a, e, d, dp
  _7_Segment_Display u_7_segment_display_102 (.b(and_118_out), .c(and_118_out));  // open: g, f, a, e, d, dp
  and and_102 (and_102_out, 1'b1, decoder_2_out10);
  and and_103 (and_103_out, 1'b1, decoder_2_out11);
  _7_Segment_Display u_7_segment_display_103 (.b(and_105_out), .c(and_105_out));  // open: g, f, a, e, d, dp
  _7_Segment_Display u_7_segment_display_104 (.b(and_120_out), .c(and_120_out));  // open: g, f, a, e, d, dp
  and and_104 (and_104_out, 1'b1, decoder_2_out10);
  and and_105 (and_105_out, 1'b1, decoder_2_out11);
  T_Flip_Flop t_ff_11 (.T(1'b1), .clk(t_ff_10_qn), .Q(t_ff_9_q[2]), .Qn(t_ff_11_qn), .reset(or_9_out), .preset(in_2));
  _7_Segment_Display u_7_segment_display_105 (.b(and_107_out), .c(and_107_out));  // open: g, f, a, e, d, dp
  and and_106 (and_106_out, 1'b1, decoder_2_out12);
  and and_107 (and_107_out, 1'b1, decoder_2_out13);
  _7_Segment_Display u_7_segment_display_106 (.b(and_109_out), .c(and_109_out));  // open: g, f, a, e, d, dp
  and and_108 (and_108_out, 1'b1, decoder_2_out12);
  and and_109 (and_109_out, 1'b1, decoder_2_out13);
  _7_Segment_Display u_7_segment_display_107 (.b(and_111_out), .c(and_111_out));  // open: g, f, a, e, d, dp
  and and_110 (and_110_out, t_ff_4_q, decoder_2_out12);
  and and_111 (and_111_out, t_ff_4_q, decoder_2_out13);
  _7_Segment_Display u_7_segment_display_108 (.b(and_113_out), .c(and_113_out));  // open: g, f, a, e, d, dp
  and and_112 (and_112_out, t_ff_6_q, decoder_2_out12);
  and and_113 (and_113_out, t_ff_6_q, decoder_2_out13);
  _7_Segment_Display u_7_segment_display_109 (.b(and_115_out), .c(and_115_out));  // open: g, f, a, e, d, dp
  and and_114 (and_114_out, t_ff_7_q, decoder_2_out12);
  and and_115 (and_115_out, t_ff_7_q, decoder_2_out13);
  _7_Segment_Display u_7_segment_display_110 (.b(and_117_out), .c(and_117_out));  // open: g, f, a, e, d, dp
  and and_116 (and_116_out, t_ff_8_q, decoder_2_out12);
  and and_117 (and_117_out, t_ff_8_q, decoder_2_out13);
  _7_Segment_Display u_7_segment_display_111 (.b(and_119_out), .c(and_119_out));  // open: g, f, a, e, d, dp
  and and_118 (and_118_out, 1'b1, decoder_2_out12);
  and and_119 (and_119_out, 1'b1, decoder_2_out13);
  _7_Segment_Display u_7_segment_display_112 (.b(and_121_out), .c(and_121_out));  // open: g, f, a, e, d, dp
  and and_120 (and_120_out, 1'b1, decoder_2_out12);
  and and_121 (and_121_out, 1'b1, decoder_2_out13);
  T_Flip_Flop t_ff_12 (.T(1'b1), .clk(t_ff_11_qn), .Q(t_ff_9_q[3]), .reset(or_9_out), .preset(in_2));  // open: Qn
  _7_Segment_Display u_7_segment_display_113 (.b(and_122_out), .c(and_122_out));  // open: g, f, a, e, d, dp
  _7_Segment_Display u_7_segment_display_114 (.b(and_130_out), .c(and_130_out));  // open: g, f, a, e, d, dp
  and and_122 (and_122_out, 1'b1, decoder_2_out14);
  _7_Segment_Display u_7_segment_display_115 (.b(and_123_out), .c(and_123_out));  // open: g, f, a, e, d, dp
  _7_Segment_Display u_7_segment_display_116 (.b(and_131_out), .c(and_131_out));  // open: g, f, a, e, d, dp
  and and_123 (and_123_out, 1'b1, decoder_2_out14);
  _7_Segment_Display u_7_segment_display_117 (.b(and_124_out), .c(and_124_out));  // open: g, f, a, e, d, dp
  _7_Segment_Display u_7_segment_display_118 (.b(and_132_out), .c(and_132_out));  // open: g, f, a, e, d, dp
  and and_124 (and_124_out, t_ff_4_q, decoder_2_out14);
  _7_Segment_Display u_7_segment_display_119 (.b(and_125_out), .c(and_125_out));  // open: g, f, a, e, d, dp
  _7_Segment_Display u_7_segment_display_120 (.b(and_133_out), .c(and_133_out));  // open: g, f, a, e, d, dp
  and and_125 (and_125_out, t_ff_6_q, decoder_2_out14);
  _7_Segment_Display u_7_segment_display_121 (.b(and_126_out), .c(and_126_out));  // open: g, f, a, e, d, dp
  _7_Segment_Display u_7_segment_display_122 (.b(and_134_out), .c(and_134_out));  // open: g, f, a, e, d, dp
  and and_126 (and_126_out, t_ff_7_q, decoder_2_out14);
  _7_Segment_Display u_7_segment_display_123 (.b(and_127_out), .c(and_127_out));  // open: g, f, a, e, d, dp
  _7_Segment_Display u_7_segment_display_124 (.b(and_135_out), .c(and_135_out));  // open: g, f, a, e, d, dp
  and and_127 (and_127_out, t_ff_8_q, decoder_2_out14);
  _7_Segment_Display u_7_segment_display_125 (.b(and_128_out), .c(and_128_out));  // open: g, f, a, e, d, dp
  _7_Segment_Display u_7_segment_display_126 (.b(and_136_out), .c(and_136_out));  // open: g, f, a, e, d, dp
  and and_128 (and_128_out, 1'b1, decoder_2_out14);
  _7_Segment_Display u_7_segment_display_127 (.b(and_129_out), .c(and_129_out));  // open: g, f, a, e, d, dp
  _7_Segment_Display u_7_segment_display_128 (.b(and_137_out), .c(and_137_out));  // open: g, f, a, e, d, dp
  and and_129 (and_129_out, 1'b1, decoder_2_out14);
  and and_130 (and_130_out, 1'b1, decoder_2_out15);
  and and_131 (and_131_out, 1'b1, decoder_2_out15);
  and and_132 (and_132_out, t_ff_4_q, decoder_2_out15);
  and and_133 (and_133_out, t_ff_6_q, decoder_2_out15);
  and and_134 (and_134_out, t_ff_7_q, decoder_2_out15);
  and and_135 (and_135_out, t_ff_8_q, decoder_2_out15);
  and and_136 (and_136_out, 1'b1, decoder_2_out15);
  and and_137 (and_137_out, 1'b1, decoder_2_out15);
  Hex_Digit_Display hex_digit_display_1 (.value(binary_to_bcd_converter_1_p3));  // open: dp
  // Binary_to_BCD_converter #(.binvalue(4)) binary_to_bcd_converter_1: pin names not known; wires that end beside it: and_137_out, t_ff_9_q, binary_to_bcd_converter_1_p3, binary_to_bcd_converter_1_p4
  Hex_Digit_Display hex_digit_display_2 (.value(binary_to_bcd_converter_1_p4));  // open: dp
  Joystick joystick_1 (.y(out_3));  // open: x
  Subtractor #(.width(4)) subtractor_1 (
    .a(out_3), .b(4'b1000), .out(subtractor_1_out), .bout(subtractor_1_bout));  // open: bin
  Comparator #(.width(4)) comparator_1 (.a(subtractor_1_out), .b(4'b0000), .eq(comparator_1_eq));  // open: gt, lt
  not not_3 (not_3_out, comparator_1_eq);
  and and_138 (and_138_out, not_3_out, subtractor_1_bout);
  not not_4 (not_4_out, and_138_out);
endmodule

module counter1 (
  input  in_1
);

  wire not_1_out, not_2_out, t_ff_1_q, t_ff_2_q, t_ff_3_q;

  not not_1 (not_1_out, t_ff_3_q);
  T_Flip_Flop t_ff_1 (.T(not_1_out), .clk(in_1), .Q(t_ff_1_q));  // open: Qn, reset, preset
  T_Flip_Flop t_ff_2 (.T(t_ff_1_q), .clk(in_1), .Q(t_ff_2_q));  // open: Qn, reset, preset
  not not_2 (not_2_out, t_ff_2_q);
  T_Flip_Flop t_ff_3 (.T(not_2_out), .clk(in_1), .Q(t_ff_3_q));  // open: Qn, reset, preset
  T_Flip_Flop t_ff_4 (.T(not_1_out), .clk(in_1));  // open: Q, Qn, reset, preset
endmodule

module counter2 (
  input  in_1,
  output out_2
);

  wire t_ff_1_q, t_ff_2_q, undriven;

  T_Flip_Flop t_ff_1 (.T(1'b1), .clk(in_1), .Q(t_ff_1_q), .preset(undriven));  // open: Qn, reset
  T_Flip_Flop t_ff_2 (.T(1'b1), .clk(t_ff_1_q), .Q(t_ff_2_q), .preset(undriven));  // open: Qn, reset
  T_Flip_Flop t_ff_3 (.T(1'b1), .clk(t_ff_2_q), .Qn(out_2), .preset(undriven));  // open: Q, reset
endmodule
