// Logisim project stcok_predictor.circ as structural Verilog: 2 circuits, main circuit main
module test (
  input  [15:0] in_1
);

  wire buffer_1_out, clock_1_out;
  wire [15:0] adder_1_out, register_1_q, register_2_q;

  Register #(.width(16)) register_1 (.D(register_2_q), .clk(clock_1_out), .Q(register_1_q));  // open: en, clr
  Clock clock_1 (.out(clock_1_out));
  Adder #(.width(16)) adder_1 (.a(in_1), .b(register_1_q), .out(adder_1_out));  // open: cin, cout
  buf buffer_1 (buffer_1_out, clock_1_out);
  Register #(.width(16)) register_2 (.D(adder_1_out), .clk(buffer_1_out), .Q(register_2_q));  // open: en, clr
endmodule

module main (
  output [15:0] t100,
  output [9:0] t_100,
  output q,
  output d,
  output [9:0] t_200,
  output t_128,
  output [8:0] out_7,
  output out_8,
  output out_9,
  output [15:0] t200,
  output [7:0] out_11
);

  wire and_1_out, and_3_out, and_4_out, and_6_out, and_8_out, and_10_out, and_11_out, and_12_out, and_13_out,
       clock_1_out, clock_2_out, clock_3_out, clock_4_out, clock_5_out, comparator_1_eq, comparator_2_gt,
       comparator_3_gt, comparator_4_gt, comparator_4_lt, decoder_1_out0, not_1_out, not_2_out, not_3_out,
       not_4_out, not_5_out, not_6_out, t_ff_1_qn, undriven;
  wire [1:0] t_ff_1_q;
  wire [7:0] and_2_out, and_5_out, and_7_out, and_9_out, pull_resistor_6_node, ram_1_dout;
  wire [7:7] decoder_1_out1, decoder_1_out2;
  wire [8:0] bit_extender_5_out;
  wire [9:0] counter_1_q, multiplexer_1_out, multiplexer_2_out, multiplexer_3_out, pull_resistor_1_node,
       pull_resistor_2_node, pull_resistor_3_node, subtractor_1_out, subtractor_2_out;
  wire [15:0] adder_1_out, adder_2_out, bit_extender_1_out, bit_extender_2_out, bit_extender_3_out,
       bit_extender_4_out, subtractor_3_out, subtractor_4_out;

  Comparator #(.width(10)) comparator_1 (.a(counter_1_q), .b({10{1'b1}}), .eq(comparator_1_eq));  // open: gt, lt
  not not_1 (not_1_out, comparator_2_gt);
  Comparator #(.width(10)) comparator_2 (.a(counter_1_q), .b(10'h7f), .gt(comparator_2_gt));  // open: eq, lt
  not not_2 (not_2_out, comparator_3_gt);
  Comparator #(.width(10)) comparator_3 (.a(counter_1_q), .b(10'hff), .gt(comparator_3_gt));  // open: eq, lt
  Clock clock_1 (.out(clock_1_out));
  Pull_Resistor pull_resistor_1 (.node(pull_resistor_1_node));
  Pull_Resistor pull_resistor_2 (.node(pull_resistor_2_node));
  T_Flip_Flop t_ff_1 (.T(1'b1), .clk(clock_1_out), .Q(t_ff_1_q[0]), .Qn(t_ff_1_qn));  // open: reset, preset
  not not_3 (not_3_out, comparator_1_eq);
  and and_1 (and_1_out, not_3_out, t_128);
  T_Flip_Flop t_ff_2 (.T(1'b1), .clk(t_ff_1_qn), .Q(t_ff_1_q[1]));  // open: Qn, reset, preset
  Counter #(.max('h3ff), .width(10)) counter_1 (
    .clr(undriven), .clk(and_1_out), .Q(counter_1_q));  // open: load, up, count, D, carry
  Multiplexer #(.width(10)) multiplexer_1 (
    .in0(subtractor_2_out), .in1(pull_resistor_2_node), .out(multiplexer_1_out), .sel(not_1_out));
  Multiplexer #(.width(10)) multiplexer_2 (
    .in0(subtractor_1_out), .in1(pull_resistor_1_node), .out(multiplexer_2_out), .sel(not_2_out));
  Decoder #(.select(2)) decoder_1 (
    .out0(decoder_1_out0), .out1(decoder_1_out1[7]), .out2(decoder_1_out2[7]), .out3(t_128), .sel(t_ff_1_q));  // open: en
  Subtractor #(.width(10)) subtractor_1 (.a(counter_1_q), .b(10'hff), .out(subtractor_1_out));  // open: bin, bout
  Subtractor #(.width(10)) subtractor_2 (.a(counter_1_q), .b(10'h7f), .out(subtractor_2_out));  // open: bin, bout
  Pull_Resistor pull_resistor_3 (.node(pull_resistor_3_node));
  Multiplexer #(.select(2), .width(10)) multiplexer_3 (
    .in0(counter_1_q), .in1(multiplexer_2_out), .in2(multiplexer_1_out), .in3(pull_resistor_3_node),
    .out(multiplexer_3_out), .sel(t_ff_1_q));
  RAM #(.addrWidth(10)) ram_1 (.addr(multiplexer_3_out), .clk(clock_2_out), .dout(ram_1_dout));  // open: we, oe, din
  Clock clock_2 (.out(clock_2_out));
  assign and_2_out = ram_1_dout & {8{t_128}};  // AND_Gate and_2, 8 bits wide
  assign bit_extender_1_out = {{8{1'b0}}, and_2_out};  // Bit_Extender bit_extender_1
  not not_4 (not_4_out, not_1_out);
  not not_5 (not_5_out, not_2_out);
  and and_3 (and_3_out, not_4_out, t_128);
  and and_4 (and_4_out, not_5_out, decoder_1_out2[7]);
  assign and_5_out = ram_1_dout & {8{decoder_1_out2[7]}};  // AND_Gate and_5, 8 bits wide
  Clock clock_3 (.out(clock_3_out));
  and and_6 (and_6_out, and_4_out, clock_4_out);
  Clock clock_4 (.out(clock_4_out));
  assign bit_extender_2_out = {{8{1'b0}}, and_5_out};  // Bit_Extender bit_extender_2
  assign and_7_out = ram_1_dout & {8{decoder_1_out1[7]}};  // AND_Gate and_7, 8 bits wide
  and and_8 (and_8_out, and_3_out, clock_3_out);
  assign and_9_out = ram_1_dout & {8{decoder_1_out1[7]}};  // AND_Gate and_9, 8 bits wide
  Pull_Resistor pull_resistor_4 (.node({out_7, t100[6:0]}));
  assign bit_extender_3_out = {{8{1'b0}}, and_7_out};  // Bit_Extender bit_extender_3
  Adder #(.width(16)) adder_1 (.a(bit_extender_3_out), .b({out_7, t100[6:0]}), .out(adder_1_out));  // open: cin, cout
  Pull_Resistor pull_resistor_5 (.node(bit_extender_1_out));
  assign bit_extender_4_out = {{8{1'b0}}, and_9_out};  // Bit_Extender bit_extender_4
  Subtractor #(.width(16)) subtractor_3 (
    .a(adder_1_out), .b(bit_extender_1_out), .out(subtractor_3_out));  // open: bin, bout
  and and_10 (and_10_out, 1'b1, decoder_1_out1[7]);
  Clock clock_5 (.out(clock_5_out));
  Pull_Resistor pull_resistor_6 (.node({out_11, pull_resistor_6_node}));
  Register #(.width(16)) register_1 (.D(subtractor_3_out), .clk(d), .Q({out_7, t100[6:0]}));  // open: en, clr
  or or_1 (d, and_11_out, and_8_out);
  and and_11 (and_11_out, and_10_out, clock_5_out);
  Adder #(.width(16)) adder_2 (
    .a(bit_extender_4_out), .b({out_11, pull_resistor_6_node}), .out(adder_2_out));  // open: cin, cout
  Pull_Resistor pull_resistor_7 (.node(bit_extender_2_out));
  Register #(.width(16)) register_2 (
    .D(subtractor_4_out), .clk(out_8), .Q({out_11, pull_resistor_6_node}));  // open: en, clr
  Subtractor #(.width(16)) subtractor_4 (
    .a(adder_2_out), .b(bit_extender_2_out), .out(subtractor_4_out));  // open: bin, bout
  or or_2 (out_8, and_6_out, and_11_out);
  Clock clock_6 (.out(out_9));
  assign bit_extender_5_out = {{1{1'b0}}, out_11};  // Bit_Extender bit_extender_5
  Comparator #(.width(9)) comparator_4 (
    .a(out_7), .b(bit_extender_5_out), .gt(comparator_4_gt), .lt(comparator_4_lt));  // open: eq
  not not_6 (not_6_out, not_2_out);
  and and_12 (and_12_out, comparator_4_gt, not_6_out);
  and and_13 (and_13_out, not_6_out, comparator_4_lt);
  LED led_1 (.in(and_12_out));
  LED led_2 (.in(and_13_out));

  assign q = d;
  assign t100[15:7] = out_7;
  assign t_100 = 10'h7f;
  assign t_200 = 10'hff;
endmodule
