// Logisim project table tennis.circ as structural Verilog: 1 circuit, main circuit main
module main (
  input  in_1,
  output [1:0] out_2,
  output [1:0] out_3
);

  wire and_1_out, and_2_out, and_3_out, and_4_out, and_5_out, and_6_out, and_7_out, and_8_out, and_9_out,
       and_10_out, and_11_out, and_12_out, and_13_out, and_14_out, and_15_out, and_16_out, and_17_out,
       and_18_out, and_19_out, and_20_out, and_21_out, and_22_out, and_23_out, and_24_out, and_25_out,
       and_26_out, and_27_out, and_28_out, and_29_out, and_30_out, and_31_out, and_32_out, and_33_out,
       and_34_out, and_35_out, and_36_out, and_37_out, and_38_out, and_39_out, and_40_out, and_41_out,
       and_42_out, and_43_out, and_44_out, and_45_out, and_46_out, and_47_out, and_48_out, and_49_out,
       and_50_out, and_51_out, and_52_out, and_53_out, and_54_out, and_55_out, and_56_out, and_57_out,
       and_58_out, and_59_out, and_60_out, and_61_out, and_62_out, and_63_out, and_64_out, and_65_out,
       and_66_out, and_67_out, and_68_out, and_69_out, and_70_out, and_71_out, and_72_out, and_73_out,
       and_74_out, and_75_out, and_76_out, and_77_out, and_78_out, and_79_out, and_80_out, and_81_out,
       and_82_out, and_83_out, and_84_out, and_85_out, and_86_out, and_87_out, and_88_out, and_89_out,
       and_90_out, and_91_out, and_92_out, and_93_out, and_94_out, and_95_out, and_96_out, and_97_out,
       and_98_out, and_99_out, and_100_out, and_101_out, and_102_out, and_103_out, and_104_out, and_105_out,
       and_106_out, and_107_out, and_108_out, and_109_out, and_110_out, and_111_out, and_112_out,
       and_113_out, and_114_out, and_115_out, and_116_out, and_117_out, and_118_out, and_119_out,
       and_120_out, and_121_out, and_122_out, and_123_out, and_124_out, and_125_out, and_126_out,
       and_127_out, and_128_out, and_129_out, and_130_out, and_131_out, and_132_out, and_133_out,
       and_134_out, and_135_out, and_136_out, and_137_out, and_138_out, and_139_out, and_140_out,
       and_141_out, and_142_out, and_143_out, and_144_out, and_145_out, and_146_out, buffer_1_out,
       buffer_2_out, clock_1_out, comparator_1_eq, comparator_2_eq, d_ff_1_q, d_ff_2_q, decoder_1_out0,
       decoder_1_out1, decoder_1_out2, decoder_1_out3, decoder_1_out4, decoder_1_out5, decoder_1_out6,
       decoder_1_out7, decoder_2_out0, decoder_2_out1, decoder_2_out2, decoder_2_out3, decoder_2_out4,
       decoder_2_out5, decoder_2_out6, decoder_2_out7, decoder_3_out0, decoder_3_out1, decoder_3_out2,
       decoder_3_out3, decoder_3_out4, decoder_3_out5, decoder_3_out6, decoder_3_out7, decoder_3_out8,
       decoder_3_out9, decoder_3_out10, decoder_3_out11, decoder_3_out12, decoder_3_out13, decoder_3_out14,
       decoder_3_out15, decoder_4_out0, decoder_4_out1, decoder_4_out2, decoder_4_out3, decoder_4_out4,
       decoder_4_out5, decoder_4_out6, decoder_4_out7, not_1_out, not_2_out, not_3_out, not_4_out, or_1_out,
       or_2_out, or_3_out, or_4_out, or_5_out, or_6_out, or_7_out, or_8_out, or_9_out, or_10_out, or_11_out,
       or_12_out, or_13_out, or_14_out, or_15_out, or_16_out, or_17_out, or_18_out, or_19_out, or_20_out,
       t_ff_1_q, t_ff_2_q, t_ff_3_qn, t_ff_4_qn, t_ff_5_qn, t_ff_7_qn, t_ff_8_qn, t_ff_9_qn;
  wire [2:0] counter_1_q, counter_3_q, counter_4_q;
  wire [3:0] counter_2_q, t_ff_3_q, t_ff_7_q;

  T_Flip_Flop t_ff_1 (.T(1'b1), .clk(or_1_out), .Q(t_ff_1_q));  // open: Qn, reset, preset
  or or_1 (or_1_out, decoder_1_out0, decoder_1_out7);
  Clock clock_1 (.out(clock_1_out));
  Counter #(.max('h7), .width(3)) counter_1 (
    .load(in_1), .up(out_3[1]), .count(not_1_out), .clk(clock_1_out), .D(3'b100), .Q(counter_1_q));  // open: clr, carry
  not not_1 (not_1_out, comparator_1_eq);
  Comparator #(.width(2)) comparator_1 (.a(out_3), .b(2'b10), .eq(comparator_1_eq));  // open: gt, lt
  Counter #(.max('hf), .width(4)) counter_2 (
    .clr(1'b0), .load(in_1), .up(t_ff_2_q), .count(1'b1), .clk(clock_1_out), .D(4'b1000), .Q(counter_2_q));  // open: carry
  Counter #(.max('h7), .width(3)) counter_3 (
    .load(in_1), .up(t_ff_1_q), .count(1'b1), .clk(clock_1_out), .D(3'b100), .Q(counter_3_q));  // open: clr, carry
  or or_2 (or_2_out, decoder_3_out15, decoder_3_out0);
  T_Flip_Flop t_ff_2 (.T(1'b1), .clk(or_2_out), .Q(t_ff_2_q));  // open: Qn, reset, preset
  Decoder #(.select(3)) decoder_1 (
    .out0(decoder_1_out0), .out1(decoder_1_out1), .out2(decoder_1_out2), .out3(decoder_1_out3),
    .out4(decoder_1_out4), .out5(decoder_1_out5), .out6(decoder_1_out6), .out7(decoder_1_out7),
    .sel(counter_3_q));  // open: en
  Decoder #(.select(3)) decoder_2 (
    .out0(decoder_2_out0), .out1(decoder_2_out1), .out2(decoder_2_out2), .out3(decoder_2_out3),
    .out4(decoder_2_out4), .out5(decoder_2_out5), .out6(decoder_2_out6), .out7(decoder_2_out7),
    .sel(counter_1_q));  // open: en
  or or_3 (or_3_out, decoder_2_out0, and_1_out);
  _7_Segment_Display u_7_segment_display_1 (
    .f(and_1_out), .a(and_1_out), .b(or_3_out), .d(and_1_out), .c(or_3_out));  // open: g, e, dp
  _7_Segment_Display u_7_segment_display_2 (
    .f(and_3_out), .a(and_3_out), .b(or_4_out), .e(and_3_out), .d(and_3_out), .c(or_4_out));  // open: g, dp
  or or_4 (or_4_out, decoder_2_out1, and_3_out);
  _7_Segment_Display u_7_segment_display_3 (
    .f(and_5_out), .a(and_5_out), .b(or_5_out), .e(and_5_out), .d(and_5_out), .c(or_5_out));  // open: g, dp
  or or_5 (or_5_out, decoder_2_out2, and_5_out);
  or or_6 (or_6_out, decoder_2_out3, and_7_out);
  _7_Segment_Display u_7_segment_display_4 (
    .f(and_7_out), .a(and_7_out), .b(or_6_out), .e(and_7_out), .d(and_7_out), .c(or_6_out));  // open: g, dp
  or or_7 (or_7_out, decoder_2_out4, and_9_out);
  _7_Segment_Display u_7_segment_display_5 (
    .f(and_9_out), .a(and_9_out), .b(or_7_out), .e(and_9_out), .d(and_9_out), .c(or_7_out));  // open: g, dp
  or or_8 (or_8_out, decoder_2_out5, and_11_out);
  _7_Segment_Display u_7_segment_display_6 (
    .f(and_11_out), .a(and_11_out), .b(or_8_out), .e(and_11_out), .d(and_11_out), .c(or_8_out));  // open: g, dp
  or or_9 (or_9_out, decoder_2_out6, and_13_out);
  _7_Segment_Display u_7_segment_display_7 (
    .f(and_13_out), .a(and_13_out), .b(or_9_out), .e(and_13_out), .d(and_13_out), .c(or_9_out));  // open: g, dp
  or or_10 (or_10_out, decoder_2_out7, and_15_out);
  _7_Segment_Display u_7_segment_display_8 (
    .f(and_15_out), .a(and_15_out), .b(or_10_out), .e(and_15_out), .d(and_15_out), .c(or_10_out));  // open: g, dp
  Decoder #(.select(4)) decoder_3 (
    .out0(decoder_3_out0), .out1(decoder_3_out1), .out2(decoder_3_out2), .out3(decoder_3_out3),
    .out4(decoder_3_out4), .out5(decoder_3_out5), .out6(decoder_3_out6), .out7(decoder_3_out7),
    .out8(decoder_3_out8), .out9(decoder_3_out9), .out10(decoder_3_out10), .out11(decoder_3_out11),
    .out12(decoder_3_out12), .out13(decoder_3_out13), .out14(decoder_3_out14), .out15(decoder_3_out15),
    .sel(counter_2_q));  // open: en
  _7_Segment_Display u_7_segment_display_9 (
    .f(and_2_out), .a(and_2_out), .b(and_2_out), .e(and_2_out), .d(and_2_out), .c(and_2_out));  // open: g, dp
  _7_Segment_Display u_7_segment_display_10 (
    .f(and_25_out), .a(and_25_out), .b(and_25_out), .e(and_25_out), .d(and_25_out), .c(and_25_out));  // open: g, dp
  and and_1 (and_1_out, decoder_3_out0, decoder_1_out0);
  and and_2 (and_2_out, decoder_3_out1, decoder_1_out0);
  _7_Segment_Display u_7_segment_display_11 (
    .f(and_4_out), .a(and_4_out), .b(and_4_out), .e(and_4_out), .d(and_4_out), .c(and_4_out));  // open: g, dp
  _7_Segment_Display u_7_segment_display_12 (
    .f(and_27_out), .a(and_27_out), .b(and_27_out), .e(and_27_out), .d(and_27_out), .c(and_27_out));  // open: g, dp
  and and_3 (and_3_out, decoder_3_out0, decoder_1_out1);
  and and_4 (and_4_out, decoder_3_out1, decoder_1_out1);
  _7_Segment_Display u_7_segment_display_13 (
    .f(and_6_out), .a(and_6_out), .b(and_6_out), .e(and_6_out), .d(and_6_out), .c(and_6_out));  // open: g, dp
  _7_Segment_Display u_7_segment_display_14 (
    .f(and_29_out), .a(and_29_out), .b(and_29_out), .e(and_29_out), .d(and_29_out), .c(and_29_out));  // open: g, dp
  and and_5 (and_5_out, decoder_3_out0, decoder_1_out2);
  and and_6 (and_6_out, decoder_3_out1, decoder_1_out2);
  _7_Segment_Display u_7_segment_display_15 (
    .f(and_8_out), .a(and_8_out), .b(and_8_out), .e(and_8_out), .d(and_8_out), .c(and_8_out));  // open: g, dp
  _7_Segment_Display u_7_segment_display_16 (
    .f(and_31_out), .a(and_31_out), .b(and_31_out), .e(and_31_out), .d(and_31_out), .c(and_31_out));  // open: g, dp
  and and_7 (and_7_out, decoder_3_out0, decoder_1_out3);
  and and_8 (and_8_out, decoder_3_out1, decoder_1_out3);
  _7_Segment_Display u_7_segment_display_17 (
    .f(and_10_out), .a(and_10_out), .b(and_10_out), .e(and_10_out), .d(and_10_out), .c(and_10_out));  // open: g, dp
  _7_Segment_Display u_7_segment_display_18 (
    .f(and_33_out), .a(and_33_out), .b(and_33_out), .e(and_33_out), .d(and_33_out), .c(and_33_out));  // open: g, dp
  and and_9 (and_9_out, decoder_3_out0, decoder_1_out4);
  and and_10 (and_10_out, decoder_3_out1, decoder_1_out4);
  _7_Segment_Display u_7_segment_display_19 (
    .f(and_12_out), .a(and_12_out), .b(and_12_out), .e(and_12_out), .d(and_12_out), .c(and_12_out));  // open: g, dp
  _7_Segment_Display u_7_segment_display_20 (
    .f(and_35_out), .a(and_35_out), .b(and_35_out), .e(and_35_out), .d(and_35_out), .c(and_35_out));  // open: g, dp
  and and_11 (and_11_out, decoder_3_out0, decoder_1_out5);
  and and_12 (and_12_out, decoder_3_out1, decoder_1_out5);
  _7_Segment_Display u_7_segment_display_21 (
    .f(and_14_out), .a(and_14_out), .b(and_14_out), .e(and_14_out), .d(and_14_out), .c(and_14_out));  // open: g, dp
  _7_Segment_Display u_7_segment_display_22 (
    .f(and_37_out), .a(and_37_out), .b(and_37_out), .e(and_37_out), .d(and_37_out), .c(and_37_out));  // open: g, dp
  and and_13 (and_13_out, decoder_3_out0, decoder_1_out6);
  and and_14 (and_14_out, decoder_3_out1, decoder_1_out6);
  _7_Segment_Display u_7_segment_display_23 (
    .f(and_16_out), .a(and_16_out), .b(and_16_out), .e(and_16_out), .d(and_16_out), .c(and_16_out));  // open: g, dp
  _7_Segment_Display u_7_segment_display_24 (
    .f(and_39_out), .a(and_39_out), .b(and_39_out), .e(and_39_out), .d(and_39_out), .c(and_39_out));  // open: g, dp
  and and_15 (and_15_out, decoder_3_out0, decoder_1_out7);
  and and_16 (and_16_out, decoder_3_out1, decoder_1_out7);
  and and_17 (and_17_out, and_1_out, decoder_2_out0);
  and and_18 (and_18_out, decoder_2_out1, and_3_out);
  and and_19 (and_19_out, and_11_out, decoder_2_out5);
  and and_20 (and_20_out, and_5_out, decoder_2_out2);
  and and_21 (and_21_out, and_7_out, decoder_2_out3);
  and and_22 (and_22_out, and_9_out, decoder_2_out4);
  and and_23 (and_23_out, decoder_2_out6, and_13_out);
  and and_24 (and_24_out, and_15_out, decoder_2_out7);
  _7_Segment_Display u_7_segment_display_25 (
    .f(and_26_out), .a(and_26_out), .b(and_26_out), .e(and_26_out), .d(and_26_out), .c(and_26_out));  // open: g, dp
  and and_25 (and_25_out, decoder_3_out2, decoder_1_out0);
  and and_26 (and_26_out, decoder_3_out3, decoder_1_out0);
  _7_Segment_Display u_7_segment_display_26 (
    .f(and_28_out), .a(and_28_out), .b(and_28_out), .e(and_28_out), .d(and_28_out), .c(and_28_out));  // open: g, dp
  and and_27 (and_27_out, decoder_3_out2, decoder_1_out1);
  and and_28 (and_28_out, decoder_3_out3, decoder_1_out1);
  _7_Segment_Display u_7_segment_display_27 (
    .f(and_30_out), .a(and_30_out), .b(and_30_out), .e(and_30_out), .d(and_30_out), .c(and_30_out));  // open: g, dp
  and and_29 (and_29_out, decoder_3_out2, decoder_1_out2);
  and and_30 (and_30_out, decoder_3_out3, decoder_1_out2);
  _7_Segment_Display u_7_segment_display_28 (
    .f(and_32_out), .a(and_32_out), .b(and_32_out), .e(and_32_out), .d(and_32_out), .c(and_32_out));  // open: g, dp
  and and_31 (and_31_out, decoder_3_out2, decoder_1_out3);
  and and_32 (and_32_out, decoder_3_out3, decoder_1_out3);
  _7_Segment_Display u_7_segment_display_29 (
    .f(and_34_out), .a(and_34_out), .b(and_34_out), .e(and_34_out), .d(and_34_out), .c(and_34_out));  // open: g, dp
  and and_33 (and_33_out, decoder_3_out2, decoder_1_out4);
  and and_34 (and_34_out, decoder_3_out3, decoder_1_out4);
  _7_Segment_Display u_7_segment_display_30 (
    .f(and_36_out), .a(and_36_out), .b(and_36_out), .e(and_36_out), .d(and_36_out), .c(and_36_out));  // open: g, dp
  and and_35 (and_35_out, decoder_3_out2, decoder_1_out5);
  and and_36 (and_36_out, decoder_3_out3, decoder_1_out5);
  _7_Segment_Display u_7_segment_display_31 (
    .f(and_38_out), .a(and_38_out), .b(and_38_out), .e(and_38_out), .d(and_38_out), .c(and_38_out));  // open: g, dp
  and and_37 (and_37_out, decoder_3_out2, decoder_1_out6);
  and and_38 (and_38_out, decoder_3_out3, decoder_1_out6);
  _7_Segment_Display u_7_segment_display_32 (
    .f(and_40_out), .a(and_40_out), .b(and_40_out), .e(and_40_out), .d(and_40_out), .c(and_40_out));  // open: g, dp
  and and_39 (and_39_out, decoder_3_out2, decoder_1_out7);
  and and_40 (and_40_out, decoder_3_out3, decoder_1_out7);
  buf buffer_1 (buffer_1_out, decoder_3_out0);
  _7_Segment_Display u_7_segment_display_33 (
    .f(and_41_out), .a(and_41_out), .b(and_41_out), .e(and_41_out), .d(and_41_out), .c(and_41_out));  // open: g, dp
  _7_Segment_Display u_7_segment_display_34 (
    .f(and_49_out), .a(and_49_out), .b(and_49_out), .e(and_49_out), .d(and_49_out), .c(and_49_out));  // open: g, dp
  and and_41 (and_41_out, decoder_3_out4, decoder_1_out0);
  _7_Segment_Display u_7_segment_display_35 (
    .f(and_42_out), .a(and_42_out), .b(and_42_out), .e(and_42_out), .d(and_42_out), .c(and_42_out));  // open: g, dp
  _7_Segment_Display u_7_segment_display_36 (
    .f(and_51_out), .a(and_51_out), .b(and_51_out), .e(and_51_out), .d(and_51_out), .c(and_51_out));  // open: g, dp
  and and_42 (and_42_out, decoder_3_out4, decoder_1_out1);
  _7_Segment_Display u_7_segment_display_37 (
    .f(and_43_out), .a(and_43_out), .b(and_43_out), .e(and_43_out), .d(and_43_out), .c(and_43_out));  // open: g, dp
  _7_Segment_Display u_7_segment_display_38 (
    .f(and_53_out), .a(and_53_out), .b(and_53_out), .e(and_53_out), .d(and_53_out), .c(and_53_out));  // open: g, dp
  and and_43 (and_43_out, decoder_3_out4, decoder_1_out2);
  _7_Segment_Display u_7_segment_display_39 (
    .f(and_44_out), .a(and_44_out), .b(and_44_out), .e(and_44_out), .d(and_44_out), .c(and_44_out));  // open: g, dp
  _7_Segment_Display u_7_segment_display_40 (
    .f(and_55_out), .a(and_55_out), .b(and_55_out), .e(and_55_out), .d(and_55_out), .c(and_55_out));  // open: g, dp
  and and_44 (and_44_out, decoder_3_out4, decoder_1_out3);
  _7_Segment_Display u_7_segment_display_41 (
    .f(and_45_out), .a(and_45_out), .b(and_45_out), .e(and_45_out), .d(and_45_out), .c(and_45_out));  // open: g, dp
  _7_Segment_Display u_7_segment_display_42 (
    .f(and_57_out), .a(and_57_out), .b(and_57_out), .e(and_57_out), .d(and_57_out), .c(and_57_out));  // open: g, dp
  and and_45 (and_45_out, decoder_3_out4, decoder_1_out4);
  _7_Segment_Display u_7_segment_display_43 (
    .f(and_46_out), .a(and_46_out), .b(and_46_out), .e(and_46_out), .d(and_46_out), .c(and_46_out));  // open: g, dp
  _7_Segment_Display u_7_segment_display_44 (
    .f(and_59_out), .a(and_59_out), .b(and_59_out), .e(and_59_out), .d(and_59_out), .c(and_59_out));  // open: g, dp
  and and_46 (and_46_out, decoder_3_out4, decoder_1_out5);
  _7_Segment_Display u_7_segment_display_45 (
    .f(and_47_out), .a(and_47_out), .b(and_47_out), .e(and_47_out), .d(and_47_out), .c(and_47_out));  // open: g, dp
  _7_Segment_Display u_7_segment_display_46 (
    .f(and_61_out), .a(and_61_out), .b(and_61_out), .e(and_61_out), .d(and_61_out), .c(and_61_out));  // open: g, dp
  and and_47 (and_47_out, decoder_3_out4, decoder_1_out6);
  _7_Segment_Display u_7_segment_display_47 (
    .f(and_48_out), .a(and_48_out), .b(and_48_out), .e(and_48_out), .d(and_48_out), .c(and_48_out));  // open: g, dp
  _7_Segment_Display u_7_segment_display_48 (
    .f(and_63_out), .a(and_63_out), .b(and_63_out), .e(and_63_out), .d(and_63_out), .c(and_63_out));  // open: g, dp
  and and_48 (and_48_out, decoder_3_out4, decoder_1_out7);
  or or_11 (or_11_out, and_17_out, and_18_out, and_19_out, and_20_out, and_21_out, and_22_out, and_23_out, and_24_out);
  not not_2 (not_2_out, or_11_out);
  _7_Segment_Display u_7_segment_display_49 (
    .f(and_50_out), .a(and_50_out), .b(and_50_out), .e(and_50_out), .d(and_50_out), .c(and_50_out));  // open: g, dp
  and and_49 (and_49_out, decoder_3_out5, decoder_1_out0);
  and and_50 (and_50_out, decoder_3_out6, decoder_1_out0);
  _7_Segment_Display u_7_segment_display_50 (
    .f(and_52_out), .a(and_52_out), .b(and_52_out), .e(and_52_out), .d(and_52_out), .c(and_52_out));  // open: g, dp
  and and_51 (and_51_out, decoder_3_out5, decoder_1_out1);
  and and_52 (and_52_out, decoder_3_out6, decoder_1_out1);
  _7_Segment_Display u_7_segment_display_51 (
    .f(and_54_out), .a(and_54_out), .b(and_54_out), .e(and_54_out), .d(and_54_out), .c(and_54_out));  // open: g, dp
  and and_53 (and_53_out, decoder_3_out5, decoder_1_out2);
  and and_54 (and_54_out, decoder_3_out6, decoder_1_out2);
  _7_Segment_Display u_7_segment_display_52 (
    .f(and_56_out), .a(and_56_out), .b(and_56_out), .e(and_56_out), .d(and_56_out), .c(and_56_out));  // open: g, dp
  and and_55 (and_55_out, decoder_3_out5, decoder_1_out3);
  and and_56 (and_56_out, decoder_3_out6, decoder_1_out3);
  _7_Segment_Display u_7_segment_display_53 (
    .f(and_58_out), .a(and_58_out), .b(and_58_out), .e(and_58_out), .d(and_58_out), .c(and_58_out));  // open: g, dp
  and and_57 (and_57_out, decoder_3_out5, decoder_1_out4);
  and and_58 (and_58_out, decoder_3_out6, decoder_1_out4);
  _7_Segment_Display u_7_segment_display_54 (
    .f(and_60_out), .a(and_60_out), .b(and_60_out), .e(and_60_out), .d(and_60_out), .c(and_60_out));  // open: g, dp
  and and_59 (and_59_out, decoder_3_out5, decoder_1_out5);
  and and_60 (and_60_out, decoder_3_out6, decoder_1_out5);
  _7_Segment_Display u_7_segment_display_55 (
    .f(and_62_out), .a(and_62_out), .b(and_62_out), .e(and_62_out), .d(and_62_out), .c(and_62_out));  // open: g, dp
  and and_61 (and_61_out, decoder_3_out5, decoder_1_out6);
  and and_62 (and_62_out, decoder_3_out6, decoder_1_out6);
  _7_Segment_Display u_7_segment_display_56 (
    .f(and_64_out), .a(and_64_out), .b(and_64_out), .e(and_64_out), .d(and_64_out), .c(and_64_out));  // open: g, dp
  and and_63 (and_63_out, decoder_3_out5, decoder_1_out7);
  and and_64 (and_64_out, decoder_3_out6, decoder_1_out7);
  and and_65 (and_65_out, buffer_1_out, not_2_out);
  D_Flip_Flop d_ff_1 (.D(and_65_out), .clk(clock_1_out), .Q(d_ff_1_q));  // open: Qn, preset, reset
  _7_Segment_Display u_7_segment_display_57 (
    .f(and_66_out), .a(and_66_out), .b(and_66_out), .e(and_66_out), .d(and_66_out), .c(and_66_out));  // open: g, dp
  _7_Segment_Display u_7_segment_display_58 (
    .f(and_74_out), .a(and_74_out), .b(and_74_out), .e(and_74_out), .d(and_74_out), .c(and_74_out));  // open: g, dp
  and and_66 (and_66_out, decoder_3_out7, decoder_1_out0);
  _7_Segment_Display u_7_segment_display_59 (
    .f(and_67_out), .a(and_67_out), .b(and_67_out), .e(and_67_out), .d(and_67_out), .c(and_67_out));  // open: g, dp
  _7_Segment_Display u_7_segment_display_60 (
    .f(and_76_out), .a(and_76_out), .b(and_76_out), .e(and_76_out), .d(and_76_out), .c(and_76_out));  // open: g, dp
  and and_67 (and_67_out, decoder_3_out7, decoder_1_out1);
  _7_Segment_Display u_7_segment_display_61 (
    .f(and_68_out), .a(and_68_out), .b(and_68_out), .e(and_68_out), .d(and_68_out), .c(and_68_out));  // open: g, dp
  _7_Segment_Display u_7_segment_display_62 (
    .f(and_78_out), .a(and_78_out), .b(and_78_out), .e(and_78_out), .d(and_78_out), .c(and_78_out));  // open: g, dp
  and and_68 (and_68_out, decoder_3_out7, decoder_1_out2);
  _7_Segment_Display u_7_segment_display_63 (
    .f(and_69_out), .a(and_69_out), .b(and_69_out), .e(and_69_out), .d(and_69_out), .c(and_69_out));  // open: g, dp
  _7_Segment_Display u_7_segment_display_64 (
    .f(and_80_out), .a(and_80_out), .b(and_80_out), .e(and_80_out), .d(and_80_out), .c(and_80_out));  // open: g, dp
  and and_69 (and_69_out, decoder_3_out7, decoder_1_out3);
  _7_Segment_Display u_7_segment_display_65 (
    .f(and_70_out), .a(and_70_out), .b(and_70_out), .e(and_70_out), .d(and_70_out), .c(and_70_out));  // open: g, dp
  _7_Segment_Display u_7_segment_display_66 (
    .f(and_82_out), .a(and_82_out), .b(and_82_out), .e(and_82_out), .d(and_82_out), .c(and_82_out));  // open: g, dp
  and and_70 (and_70_out, decoder_3_out7, decoder_1_out4);
  _7_Segment_Display u_7_segment_display_67 (
    .f(and_71_out), .a(and_71_out), .b(and_71_out), .e(and_71_out), .d(and_71_out), .c(and_71_out));  // open: g, dp
  _7_Segment_Display u_7_segment_display_68 (
    .f(and_84_out), .a(and_84_out), .b(and_84_out), .e(and_84_out), .d(and_84_out), .c(and_84_out));  // open: g, dp
  and and_71 (and_71_out, decoder_3_out7, decoder_1_out5);
  _7_Segment_Display u_7_segment_display_69 (
    .f(and_72_out), .a(and_72_out), .b(and_72_out), .e(and_72_out), .d(and_72_out), .c(and_72_out));  // open: g, dp
  _7_Segment_Display u_7_segment_display_70 (
    .f(and_86_out), .a(and_86_out), .b(and_86_out), .e(and_86_out), .d(and_86_out), .c(and_86_out));  // open: g, dp
  and and_72 (and_72_out, decoder_3_out7, decoder_1_out6);
  _7_Segment_Display u_7_segment_display_71 (
    .f(and_73_out), .a(and_73_out), .b(and_73_out), .e(and_73_out), .d(and_73_out), .c(and_73_out));  // open: g, dp
  _7_Segment_Display u_7_segment_display_72 (
    .f(and_88_out), .a(and_88_out), .b(and_88_out), .e(and_88_out), .d(and_88_out), .c(and_88_out));  // open: g, dp
  and and_73 (and_73_out, decoder_3_out7, decoder_1_out7);
  T_Flip_Flop t_ff_3 (.T(1'b1), .clk(d_ff_1_q), .Q(t_ff_3_q[0]), .Qn(t_ff_3_qn), .reset(in_1));  // open: preset
  _7_Segment_Display u_7_segment_display_73 (
    .f(and_75_out), .a(and_75_out), .b(and_75_out), .e(and_75_out), .d(and_75_out), .c(and_75_out));  // open: g, dp
  _7_Segment_Display u_7_segment_display_74 (
    .f(and_90_out), .a(and_90_out), .b(and_90_out), .e(and_90_out), .d(and_90_out), .c(and_90_out));  // open: g, dp
  and and_74 (and_74_out, decoder_3_out8, decoder_1_out0);
  and and_75 (and_75_out, decoder_3_out9, decoder_1_out0);
  _7_Segment_Display u_7_segment_display_75 (
    .f(and_77_out), .a(and_77_out), .b(and_77_out), .e(and_77_out), .d(and_77_out), .c(and_77_out));  // open: g, dp
  _7_Segment_Display u_7_segment_display_76 (
    .f(and_92_out), .a(and_92_out), .b(and_92_out), .e(and_92_out), .d(and_92_out), .c(and_92_out));  // open: g, dp
  and and_76 (and_76_out, decoder_3_out8, decoder_1_out1);
  and and_77 (and_77_out, decoder_3_out9, decoder_1_out1);
  _7_Segment_Display u_7_segment_display_77 (
    .f(and_79_out), .a(and_79_out), .b(and_79_out), .e(and_79_out), .d(and_79_out), .c(and_79_out));  // open: g, dp
  _7_Segment_Display u_7_segment_display_78 (
    .f(and_94_out), .a(and_94_out), .b(and_94_out), .e(and_94_out), .d(and_94_out), .c(and_94_out));  // open: g, dp
  and and_78 (and_78_out, decoder_3_out8, decoder_1_out2);
  and and_79 (and_79_out, decoder_3_out9, decoder_1_out2);
  _7_Segment_Display u_7_segment_display_79 (
    .f(and_81_out), .a(and_81_out), .b(and_81_out), .e(and_81_out), .d(and_81_out), .c(and_81_out));  // open: g, dp
  _7_Segment_Display u_7_segment_display_80 (
    .f(and_96_out), .a(and_96_out), .b(and_96_out), .e(and_96_out), .d(and_96_out), .c(and_96_out));  // open: g, dp
  and and_80 (and_80_out, decoder_3_out8, decoder_1_out3);
  and and_81 (and_81_out, decoder_3_out9, decoder_1_out3);
  _7_Segment_Display u_7_segment_display_81 (
    .f(and_83_out), .a(and_83_out), .b(and_83_out), .e(and_83_out), .d(and_83_out), .c(and_83_out));  // open: g, dp
  _7_Segment_Display u_7_segment_display_82 (
    .f(and_98_out), .a(and_98_out), .b(and_98_out), .e(and_98_out), .d(and_98_out), .c(and_98_out));  // open: g, dp
  and and_82 (and_82_out, decoder_3_out8, decoder_1_out4);
  and and_83 (and_83_out, decoder_3_out9, decoder_1_out4);
  _7_Segment_Display u_7_segment_display_83 (
    .f(and_85_out), .a(and_85_out), .b(and_85_out), .e(and_85_out), .d(and_85_out), .c(and_85_out));  // open: g, dp
  _7_Segment_Display u_7_segment_display_84 (
    .f(and_100_out), .a(and_100_out), .b(and_100_out), .e(and_100_out), .d(and_100_out), .c(and_100_out));  // open: g, dp
  and and_84 (and_84_out, decoder_3_out8, decoder_1_out5);
  and and_85 (and_85_out, decoder_3_out9, decoder_1_out5);
  _7_Segment_Display u_7_segment_display_85 (
    .f(and_87_out), .a(and_87_out), .b(and_87_out), .e(and_87_out), .d(and_87_out), .c(and_87_out));  // open: g, dp
  _7_Segment_Display u_7_segment_display_86 (
    .f(and_102_out), .a(and_102_out), .b(and_102_out), .e(and_102_out), .d(and_102_out), .c(and_102_out));  // open: g, dp
  and and_86 (and_86_out, decoder_3_out8, decoder_1_out6);
  and and_87 (and_87_out, decoder_3_out9, decoder_1_out6);
  _7_Segment_Display u_7_segment_display_87 (
    .f(and_89_out), .a(and_89_out), .b(and_89_out), .e(and_89_out), .d(and_89_out), .c(and_89_out));  // open: g, dp
  _7_Segment_Display u_7_segment_display_88 (
    .f(and_104_out), .a(and_104_out), .b(and_104_out), .e(and_104_out), .d(and_104_out), .c(and_104_out));  // open: g, dp
  and and_88 (and_88_out, decoder_3_out8, decoder_1_out7);
  and and_89 (and_89_out, decoder_3_out9, decoder_1_out7);
  T_Flip_Flop t_ff_4 (.T(1'b1), .clk(t_ff_3_qn), .Q(t_ff_3_q[1]), .Qn(t_ff_4_qn), .reset(in_1));  // open: preset
  _7_Segment_Display u_7_segment_display_89 (
    .f(and_91_out), .a(and_91_out), .b(and_91_out), .e(and_91_out), .d(and_91_out), .c(and_91_out));  // open: g, dp
  and and_90 (and_90_out, decoder_3_out10, decoder_1_out0);
  and and_91 (and_91_out, decoder_3_out11, decoder_1_out0);
  _7_Segment_Display u_7_segment_display_90 (
    .f(and_93_out), .a(and_93_out), .b(and_93_out), .e(and_93_out), .d(and_93_out), .c(and_93_out));  // open: g, dp
  and and_92 (and_92_out, decoder_3_out10, decoder_1_out1);
  and and_93 (and_93_out, decoder_3_out11, decoder_1_out1);
  _7_Segment_Display u_7_segment_display_91 (
    .f(and_95_out), .a(and_95_out), .b(and_95_out), .e(and_95_out), .d(and_95_out), .c(and_95_out));  // open: g, dp
  and and_94 (and_94_out, decoder_3_out10, decoder_1_out2);
  and and_95 (and_95_out, decoder_3_out11, decoder_1_out2);
  _7_Segment_Display u_7_segment_display_92 (
    .f(and_97_out), .a(and_97_out), .b(and_97_out), .e(and_97_out), .d(and_97_out), .c(and_97_out));  // open: g, dp
  and and_96 (and_96_out, decoder_3_out10, decoder_1_out3);
  and and_97 (and_97_out, decoder_3_out11, decoder_1_out3);
  _7_Segment_Display u_7_segment_display_93 (
    .f(and_99_out), .a(and_99_out), .b(and_99_out), .e(and_99_out), .d(and_99_out), .c(and_99_out));  // open: g, dp
  and and_98 (and_98_out, decoder_3_out10, decoder_1_out4);
  and and_99 (and_99_out, decoder_3_out11, decoder_1_out4);
  _7_Segment_Display u_7_segment_display_94 (
    .f(and_101_out), .a(and_101_out), .b(and_101_out), .e(and_101_out), .d(and_101_out), .c(and_101_out));  // open: g, dp
  and and_100 (and_100_out, decoder_3_out10, decoder_1_out5);
  and and_101 (and_101_out, decoder_3_out11, decoder_1_out5);
  _7_Segment_Display u_7_segment_display_95 (
    .f(and_103_out), .a(and_103_out), .b(and_103_out), .e(and_103_out), .d(and_103_out), .c(and_103_out));  // open: g, dp
  and and_102 (and_102_out, decoder_3_out10, decoder_1_out6);
  and and_103 (and_103_out, decoder_3_out11, decoder_1_out6);
  _7_Segment_Display u_7_segment_display_96 (
    .f(and_105_out), .a(and_105_out), .b(and_105_out), .e(and_105_out), .d(and_105_out), .c(and_105_out));  // open: g, dp
  and and_104 (and_104_out, decoder_3_out10, decoder_1_out7);
  and and_105 (and_105_out, decoder_3_out11, decoder_1_out7);
  T_Flip_Flop t_ff_5 (.T(1'b1), .clk(t_ff_4_qn), .Q(t_ff_3_q[2]), .Qn(t_ff_5_qn), .reset(in_1));  // open: preset
  _7_Segment_Display u_7_segment_display_97 (
    .f(and_106_out), .a(and_106_out), .b(and_106_out), .e(and_106_out), .d(and_106_out), .c(and_106_out));  // open: g, dp
  _7_Segment_Display u_7_segment_display_98 (
    .f(and_114_out), .a(and_114_out), .b(and_114_out), .e(and_114_out), .d(and_114_out), .c(and_114_out));  // open: g, dp
  and and_106 (and_106_out, decoder_3_out12, decoder_1_out0);
  _7_Segment_Display u_7_segment_display_99 (
    .f(and_107_out), .a(and_107_out), .b(and_107_out), .e(and_107_out), .d(and_107_out), .c(and_107_out));  // open: g, dp
  _7_Segment_Display u_7_segment_display_100 (
    .f(and_116_out), .a(and_116_out), .b(and_116_out), .e(and_116_out), .d(and_116_out), .c(and_116_out));  // open: g, dp
  and and_107 (and_107_out, decoder_3_out12, decoder_1_out1);
  _7_Segment_Display u_7_segment_display_101 (
    .f(and_108_out), .a(and_108_out), .b(and_108_out), .e(and_108_out), .d(and_108_out), .c(and_108_out));  // open: g, dp
  _7_Segment_Display u_7_segment_display_102 (
    .f(and_118_out), .a(and_118_out), .b(and_118_out), .e(and_118_out), .d(and_118_out), .c(and_118_out));  // open: g, dp
  and and_108 (and_108_out, decoder_3_out12, decoder_1_out2);
  _7_Segment_Display u_7_segment_display_103 (
    .f(and_109_out), .a(and_109_out), .b(and_109_out), .e(and_109_out), .d(and_109_out), .c(and_109_out));  // open: g, dp
  _7_Segment_Display u_7_segment_display_104 (
    .f(and_120_out), .a(and_120_out), .b(and_120_out), .e(and_120_out), .d(and_120_out), .c(and_120_out));  // open: g, dp
  and and_109 (and_109_out, decoder_3_out12, decoder_1_out3);
  _7_Segment_Display u_7_segment_display_105 (
    .f(and_110_out), .a(and_110_out), .b(and_110_out), .e(and_110_out), .d(and_110_out), .c(and_110_out));  // open: g, dp
  _7_Segment_Display u_7_segment_display_106 (
    .f(and_122_out), .a(and_122_out), .b(and_122_out), .e(and_122_out), .d(and_122_out), .c(and_122_out));  // open: g, dp
  and and_110 (and_110_out, decoder_3_out12, decoder_1_out4);
  _7_Segment_Display u_7_segment_display_107 (
    .f(and_111_out), .a(and_111_out), .b(and_111_out), .e(and_111_out), .d(and_111_out), .c(and_111_out));  // open: g, dp
  _7_Segment_Display u_7_segment_display_108 (
    .f(and_124_out), .a(and_124_out), .b(and_124_out), .e(and_124_out), .d(and_124_out), .c(and_124_out));  // open: g, dp
  and and_111 (and_111_out, decoder_3_out12, decoder_1_out5);
  _7_Segment_Display u_7_segment_display_109 (
    .f(and_112_out), .a(and_112_out), .b(and_112_out), .e(and_112_out), .d(and_112_out), .c(and_112_out));  // open: g, dp
  _7_Segment_Display u_7_segment_display_110 (
    .f(and_126_out), .a(and_126_out), .b(and_126_out), .e(and_126_out), .d(and_126_out), .c(and_126_out));  // open: g, dp
  and and_112 (and_112_out, decoder_3_out12, decoder_1_out6);
  _7_Segment_Display u_7_segment_display_111 (
    .f(and_113_out), .a(and_113_out), .b(and_113_out), .e(and_113_out), .d(and_113_out), .c(and_113_out));  // open: g, dp
  _7_Segment_Display u_7_segment_display_112 (
    .f(and_128_out), .a(and_128_out), .b(and_128_out), .e(and_128_out), .d(and_128_out), .c(and_128_out));  // open: g, dp
  and and_113 (and_113_out, decoder_3_out12, decoder_1_out7);
  T_Flip_Flop t_ff_6 (.T(1'b1), .clk(t_ff_5_qn), .Q(t_ff_3_q[3]), .reset(in_1));  // open: Qn, preset
  _7_Segment_Display u_7_segment_display_113 (
    .f(and_115_out), .a(and_115_out), .b(and_115_out), .e(and_115_out), .d(and_115_out), .c(and_115_out));  // open: g, dp
  and and_114 (and_114_out, decoder_3_out13, decoder_1_out0);
  and and_115 (and_115_out, decoder_3_out14, decoder_1_out0);
  _7_Segment_Display u_7_segment_display_114 (
    .f(and_117_out), .a(and_117_out), .b(and_117_out), .e(and_117_out), .d(and_117_out), .c(and_117_out));  // open: g, dp
  and and_116 (and_116_out, decoder_3_out13, decoder_1_out1);
  and and_117 (and_117_out, decoder_3_out14, decoder_1_out1);
  _7_Segment_Display u_7_segment_display_115 (
    .f(and_119_out), .a(and_119_out), .b(and_119_out), .e(and_119_out), .d(and_119_out), .c(and_119_out));  // open: g, dp
  and and_118 (and_118_out, decoder_3_out13, decoder_1_out2);
  and and_119 (and_119_out, decoder_3_out14, decoder_1_out2);
  _7_Segment_Display u_7_segment_display_116 (
    .f(and_121_out), .a(and_121_out), .b(and_121_out), .e(and_121_out), .d(and_121_out), .c(and_121_out));  // open: g, dp
  and and_120 (and_120_out, decoder_3_out13, decoder_1_out3);
  and and_121 (and_121_out, decoder_3_out14, decoder_1_out3);
  _7_Segment_Display u_7_segment_display_117 (
    .f(and_123_out), .a(and_123_out), .b(and_123_out), .e(and_123_out), .d(and_123_out), .c(and_123_out));  // open: g, dp
  and and_122 (and_122_out, decoder_3_out13, decoder_1_out4);
  and and_123 (and_123_out, decoder_3_out14, decoder_1_out4);
  _7_Segment_Display u_7_segment_display_118 (
    .f(and_125_out), .a(and_125_out), .b(and_125_out), .e(and_125_out), .d(and_125_out), .c(and_125_out));  // open: g, dp
  and and_124 (and_124_out, decoder_3_out13, decoder_1_out5);
  and and_125 (and_125_out, decoder_3_out14, decoder_1_out5);
  _7_Segment_Display u_7_segment_display_119 (
    .f(and_127_out), .a(and_127_out), .b(and_127_out), .e(and_127_out), .d(and_127_out), .c(and_127_out));  // open: g, dp
  and and_126 (and_126_out, decoder_3_out13, decoder_1_out6);
  and and_127 (and_127_out, decoder_3_out14, decoder_1_out6);
  _7_Segment_Display u_7_segment_display_120 (
    .f(and_129_out), .a(and_129_out), .b(and_129_out), .e(and_129_out), .d(and_129_out), .c(and_129_out));  // open: g, dp
  and and_128 (and_128_out, decoder_3_out13, decoder_1_out7);
  and and_129 (and_129_out, decoder_3_out14, decoder_1_out7);
  Joystick #(.bits(2)) joystick_1 ();  // open: x, y
  or or_12 (or_12_out, decoder_4_out0, and_130_out);
  _7_Segment_Display u_7_segment_display_121 (
    .f(and_130_out), .a(and_130_out), .b(or_12_out), .e(and_130_out), .d(and_130_out), .c(or_12_out));  // open: g, dp
  and and_130 (and_130_out, decoder_3_out15, decoder_1_out0);
  _7_Segment_Display u_7_segment_display_122 (
    .f(and_131_out), .a(and_131_out), .b(or_13_out), .e(and_131_out), .d(and_131_out), .c(or_13_out));  // open: g, dp
  or or_13 (or_13_out, decoder_4_out1, and_131_out);
  and and_131 (and_131_out, decoder_3_out15, decoder_1_out1);
  _7_Segment_Display u_7_segment_display_123 (
    .f(and_132_out), .a(and_132_out), .b(or_14_out), .e(and_132_out), .d(and_132_out), .c(or_14_out));  // open: g, dp
  and and_132 (and_132_out, decoder_3_out15, decoder_1_out2);
  or or_14 (or_14_out, decoder_4_out2, and_132_out);
  _7_Segment_Display u_7_segment_display_124 (
    .f(and_133_out), .a(and_133_out), .b(or_15_out), .e(and_133_out), .d(and_133_out), .c(or_15_out));  // open: g, dp
  and and_133 (and_133_out, decoder_3_out15, decoder_1_out3);
  or or_15 (or_15_out, decoder_4_out3, and_133_out);
  _7_Segment_Display u_7_segment_display_125 (
    .f(and_134_out), .a(and_134_out), .b(or_16_out), .e(and_134_out), .d(and_134_out), .c(or_16_out));  // open: g, dp
  or or_16 (or_16_out, decoder_4_out4, and_134_out);
  and and_134 (and_134_out, decoder_3_out15, decoder_1_out4);
  _7_Segment_Display u_7_segment_display_126 (
    .f(and_135_out), .a(and_135_out), .b(or_17_out), .e(and_135_out), .d(and_135_out), .c(or_17_out));  // open: g, dp
  or or_17 (or_17_out, decoder_4_out5, and_135_out);
  and and_135 (and_135_out, decoder_3_out15, decoder_1_out5);
  _7_Segment_Display u_7_segment_display_127 (
    .f(and_136_out), .a(and_136_out), .b(or_18_out), .e(and_136_out), .d(and_136_out), .c(or_18_out));  // open: g, dp
  and and_136 (and_136_out, decoder_3_out15, decoder_1_out6);
  or or_18 (or_18_out, decoder_4_out6, and_136_out);
  _7_Segment_Display u_7_segment_display_128 (
    .f(and_137_out), .a(and_137_out), .b(or_19_out), .e(and_137_out), .d(and_137_out), .c(or_19_out));  // open: g, dp
  and and_137 (and_137_out, decoder_3_out15, decoder_1_out7);
  or or_19 (or_19_out, decoder_4_out7, and_137_out);
  Hex_Digit_Display hex_digit_display_1 (.value(t_ff_7_q));  // open: dp
  Joystick #(.bits(2)) joystick_2 (.y(out_2));  // open: x
  and and_138 (and_138_out, and_130_out, decoder_4_out0);
  Decoder #(.select(3)) decoder_4 (
    .out0(decoder_4_out0), .out1(decoder_4_out1), .out2(decoder_4_out2), .out3(decoder_4_out3),
    .out4(decoder_4_out4), .out5(decoder_4_out5), .out6(decoder_4_out6), .out7(decoder_4_out7),
    .sel(counter_4_q));  // open: en
  and and_139 (and_139_out, decoder_4_out1, and_131_out);
  and and_140 (and_140_out, decoder_4_out2, and_132_out);
  and and_141 (and_141_out, decoder_4_out3, and_133_out);
  and and_142 (and_142_out, decoder_4_out4, and_134_out);
  and and_143 (and_143_out, decoder_4_out5, and_135_out);
  and and_144 (and_144_out, decoder_4_out6, and_136_out);
  and and_145 (and_145_out, decoder_4_out7, and_137_out);
  Hex_Digit_Display hex_digit_display_2 (.value(t_ff_3_q));  // open: dp
  Comparator #(.width(2)) comparator_2 (.a(out_2), .b(2'b10), .eq(comparator_2_eq));  // open: gt, lt
  Counter #(.max('h7), .width(3)) counter_4 (
    .load(in_1), .up(out_2[1]), .count(not_3_out), .clk(clock_1_out), .D(3'b100), .Q(counter_4_q));  // open: clr, carry
  not not_3 (not_3_out, comparator_2_eq);
  or or_20 (or_20_out, and_138_out, and_139_out, and_140_out, and_141_out, and_142_out, and_143_out, and_144_out, and_145_out);
  not not_4 (not_4_out, or_20_out);
  and and_146 (and_146_out, not_4_out, buffer_2_out);
  D_Flip_Flop d_ff_2 (.D(and_146_out), .clk(clock_1_out), .Q(d_ff_2_q));  // open: Qn, preset, reset
  buf buffer_2 (buffer_2_out, decoder_3_out15);
  T_Flip_Flop t_ff_7 (.T(1'b1), .clk(d_ff_2_q), .Q(t_ff_7_q[0]), .Qn(t_ff_7_qn), .reset(in_1));  // open: preset
  T_Flip_Flop t_ff_8 (.T(1'b1), .clk(t_ff_7_qn), .Q(t_ff_7_q[1]), .Qn(t_ff_8_qn), .reset(in_1));  // open: preset
  T_Flip_Flop t_ff_9 (.T(1'b1), .clk(t_ff_8_qn), .Q(t_ff_7_q[2]), .Qn(t_ff_9_qn), .reset(in_1));  // open: preset
  T_Flip_Flop t_ff_10 (.T(1'b1), .clk(t_ff_9_qn), .Q(t_ff_7_q[3]), .reset(in_1));  // open: Qn, preset
endmodule
